// Logisim project CPU.circ as structural Verilog: 38 circuits, main circuit CPU
module CPU (
  input  in_1,
  input  _0,
  input  _1,
  input  _2,
  input  _3,
  input  in_6,
  input  in_7,
  input  Enable_Program_Write,
  input  Auto_Clock,
  input  One_by_One,
  input  in_11,
  input  in_12,
  input  in_13,
  input  in_14,
  input  in_15,
  input  in_16,
  input  in_17,
  input  in_18,
  input  in_19,
  input  in_20,
  input  in_21,
  input  in_22,
  input  in_23,
  input  in_24,
  input  in_25
);

  wire Accumulator__0_3, Accumulator__1_2, Accumulator__2_2, Accumulator__3_2, Accumulator__4_2,
       Accumulator__5_2, Accumulator__6_2, Accumulator__7_2, Accumulator_A__0_3, Accumulator_A__1_2,
       Accumulator_A__2_2, Accumulator_A__3_2, Accumulator_A__4_2, Accumulator_A__5_2, Accumulator_A__6_2,
       Accumulator_A__7_2, Accumulator_B__0_3, Accumulator_B__1_2, Accumulator_B__2_2, Accumulator_B__3_2,
       Accumulator_B__4_2, Accumulator_B__5_2, Accumulator_B__6_2, Accumulator_B__7_2, alu_1_a_greater_b,
       alu_1_b_greater_a, alu_1_not_equal, alu_1_overflow, alu_1_x0, alu_1_x1, alu_1_x2, alu_1_x3, alu_1_x4,
       alu_1_x5, alu_1_x6, alu_1_x7, alu_1_zero, and_1_out, and_2_out, and_3_out, and_4_out, and_5_out,
       and_6_out, and_7_out, and_8_out, and_9_out, buffer_1_out, buffer_2_out, buffer_3_out, buffer_4_out,
       buffer_5_out, buffer_6_out, buffer_7_out, Clear_Input_out, clock_1_out,
       condition_code_register_1_a_greater_b_2, condition_code_register_1_b_greater_a_2,
       condition_code_register_1_finished_2, condition_code_register_1_negative_2,
       condition_code_register_1_not_equal_2, condition_code_register_1_overflow_2,
       condition_code_register_1_waiting_2, condition_code_register_1_zero_2, control_panel_1_clock,
       control_panel_1_enable_write, control_panel_1_next_instruction_2, control_panel_1_one_by_one_2,
       control_panel_1_program_reset_out, control_panel_1_reset_out, control_panel_1_system_clock,
       control_panel_1_write_next_byte, control_unit_1_a, control_unit_1_a_invert, control_unit_1_add,
       control_unit_1_and, control_unit_1_b, control_unit_1_b_invert, control_unit_1_clock_b_greater_a,
       control_unit_1_clock_ccr, control_unit_1_increment, control_unit_1_m_clock, control_unit_1_multiply,
       control_unit_1_or, control_unit_1_shift_a_left, control_unit_1_shift_a_right,
       control_unit_1_shift_b_left, control_unit_1_shift_b_right, control_unit_1_shift_loop,
       control_unit_1_x_invert, control_unit_1_xor, controlled_buffer_5_out, IR__0_3, IR__1_2, IR__2_2,
       IR__3_2, IR__4_2, IR__5_2, IR__6_2, IR__7_2, keyboard_1_avail, MAR__0_3, MAR__1_2, MAR__2_2, MAR__3_2,
       MAR__4_2, MAR__5_2, MAR__6_2, MAR__7_2, MAR_Offset__0_3, MAR_Offset__1_2, MAR_Offset__2_2,
       MAR_Offset__3_2, MAR_Offset__4_2, MAR_Offset__5_2, MAR_Offset__6_2, MAR_Offset__7_2, MBR__0_3,
       MBR__1_2, MBR__2_2, MBR__3_2, MBR__4_2, MBR__5_2, MBR__6_2, MBR__7_2, n8_bit_adder_1_carry_out,
       n8_bit_adder_1_x0, n8_bit_adder_1_x1, n8_bit_adder_1_x2, n8_bit_adder_1_x3, n8_bit_adder_1_x4,
       n8_bit_adder_1_x5, n8_bit_adder_1_x6, n8_bit_adder_1_x7, Next_Instruction_out, not_1_out, or_1_out,
       or_2_out, or_3_out, PC_2_count_out, PC_2_decrement_mode_carry, PC_2_set_carry, PC__0_2, PC__1_2,
       PC__2_2, PC__3_2, PC__4_2, PC__5_2, PC__6_2, PC__7_2, PC_count_out, PC_decrement_mode_carry,
       PC_set_carry, Program_Reset_out, Reset_out, SP__0_2, SP__1_2, SP__2_2, SP__3_2, SP__4_2, SP__5_2,
       SP__6_2, SP__7_2, Tick_out, undriven, undriven_2, undriven_3, undriven_4, undriven_5, undriven_6,
       undriven_7, undriven_8, undriven_9, undriven_10, undriven_11, undriven_12, undriven_13, undriven_14,
       undriven_15, undriven_16, undriven_17, undriven_18, undriven_19, undriven_20, undriven_21,
       undriven_22, undriven_23, undriven_24, undriven_25, undriven_26, undriven_27, undriven_28,
       undriven_29, undriven_30, undriven_32, undriven_33, Write_Byte_out, x_1__0_2, x_1__1_2, x_1__2_2,
       x_1__3_2, x_1__4_2, x_1__5_2, x_1__6_2, x_1__7_2;
  wire [3:0] joystick_1_x, joystick_1_y, PC_2__0_2, PC_2__4_2, SP_2__0_2, SP_2__4_2;
  wire [6:0] keyboard_1_data, undriven_31;
  wire [7:0] Accumulator__0_2, Accumulator_A__0_2, Accumulator_B__0_2, CCR__0_2, controlled_buffer_1_out,
       IR__0_2, MAR__0_2, MAR_Offset__0_2, MBR__0_2, multiplexer_1_out, n2_way_multiplexor_1__0_3,
       n3_way_multiplexor_1__0_4, n8_bit_counter_1__0_2, R0__0_2, R1__0_2, R2__0_2, R3__0_2, R4__0_2,
       R5__0_2, R6__0_2, R7__0_2, ram_1_data, rom_1_data, rom_2_data, rom_3_data, rom_4_data;
  wire [15:0] led_matrix_controller_1_out_12, led_matrix_controller_1_out_13, led_matrix_controller_1_out_14,
       led_matrix_controller_1_out_15, led_matrix_controller_1_out_16, led_matrix_controller_1_out_17,
       led_matrix_controller_1_out_18, led_matrix_controller_1_out_19, led_matrix_controller_1_out_20,
       led_matrix_controller_1_out_21, led_matrix_controller_1_out_22, led_matrix_controller_1_out_23,
       led_matrix_controller_1_out_24, led_matrix_controller_1_out_25, led_matrix_controller_1_out_26,
       led_matrix_controller_1_out_27;

  _8_bit_Register R0 (
    ._0_2(R0__0_2), .in_1({8{1'b0}}));  // open: _6, _5, _4, _3, _2, _1, _0, _0_3, _1_2, _2_2, _3_2, _4_2, _5_2, _6_2, _7_2, _7, Reset, Clock, Enable
  // Probe on R0__0_2
  _8_bit_Register R1 (
    ._0_2(R1__0_2), .in_1({8{1'b0}}));  // open: _6, _5, _4, _3, _2, _1, _0, _0_3, _1_2, _2_2, _3_2, _4_2, _5_2, _6_2, _7_2, _7, Reset, Clock, Enable
  // Probe on R1__0_2
  _8_bit_Register R2 (
    ._0_2(R2__0_2), .in_1({8{1'b0}}));  // open: _6, _5, _4, _3, _2, _1, _0, _0_3, _1_2, _2_2, _3_2, _4_2, _5_2, _6_2, _7_2, _7, Reset, Clock, Enable
  // Probe on R2__0_2
  // Probe on R3__0_2
  _8_bit_Register R3 (
    ._0_2(R3__0_2), .in_1({8{1'b0}}));  // open: _6, _5, _4, _3, _2, _1, _0, _0_3, _1_2, _2_2, _3_2, _4_2, _5_2, _6_2, _7_2, _7, Reset, Clock, Enable
  _8_bit_Register R4 (
    ._0_2(R4__0_2), .in_1({8{1'b0}}));  // open: _6, _5, _4, _3, _2, _1, _0, _0_3, _1_2, _2_2, _3_2, _4_2, _5_2, _6_2, _7_2, _7, Reset, Clock, Enable
  // Probe on R4__0_2
  // Probe on R5__0_2
  _8_bit_Register R5 (
    ._0_2(R5__0_2), .in_1({8{1'b0}}));  // open: _6, _5, _4, _3, _2, _1, _0, _0_3, _1_2, _2_2, _3_2, _4_2, _5_2, _6_2, _7_2, _7, Reset, Clock, Enable
  // Probe on R6__0_2
  _8_bit_Register R6 (
    ._0_2(R6__0_2), .in_1({8{1'b0}}));  // open: _6, _5, _4, _3, _2, _1, _0, _0_3, _1_2, _2_2, _3_2, _4_2, _5_2, _6_2, _7_2, _7, Reset, Clock, Enable
  _8_bit_Register R7 (
    ._0_2(R7__0_2), .in_1({8{1'b0}}));  // open: _6, _5, _4, _3, _2, _1, _0, _0_3, _1_2, _2_2, _3_2, _4_2, _5_2, _6_2, _7_2, _7, Reset, Clock, Enable
  // Probe on R7__0_2
  buf buffer_1 (buffer_1_out, and_1_out);
  buf buffer_2 (buffer_2_out, buffer_1_out);
  buf buffer_3 (buffer_3_out, buffer_2_out);
  buf buffer_4 (buffer_4_out, buffer_3_out);
  buf buffer_5 (buffer_5_out, buffer_4_out);
  buf buffer_6 (buffer_6_out, buffer_5_out);
  buf buffer_7 (buffer_7_out, buffer_6_out);
  not not_1 (not_1_out, and_2_out);
  and and_1 (and_1_out, not_1_out, control_panel_1_write_next_byte);
  and and_2 (and_2_out, n8_bit_counter_1__0_2[0], and_3_out);
  ROM rom_1 (.addr(n8_bit_counter_1__0_2), .data(rom_1_data));  // open: sel
  assign controlled_buffer_1_out = _0 ? rom_1_data : 8'bz;  // Controlled_Buffer_part controlled_buffer_1
  and and_3 (and_3_out, n8_bit_counter_1__0_2[1], and_4_out);
  and and_4 (and_4_out, n8_bit_counter_1__0_2[2], and_5_out);
  and and_5 (and_5_out, n8_bit_counter_1__0_2[3], and_6_out);
  or or_1 (or_1_out, buffer_7_out, control_unit_1_m_clock);
  _15_Way_Multiplexor u_15_way_multiplexor_1 (
    .I0(SP__0_2), ._1_9(SP__1_2), ._2_9(SP__2_2), ._3_9(SP__3_2), ._4_9(SP__4_2), ._5_9(SP__5_2),
    ._6_9(SP__6_2), ._7_9(SP__7_2), .O0(PC__0_2), ._1_15(PC__1_2), ._2_15(PC__2_2), ._3_15(PC__3_2),
    ._4_15(PC__4_2), ._5_15(PC__5_2), ._6_15(PC__6_2), ._7_15(PC__7_2));  // open: A0, _1, _2, _3, _4, _5, _6, _7, B0, _1_2, _2_2, _3_2, _4_2, _5_2, _6_2, _7_2, C0, _1_3, _2_3, _3_3, _4_3, _5_3, _6_3, _7_3, D0, _1_4, _2_4, _3_4, _4_4, _5_4, _6_4, _7_4, E0, _1_5, _2_5, _3_5, _4_5, _5_5, _6_5, _7_5, F0, _1_6, _2_6, _3_6, _4_6, _5_6, _6_6, _7_6, G0, _1_7, _2_7, _3_7, _4_7, _5_7, _6_7, _7_7, H0, _1_8, _2_8, _3_8, _4_8, _5_8, _6_8, _7_8, J0, _1_10, _2_10, _3_10, _4_10, _5_10, _6_10, _7_10, K0, _1_11, _2_11, _3_11, _4_11, _5_11, _6_11, _7_11, L0, _1_12, _2_12, _3_12, _4_12, _5_12, _6_12, _7_12, M0, _1_13, _2_13, _3_13, _4_13, _5_13, _6_13, _7_13, N0, _1_14, _2_14, _3_14, _4_14, _5_14, _6_14, _7_14, S3, S2, S1, S0, _7_16, _6_16, _5_16, _4_16, _3_16, _2_16, _1_16, _0
  and and_6 (and_6_out, n8_bit_counter_1__0_2[4], and_7_out);
  and and_7 (and_7_out, n8_bit_counter_1__0_2[5], and_8_out);
  RAM #(.bus("separate")) ram_1 (
    .addr(n2_way_multiplexor_1__0_3), .din(n3_way_multiplexor_1__0_4), .data(ram_1_data), .clk(or_1_out),
    .clr(control_panel_1_program_reset_out));  // open: str, sel, ld
  _8_bit_Counter SP (
    .Set(PC_set_carry), ._7_2(SP__7_2), ._6_2(SP__6_2), ._5_2(SP__5_2), ._4_2(SP__4_2), ._3_2(SP__3_2),
    ._2_2(SP__2_2), ._1_2(SP__1_2), ._0_2(SP__0_2), .Decrement_Mode(PC_decrement_mode_carry),
    .Count(PC_count_out));  // open: _7, _6, _5, _4, _3, _2, _1, _0, Count_Out, Set_Carry, Decrement_Mode_Carry
  // Probe on CCR__0_2
  _8_bit_Register CCR (
    ._0_2(CCR__0_2), .in_1({8{1'b0}}));  // open: _6, _5, _4, _3, _2, _1, _0, _0_3, _1_2, _2_2, _3_2, _4_2, _5_2, _6_2, _7_2, _7, Reset, Clock, Enable
  ROM rom_2 (.addr(n8_bit_counter_1__0_2), .data(rom_2_data));  // open: sel
  assign controlled_buffer_1_out = _1 ? rom_2_data : 8'bz;  // Controlled_Buffer_part controlled_buffer_2
  Multiplexer #(.width(8), .enable("false")) multiplexer_1 (
    .in0({8{1'b0}}), .in1(controlled_buffer_1_out), .out(multiplexer_1_out),
    .sel(control_panel_1_enable_write));
  and and_8 (and_8_out, n8_bit_counter_1__0_2[6], n8_bit_counter_1__0_2[7]);
  // Probe on MBR__0_2
  _8_bit_Register MBR (
    ._6(ram_1_data[6]), ._5(ram_1_data[5]), ._4(ram_1_data[4]), ._3(ram_1_data[3]), ._2(ram_1_data[2]),
    ._1(ram_1_data[1]), ._0(ram_1_data[0]), ._0_3(MBR__0_3), ._1_2(MBR__1_2), ._2_2(MBR__2_2),
    ._3_2(MBR__3_2), ._4_2(MBR__4_2), ._5_2(MBR__5_2), ._6_2(MBR__6_2), ._0_2(MBR__0_2), .in_1({8{1'b0}}),
    ._7_2(MBR__7_2), ._7(ram_1_data[7]));  // open: Reset, Clock, Enable
  _8_bit_Counter PC (
    ._7_2(PC__7_2), ._6_2(PC__6_2), ._5_2(PC__5_2), ._4_2(PC__4_2), ._3_2(PC__3_2), ._2_2(PC__2_2),
    ._1_2(PC__1_2), ._0_2(PC__0_2), .Count_Out(PC_count_out), .Set_Carry(PC_set_carry),
    .Decrement_Mode_Carry(PC_decrement_mode_carry));  // open: Set, _7, _6, _5, _4, _3, _2, _1, _0, Decrement_Mode, Count
  _8_bit_Counter u_8_bit_counter_1 (
    ._7_2(n8_bit_counter_1__0_2[7]), ._6_2(n8_bit_counter_1__0_2[6]), ._5_2(n8_bit_counter_1__0_2[5]),
    ._4_2(n8_bit_counter_1__0_2[4]), ._3_2(n8_bit_counter_1__0_2[3]), ._2_2(n8_bit_counter_1__0_2[2]),
    ._1_2(n8_bit_counter_1__0_2[1]), ._0_2(n8_bit_counter_1__0_2[0]), ._7(1'b0), ._6(1'b0), ._5(1'b0),
    ._4(1'b0), ._3(1'b0), ._2(1'b0), ._1(1'b0), ._0(1'b0), .Decrement_Mode(and_1_out),
    .Count(control_panel_1_program_reset_out));  // open: Set, Count_Out, Set_Carry, Decrement_Mode_Carry
  _2_Way_Multiplexor u_2_way_multiplexor_1 (
    ._0(MAR__0_3), ._1(MAR__1_2), ._2(MAR__2_2), ._3(MAR__3_2), ._4(MAR__4_2), ._5(MAR__5_2), ._6(MAR__6_2),
    ._7(MAR__7_2), ._0_2(n8_bit_counter_1__0_2[0]), ._1_2(n8_bit_counter_1__0_2[1]),
    ._2_2(n8_bit_counter_1__0_2[2]), ._3_2(n8_bit_counter_1__0_2[3]), ._4_2(n8_bit_counter_1__0_2[4]),
    ._5_2(n8_bit_counter_1__0_2[5]), ._6_2(n8_bit_counter_1__0_2[6]), ._7_2(n8_bit_counter_1__0_2[7]),
    .S(control_panel_1_enable_write), ._0_3(n2_way_multiplexor_1__0_3[0]),
    ._1_3(n2_way_multiplexor_1__0_3[1]), ._2_3(n2_way_multiplexor_1__0_3[2]),
    ._3_3(n2_way_multiplexor_1__0_3[3]), ._4_3(n2_way_multiplexor_1__0_3[4]),
    ._5_3(n2_way_multiplexor_1__0_3[5]), ._6_3(n2_way_multiplexor_1__0_3[6]),
    ._7_3(n2_way_multiplexor_1__0_3[7]));
  ROM rom_3 (.addr(n8_bit_counter_1__0_2), .data(rom_3_data));  // open: sel
  // Probe on IR__0_2
  _8_bit_Register IR (
    ._6(MBR__6_2), ._5(MBR__5_2), ._4(MBR__4_2), ._3(MBR__3_2), ._2(MBR__2_2), ._1(MBR__1_2), ._0(MBR__0_3),
    ._0_3(IR__0_3), ._1_2(IR__1_2), ._2_2(IR__2_2), ._3_2(IR__3_2), ._4_2(IR__4_2), ._5_2(IR__5_2),
    ._6_2(IR__6_2), ._0_2(IR__0_2), .in_1({8{1'b0}}), ._7_2(IR__7_2), ._7(MBR__7_2));  // open: Reset, Clock, Enable
  Hex_Digit_Display hex_digit_display_1 (.value(SP_2__4_2));  // open: dp
  assign controlled_buffer_1_out = _2 ? rom_3_data : 8'bz;  // Controlled_Buffer_part controlled_buffer_3
  Hex_Digit_Display hex_digit_display_2 (.value(SP_2__0_2));  // open: dp
  _8_bit_Counter SP_2 (
    .Set(PC_2_set_carry), ._7_2(SP_2__4_2[3]), ._6_2(SP_2__4_2[2]), ._5_2(SP_2__4_2[1]), ._4_2(SP_2__4_2[0]),
    ._3_2(SP_2__0_2[3]), ._2_2(SP_2__0_2[2]), ._1_2(SP_2__0_2[1]), ._0_2(SP_2__0_2[0]), ._7(in_25),
    ._6(in_25), ._5(in_25), ._4(in_25), ._3(in_25), ._2(in_25), ._1(in_25), ._0(in_25),
    .Decrement_Mode(PC_2_decrement_mode_carry), .Count(PC_2_count_out));  // open: Count_Out, Set_Carry, Decrement_Mode_Carry
  Hex_Digit_Display hex_digit_display_3 (.value(PC_2__4_2));  // open: dp
  Hex_Digit_Display hex_digit_display_4 (.value(PC_2__0_2));  // open: dp
  _8_bit_Counter PC_2 (
    .Set(in_23), ._7_2(PC_2__4_2[3]), ._6_2(PC_2__4_2[2]), ._5_2(PC_2__4_2[1]), ._4_2(PC_2__4_2[0]),
    ._3_2(PC_2__0_2[3]), ._2_2(PC_2__0_2[2]), ._1_2(PC_2__0_2[1]), ._0_2(PC_2__0_2[0]), ._7(in_25),
    ._6(in_25), ._5(in_25), ._4(in_25), ._3(in_25), ._2(in_25), ._1(in_25), ._0(in_25),
    .Count_Out(PC_2_count_out), .Set_Carry(PC_2_set_carry), .Decrement_Mode(in_20),
    .Decrement_Mode_Carry(PC_2_decrement_mode_carry), .Count(clock_1_out));
  ROM rom_4 (.addr(n8_bit_counter_1__0_2), .data(rom_4_data));  // open: sel
  assign controlled_buffer_1_out = _3 ? rom_4_data : 8'bz;  // Controlled_Buffer_part controlled_buffer_4
  // Probe on Accumulator_A__0_2
  _8_bit_Register Accumulator_A (
    ._6(undriven_2), ._5(undriven_4), ._4(undriven_5), ._3(undriven), ._2(undriven_6), ._1(undriven_7),
    ._0(undriven_8), ._0_3(Accumulator_A__0_3), ._1_2(Accumulator_A__1_2), ._2_2(Accumulator_A__2_2),
    ._3_2(Accumulator_A__3_2), ._4_2(Accumulator_A__4_2), ._5_2(Accumulator_A__5_2),
    ._6_2(Accumulator_A__6_2), ._0_2(Accumulator_A__0_2), .in_1({8{1'b0}}), ._7_2(Accumulator_A__7_2),
    ._7(undriven_3), .Reset(undriven_17), .Clock(undriven_10), .Enable(undriven_11));
  // Probe on Accumulator_B__0_2
  _8_bit_Register Accumulator_B (
    ._6(undriven_2), ._5(undriven_4), ._4(undriven_5), ._3(undriven), ._2(undriven_6), ._1(undriven_7),
    ._0(undriven_8), ._0_3(Accumulator_B__0_3), ._1_2(Accumulator_B__1_2), ._2_2(Accumulator_B__2_2),
    ._3_2(Accumulator_B__3_2), ._4_2(Accumulator_B__4_2), ._5_2(Accumulator_B__5_2),
    ._6_2(Accumulator_B__6_2), ._0_2(Accumulator_B__0_2), .in_1({8{1'b0}}), ._7_2(Accumulator_B__7_2),
    ._7(undriven_3), .Reset(undriven_17), .Clock(undriven_10), .Enable(undriven_12));
  Clock clock_1 (.out(clock_1_out));
  LED led_1 (.in(control_panel_1_system_clock));
  Control_Panel control_panel_1 (
    .Program_Reset_Out(control_panel_1_program_reset_out), .Write_Next_Byte(control_panel_1_write_next_byte),
    .Pregram_Reset(Program_Reset_out), .Write_Byte(Write_Byte_out),
    .Enable_Program_Write(Enable_Program_Write), .Reset(Reset_out), .Enable_Auto_Clock(Auto_Clock),
    .Tick(Tick_out), .One_by_One(One_by_One), .Reset_Out(control_panel_1_reset_out),
    .Clock(control_panel_1_clock), .One_by_One_2(control_panel_1_one_by_one_2),
    .Enable_Write(control_panel_1_enable_write), .Next_Instruction_2(control_panel_1_next_instruction_2),
    .Next_Instruction(Next_Instruction_out), .System_Clock(control_panel_1_system_clock));
  _3_Way_Multiplexor u_3_way_multiplexor_1 (
    ._0_2(x_1__0_2), ._1_2(x_1__1_2), ._2_2(x_1__2_2), ._3_2(x_1__3_2), ._4_2(x_1__4_2), ._5_2(x_1__5_2),
    ._6_2(x_1__6_2), ._7_2(x_1__7_2), ._0_3(multiplexer_1_out[0]), ._1_3(multiplexer_1_out[1]),
    ._2_3(multiplexer_1_out[2]), ._3_3(multiplexer_1_out[3]), ._4_3(multiplexer_1_out[4]),
    ._5_3(multiplexer_1_out[5]), ._6_3(multiplexer_1_out[6]), ._7_3(multiplexer_1_out[7]),
    ._7_4(n3_way_multiplexor_1__0_4[7]), ._6_4(n3_way_multiplexor_1__0_4[6]),
    ._5_4(n3_way_multiplexor_1__0_4[5]), ._4_4(n3_way_multiplexor_1__0_4[4]),
    ._3_4(n3_way_multiplexor_1__0_4[3]), ._2_4(n3_way_multiplexor_1__0_4[2]),
    ._1_4(n3_way_multiplexor_1__0_4[1]), ._0_4(n3_way_multiplexor_1__0_4[0]), .S0(1'b1),
    .S1(control_panel_1_enable_write));  // open: _7, _6, _5, _4, _3, _2, _1, _0
  Control_Unit control_unit_1 (
    .Clock(control_panel_1_clock), .Not_Equal(condition_code_register_1_not_equal_2),
    .B_Greater_A(condition_code_register_1_b_greater_a_2),
    .A_Greater_B(condition_code_register_1_a_greater_b_2), .Carry_Out(condition_code_register_1_overflow_2),
    .Nero(undriven_15), .Negative(undriven_16), .Clock_B_Greater_A(control_unit_1_clock_b_greater_a),
    .Clock_CCR(control_unit_1_clock_ccr), .M_Clock(control_unit_1_m_clock), ._7(IR__7_2), ._6(IR__6_2),
    ._5(IR__5_2), ._4(IR__4_2), ._3(IR__3_2), ._2(IR__2_2), ._1(IR__1_2), ._0(IR__0_3),
    .A_Invert(control_unit_1_a_invert), .B_Invert(control_unit_1_b_invert), .AND(control_unit_1_and),
    .OR(control_unit_1_or), .A(control_unit_1_a), .B(control_unit_1_b),
    .Shift_A_Right(control_unit_1_shift_a_right), .Shift_B_Right(control_unit_1_shift_b_right),
    .Shift_Loop(control_unit_1_shift_loop), .Shift_A_Left(control_unit_1_shift_a_left),
    .Shift_B_Left(control_unit_1_shift_b_left), .XOR(control_unit_1_xor),
    .Increment(control_unit_1_increment), .ADD(control_unit_1_add), .X_Invert(control_unit_1_x_invert),
    .Reset(control_panel_1_reset_out), .Next_Instruction(control_panel_1_next_instruction_2),
    .One_by_One(control_panel_1_one_by_one_2), .Multiply(control_unit_1_multiply));  // open: MP_ALU_A_S0, MP_ALU_A_S1, MP_ALU_B_S0, MP_ALU_B_S1, MAR_Clock, MBR_Clock, Acc_X_Clock, Acc_A_Clock, Acc_B_Clock, Acc_Y_Clock, A_Clock, MAR_Reset, MBR_Reset, AX_Reset, AA_Reset, AB_Reset, AY_Reset, A_Reset, PC_Set, PC_Count, Set_Carry_Selector, Set_Carry_Data, MP_MAR_S1, MP_MAR_S0, MP_PC_S0, IR_Reset, IR_Clock, MP_PC_S1, Stack_Pop, Stack_Push, Stack_Reset, Display_Clock, MP_MAR_S2, Read_Input, Input_Available, Reset_IO, Set_MAR_Add_MBR
  ALU alu_1 (
    .A0(Accumulator_A__0_3), .B0(Accumulator_B__0_3), .A1(Accumulator_A__1_2), .B1(Accumulator_B__1_2),
    .A2(Accumulator_A__2_2), .B2(Accumulator_B__2_2), .A3(Accumulator_A__3_2), .B3(Accumulator_B__3_2),
    .A4(Accumulator_A__4_2), .B4(Accumulator_B__4_2), .A5(Accumulator_A__5_2), .B5(Accumulator_B__5_2),
    .A6(Accumulator_A__6_2), .B6(Accumulator_B__6_2), .A7(Accumulator_A__7_2), .B7(Accumulator_B__7_2),
    .X0(alu_1_x0), .X1(alu_1_x1), .X2(alu_1_x2), .X3(alu_1_x3), .X4(alu_1_x4), .X5(alu_1_x5), .X6(alu_1_x6),
    .X7(alu_1_x7), .A_Invert(control_unit_1_a_invert), .B_Invert(control_unit_1_b_invert),
    .AND(control_unit_1_and), .OR(control_unit_1_or), .A(control_unit_1_a), .B(control_unit_1_b),
    .Shift_A_Right(control_unit_1_shift_a_right), .Shift_B_Right(control_unit_1_shift_b_right),
    .Shift_A_Left(control_unit_1_shift_a_left), .Shift_B_Left(control_unit_1_shift_b_left),
    .XOR(control_unit_1_xor), .Increment(control_unit_1_increment), .ADD(control_unit_1_add),
    .X_Invert(control_unit_1_x_invert), .Not_Equal(alu_1_not_equal), .B_Greater_A(alu_1_b_greater_a),
    .A_Greater_B(alu_1_a_greater_b), .Overflow(alu_1_overflow), .Shift_Loop(control_unit_1_shift_loop),
    .Zero(alu_1_zero), .Multiply(control_unit_1_multiply));
  Button Program_Reset (.out(Program_Reset_out));
  Button Write_Byte (.out(Write_Byte_out));
  Button Reset (.out(Reset_out));
  Button Tick (.out(Tick_out));
  Button Next_Instruction (.out(Next_Instruction_out));
  X x_1 (
    ._0_2(x_1__0_2), ._1_2(x_1__1_2), ._2_2(x_1__2_2), ._3_2(x_1__3_2), ._4_2(x_1__4_2), ._5_2(x_1__5_2),
    ._6_2(x_1__6_2), ._7_2(x_1__7_2), ._7(undriven_14), ._6(undriven_13), ._5(undriven_18), ._4(undriven_19),
    ._3(undriven_20), ._2(undriven_21), ._1(undriven_22), ._0(undriven_23));
  assign controlled_buffer_5_out = in_21 ? in_19 : 1'bz;  // Controlled_Buffer_part controlled_buffer_5
  Pull_Resistor pull_resistor_1 (.node(controlled_buffer_5_out));
  assign controlled_buffer_5_out = in_24 ? in_22 : 1'bz;  // Controlled_Buffer_part controlled_buffer_6
  // Probe on Accumulator__0_2
  _8_bit_Register Accumulator (
    ._6(alu_1_x6), ._5(alu_1_x5), ._4(alu_1_x4), ._3(alu_1_x3), ._2(alu_1_x2), ._1(alu_1_x1), ._0(alu_1_x0),
    ._0_3(Accumulator__0_3), ._1_2(Accumulator__1_2), ._2_2(Accumulator__2_2), ._3_2(Accumulator__3_2),
    ._4_2(Accumulator__4_2), ._5_2(Accumulator__5_2), ._6_2(Accumulator__6_2), ._0_2(Accumulator__0_2),
    .in_1({8{1'b0}}), ._7_2(Accumulator__7_2), ._7(alu_1_x7), .Reset(undriven_17), .Clock(undriven_10),
    .Enable(undriven_9));
  _8_bit_Register MAR_Offset (
    ._6(undriven_22), ._5(undriven_21), ._4(undriven_20), ._3(undriven_19), ._2(undriven_18),
    ._1(undriven_13), ._0(undriven_14), ._0_3(MAR_Offset__0_3), ._1_2(MAR_Offset__1_2),
    ._2_2(MAR_Offset__2_2), ._3_2(MAR_Offset__3_2), ._4_2(MAR_Offset__4_2), ._5_2(MAR_Offset__5_2),
    ._6_2(MAR_Offset__6_2), ._0_2(MAR_Offset__0_2), .in_1({8{1'b0}}), ._7_2(MAR_Offset__7_2),
    ._7(undriven_23), .Reset(undriven_24), .Clock(undriven_25));  // open: Enable
  // Probe on MAR_Offset__0_2
  _8_bit_Adder u_8_bit_adder_1 (
    .A0(MAR_Offset__0_3), .B0(undriven_14), .A1(MAR_Offset__1_2), .B1(undriven_13), .A2(MAR_Offset__2_2),
    .B2(undriven_18), .A3(MAR_Offset__3_2), .B3(undriven_19), .A4(MAR_Offset__4_2), .B4(undriven_20),
    .A5(MAR_Offset__5_2), .B5(undriven_21), .A6(MAR_Offset__6_2), .B6(undriven_22), .A7(MAR_Offset__7_2),
    .B7(undriven_23), .X0(n8_bit_adder_1_x0), .X1(n8_bit_adder_1_x1), .X2(n8_bit_adder_1_x2),
    .X3(n8_bit_adder_1_x3), .X4(n8_bit_adder_1_x4), .X5(n8_bit_adder_1_x5), .X6(n8_bit_adder_1_x6),
    .X7(n8_bit_adder_1_x7), .Increment(1'b0), .Carry_Out(n8_bit_adder_1_carry_out));
  // Probe on MAR__0_2
  _8_bit_Register MAR (
    ._6(n8_bit_adder_1_x6), ._5(n8_bit_adder_1_x5), ._4(n8_bit_adder_1_x4), ._3(n8_bit_adder_1_x3),
    ._2(n8_bit_adder_1_x2), ._1(n8_bit_adder_1_x1), ._0(n8_bit_adder_1_x0), ._0_3(MAR__0_3), ._1_2(MAR__1_2),
    ._2_2(MAR__2_2), ._3_2(MAR__3_2), ._4_2(MAR__4_2), ._5_2(MAR__5_2), ._6_2(MAR__6_2), ._0_2(MAR__0_2),
    .in_1({8{1'b0}}), ._7_2(MAR__7_2), ._7(n8_bit_adder_1_x7), .Reset(undriven_28), .Clock(undriven_29));  // open: Enable
  LED led_2 (.in(condition_code_register_1_not_equal_2));
  Condition_Code_Register condition_code_register_1 (
    .Not_Equal(alu_1_not_equal), .B_Greater_A(alu_1_b_greater_a), .A_Greater_B(alu_1_a_greater_b),
    .Overflow(alu_1_overflow), .Zero(alu_1_zero), .Negative(Accumulator__7_2),
    .Not_Equal_2(condition_code_register_1_not_equal_2),
    .B_Greater_A_2(condition_code_register_1_b_greater_a_2),
    .A_Greater_B_2(condition_code_register_1_a_greater_b_2),
    .Overflow_2(condition_code_register_1_overflow_2), .Zero_2(condition_code_register_1_zero_2),
    .Negative_2(condition_code_register_1_negative_2), .Waiting_2(condition_code_register_1_waiting_2),
    .Finished_2(condition_code_register_1_finished_2), .Clear_Finished(undriven_26),
    .Clear_Wait(undriven_27), .Clock(control_unit_1_clock_ccr));  // open: Waiting, Finished
  LED led_3 (.in(condition_code_register_1_b_greater_a_2));
  LED led_4 (.in(condition_code_register_1_a_greater_b_2));
  LED led_5 (.in(condition_code_register_1_overflow_2));
  LED led_6 (.in(condition_code_register_1_zero_2));
  LED led_7 (.in(condition_code_register_1_negative_2));
  LED led_8 (.in(condition_code_register_1_waiting_2));
  LED led_9 (.in(condition_code_register_1_finished_2));
  TTY #(.rows(10)) tty_1 (.data(undriven_31), .clk(undriven_30), .clr(or_2_out));  // open: we
  or or_2 (or_2_out, and_9_out, undriven_32);
  Keyboard keyboard_1 (
    .clk(undriven_33), .clr(or_3_out), .avail(keyboard_1_avail), .data(keyboard_1_data));  // open: re
  buf and_9 (and_9_out, undriven_30);  // AND_Gate
  or or_3 (or_3_out, undriven_32, Clear_Input_out);
  Button Clear_Input (.out(Clear_Input_out));
  Demultiplexer #(.select(4), .width(8), .enable("false")) demultiplexer_1 ();  // open: out0, out1, out2, out3, out4, out5, out6, out7, out8, out9, out10, out11, out12, out13, out14, out15, in, sel
  // Probe on joystick_1_x
  Joystick joystick_1 (.x(joystick_1_x), .y(joystick_1_y));
  // Probe on joystick_1_y
  LED_Matrix_Controller led_matrix_controller_1 (
    .Value(in_1), .Clear(in_6), .Clock(in_7), .out_12(led_matrix_controller_1_out_12),
    .out_13(led_matrix_controller_1_out_13), .out_14(led_matrix_controller_1_out_14),
    .out_15(led_matrix_controller_1_out_15), .out_16(led_matrix_controller_1_out_16),
    .out_17(led_matrix_controller_1_out_17), .out_18(led_matrix_controller_1_out_18),
    .out_19(led_matrix_controller_1_out_19), .out_20(led_matrix_controller_1_out_20),
    .out_21(led_matrix_controller_1_out_21), .out_22(led_matrix_controller_1_out_22),
    .out_23(led_matrix_controller_1_out_23), .out_24(led_matrix_controller_1_out_24),
    .out_25(led_matrix_controller_1_out_25), .out_26(led_matrix_controller_1_out_26),
    .out_27(led_matrix_controller_1_out_27), .in_4(in_11), .in_5(in_12), .in_6(in_13), .in_7(in_14),
    .in_8(in_15), .in_9(in_16), .in_10(in_17), .in_11(in_18));
  Multiplexer #(.select(4), .width(8), .enable("false")) multiplexer_2 ();  // open: in0, in1, in2, in3, in4, in5, in6, in7, in8, in9, in10, in11, in12, in13, in14, in15, out, sel
  DotMatrix #(.inputtype("row"), .matrixcols(16), .matrixrows(16)) dotmatrix_1 (
    .row0(led_matrix_controller_1_out_12), .row1(led_matrix_controller_1_out_13),
    .row2(led_matrix_controller_1_out_14), .row3(led_matrix_controller_1_out_15),
    .row4(led_matrix_controller_1_out_16), .row5(led_matrix_controller_1_out_17),
    .row6(led_matrix_controller_1_out_18), .row7(led_matrix_controller_1_out_19),
    .row8(led_matrix_controller_1_out_20), .row9(led_matrix_controller_1_out_21),
    .row10(led_matrix_controller_1_out_22), .row11(led_matrix_controller_1_out_23),
    .row12(led_matrix_controller_1_out_24), .row13(led_matrix_controller_1_out_25),
    .row14(led_matrix_controller_1_out_26), .row15(led_matrix_controller_1_out_27));

  // Notes on the sheet:
  //   Program 0
  //   contents of rom_1 (hex, n*v repeats v):
  //   36 0 3a 0 34 15 6f 78 d 4e 26 75 4 52 a 58 56 4e 75 f 3 48 65 6c 6c 6f 20 57 6f 72 6c 64 21 20 3a 29
  //   Program 1
  //   contents of rom_2 (hex, n*v repeats v):
  //   58 56 4e 20 46 71 a 7a b 20 47 59 52 20 52 2b 52 20 58 56 4e 20 46 71 a 7a 1d 20 47 10 52 20 52 3d
  //   52 20 5d 36 f0 3e f 8c 8f 4*65 19 46 71 39 7c 37 19 47 4e 5e 19 46 71 39 7c 41 19 47 4e 52 a 75 0 30
  //   7 0 0 1 8
  //   Program 2
  //   contents of rom_3 (hex, n*v repeats v):
  //   58 56 4e 20 46 71 a 7a b 20 47 59 52 20 52 78 52 20 58 56 4e 20 46 71 a 7a 1d 20 47 4 52 20 52 3d 52
  //   20 5d 36 f0 3e f 8c 8f 4*65 19 46 71 39 7c 37 19 47 4e 5e 19 46 71 39 7c 41 19 47 4e 52 a 75 0 30 7
  //   0 0 1 8
  //   Program 3
  //   contents of rom_4 (hex, n*v repeats v):
  //   37 0 3b 0 35 22 70 79 d 4f 27 76 4 53 a 1 1b 53 58 53 a 59 57 4f 76 15 4 53 46 53 75 53 6e 3 48 65
  //   6c 6c 6f 20 57 6f 72 6c 64 21 20 3a 29
endmodule

module _1_bit_ALU (
  input  SLAI,
  input  SLBI,
  input  Carry_in,
  input  A_invert,
  input  B_invert,
  input  And,
  input  Or,
  input  A,
  input  B,
  input  SRA,
  input  SRB,
  input  SLA,
  input  SLB,
  input  XOr,
  input  Add,
  input  X_invert,
  input  Not_Zero_In,
  input  A_2,
  input  B_2,
  input  NEI,
  input  GRI,
  input  LSI,
  input  SRAI,
  input  SRBI,
  output SRAO,
  output SRBO,
  output NEO,
  output GRO,
  output LSO,
  output X,
  output out_31,
  output out_32,
  output out_33,
  output out_34,
  output out_35,
  output out_36,
  output out_37,
  output out_38,
  output out_39,
  output out_40,
  output out_41,
  output Carry_out,
  output out_43,
  output out_44,
  output Not_Zero_Out,
  output SLAO,
  output SLBO
);

  wire and_1_out, and_2_out, and_5_out, and_6_out, and_7_out, and_8_out, and_9_out, and_10_out, and_11_out,
       and_12_out, and_13_out, and_14_out, and_15_out, and_16_out, and_17_out, and_18_out, and_19_out,
       and_20_out, and_21_out, and_22_out, and_23_out, and_24_out, and_25_out, and_26_out, not_1_out,
       not_2_out, not_3_out, not_4_out, not_5_out, not_6_out, not_7_out, not_8_out, not_9_out, not_10_out,
       or_1_out, or_2_out, or_3_out, or_4_out, or_5_out, or_6_out, or_7_out, or_8_out, or_9_out, or_10_out,
       or_12_out, or_13_out, or_16_out, or_18_out, or_19_out, or_20_out;

  or or_1 (or_1_out, A_invert, A_2);
  and and_1 (and_1_out, A_invert, A_2);
  and and_2 (and_2_out, B_2, B_invert);
  or or_2 (or_2_out, B_2, B_invert);
  and and_3 (SLAO, or_1_out, not_1_out);
  not not_1 (not_1_out, and_1_out);
  not not_2 (not_2_out, and_2_out);
  and and_4 (SLBO, not_2_out, or_2_out);
  and and_5 (and_5_out, SLBO, SLAO);
  or or_3 (or_3_out, SLBO, SLAO);
  and and_6 (and_6_out, and_5_out, And);
  and and_7 (and_7_out, or_3_out, Or);
  and and_8 (and_8_out, SLAO, A);
  or or_4 (or_4_out, and_7_out, and_6_out);
  and and_9 (and_9_out, SLBO, B);
  or or_5 (or_5_out, and_9_out, or_6_out);
  or or_6 (or_6_out, and_8_out, or_4_out);
  and and_10 (and_10_out, SRAI, SRA);
  and and_11 (and_11_out, SRBI, SRB);
  or or_7 (or_7_out, and_10_out, or_5_out);
  or or_8 (or_8_out, or_7_out, and_11_out);
  and and_12 (and_12_out, SLBI, SLB);
  or or_9 (or_9_out, and_12_out, and_13_out);
  and and_13 (and_13_out, SLAI, SLA);
  or or_10 (or_10_out, SLAO, SLBO);
  and and_14 (and_14_out, SLAO, SLBO);
  not not_3 (not_3_out, and_14_out);
  and and_15 (and_15_out, or_10_out, not_3_out);
  or or_11 (NEO, and_15_out, NEI);
  and and_16 (and_16_out, and_15_out, XOr);
  or or_12 (or_12_out, and_16_out, or_8_out);
  not not_4 (not_4_out, SLAO);
  and and_17 (and_17_out, not_4_out, SLBO);
  or or_13 (or_13_out, or_9_out, or_12_out);
  or or_14 (GRO, and_18_out, GRI);
  and and_18 (and_18_out, and_17_out, not_5_out);
  not not_5 (not_5_out, LSI);
  not not_6 (not_6_out, GRI);
  not not_7 (not_7_out, SLBO);
  or or_15 (LSO, and_19_out, LSI);
  and and_19 (and_19_out, not_6_out, and_20_out);
  and and_20 (and_20_out, SLAO, not_7_out);
  or or_16 (or_16_out, SLAO, SLBO);
  and and_21 (and_21_out, SLAO, SLBO);
  and and_22 (and_22_out, or_16_out, not_8_out);
  not not_8 (not_8_out, and_21_out);
  or or_17 (Carry_out, and_21_out, and_23_out);
  or or_18 (or_18_out, and_22_out, Carry_in);
  not not_9 (not_9_out, and_23_out);
  and and_23 (and_23_out, and_22_out, Carry_in);
  and and_24 (and_24_out, or_18_out, not_9_out);
  and and_25 (and_25_out, and_24_out, Add);
  or or_19 (or_19_out, and_25_out, or_13_out);
  or or_20 (or_20_out, X_invert, or_19_out);
  not not_10 (not_10_out, and_26_out);
  and and_26 (and_26_out, X_invert, or_19_out);
  and and_27 (X, or_20_out, not_10_out);
  or or_21 (Not_Zero_Out, X, Not_Zero_In);

  assign out_31 = A_invert;
  assign out_32 = B_invert;
  assign out_33 = And;
  assign out_34 = Or;
  assign out_35 = A;
  assign out_36 = B;
  assign out_37 = SRA;
  assign out_38 = SRB;
  assign out_39 = SLA;
  assign out_40 = SLB;
  assign out_41 = XOr;
  assign out_43 = Add;
  assign out_44 = X_invert;
  assign SRAO = SLAO;
  assign SRBO = SLBO;
endmodule

module ALU (
  input  A_Invert,
  input  B_Invert,
  input  AND,
  input  OR,
  input  A,
  input  B,
  input  Shift_A_Right,
  input  Shift_B_Right,
  input  Shift_Loop,
  input  Shift_A_Left,
  input  Shift_B_Left,
  input  XOR,
  input  Increment,
  input  ADD,
  input  X_Invert,
  input  Multiply,
  input  A0,
  input  A1,
  input  A2,
  input  A3,
  input  A4,
  input  A5,
  input  A6,
  input  A7,
  input  B0,
  input  B1,
  input  B2,
  input  B3,
  input  B4,
  input  B5,
  input  B6,
  input  B7,
  output Not_Equal,
  output B_Greater_A,
  output A_Greater_B,
  output X0,
  output X1,
  output X2,
  output X3,
  output X4,
  output X5,
  output X6,
  output X7,
  output Zero,
  output Overflow
);

  wire and_1_out, and_2_out, and_3_out, and_4_out, n1_bit_alu_1_carry_out, n1_bit_alu_1_not_zero_out,
       n1_bit_alu_1_out_31, n1_bit_alu_1_out_32, n1_bit_alu_1_out_33, n1_bit_alu_1_out_34,
       n1_bit_alu_1_out_35, n1_bit_alu_1_out_36, n1_bit_alu_1_out_37, n1_bit_alu_1_out_38,
       n1_bit_alu_1_out_39, n1_bit_alu_1_out_40, n1_bit_alu_1_out_41, n1_bit_alu_1_out_43,
       n1_bit_alu_1_out_44, n1_bit_alu_1_slao, n1_bit_alu_1_slbo, n1_bit_alu_1_srao, n1_bit_alu_1_srbo,
       n1_bit_alu_1_x, n1_bit_alu_2_carry_out, n1_bit_alu_2_gro, n1_bit_alu_2_lso, n1_bit_alu_2_neo,
       n1_bit_alu_2_not_zero_out, n1_bit_alu_2_out_31, n1_bit_alu_2_out_32, n1_bit_alu_2_out_33,
       n1_bit_alu_2_out_34, n1_bit_alu_2_out_35, n1_bit_alu_2_out_36, n1_bit_alu_2_out_37,
       n1_bit_alu_2_out_38, n1_bit_alu_2_out_39, n1_bit_alu_2_out_40, n1_bit_alu_2_out_41,
       n1_bit_alu_2_out_43, n1_bit_alu_2_out_44, n1_bit_alu_2_slao, n1_bit_alu_2_slbo, n1_bit_alu_2_srao,
       n1_bit_alu_2_srbo, n1_bit_alu_2_x, n1_bit_alu_3_carry_out, n1_bit_alu_3_gro, n1_bit_alu_3_lso,
       n1_bit_alu_3_neo, n1_bit_alu_3_not_zero_out, n1_bit_alu_3_out_31, n1_bit_alu_3_out_32,
       n1_bit_alu_3_out_33, n1_bit_alu_3_out_34, n1_bit_alu_3_out_35, n1_bit_alu_3_out_36,
       n1_bit_alu_3_out_37, n1_bit_alu_3_out_38, n1_bit_alu_3_out_39, n1_bit_alu_3_out_40,
       n1_bit_alu_3_out_41, n1_bit_alu_3_out_43, n1_bit_alu_3_out_44, n1_bit_alu_3_slao, n1_bit_alu_3_slbo,
       n1_bit_alu_3_srao, n1_bit_alu_3_srbo, n1_bit_alu_3_x, n1_bit_alu_4_carry_out, n1_bit_alu_4_gro,
       n1_bit_alu_4_lso, n1_bit_alu_4_neo, n1_bit_alu_4_not_zero_out, n1_bit_alu_4_out_31,
       n1_bit_alu_4_out_32, n1_bit_alu_4_out_33, n1_bit_alu_4_out_34, n1_bit_alu_4_out_35,
       n1_bit_alu_4_out_36, n1_bit_alu_4_out_37, n1_bit_alu_4_out_38, n1_bit_alu_4_out_39,
       n1_bit_alu_4_out_40, n1_bit_alu_4_out_41, n1_bit_alu_4_out_43, n1_bit_alu_4_out_44, n1_bit_alu_4_slao,
       n1_bit_alu_4_slbo, n1_bit_alu_4_srao, n1_bit_alu_4_srbo, n1_bit_alu_4_x, n1_bit_alu_5_carry_out,
       n1_bit_alu_5_gro, n1_bit_alu_5_lso, n1_bit_alu_5_neo, n1_bit_alu_5_not_zero_out, n1_bit_alu_5_out_31,
       n1_bit_alu_5_out_32, n1_bit_alu_5_out_33, n1_bit_alu_5_out_34, n1_bit_alu_5_out_35,
       n1_bit_alu_5_out_36, n1_bit_alu_5_out_37, n1_bit_alu_5_out_38, n1_bit_alu_5_out_39,
       n1_bit_alu_5_out_40, n1_bit_alu_5_out_41, n1_bit_alu_5_out_43, n1_bit_alu_5_out_44, n1_bit_alu_5_slao,
       n1_bit_alu_5_slbo, n1_bit_alu_5_srao, n1_bit_alu_5_srbo, n1_bit_alu_5_x, n1_bit_alu_6_carry_out,
       n1_bit_alu_6_gro, n1_bit_alu_6_lso, n1_bit_alu_6_neo, n1_bit_alu_6_not_zero_out, n1_bit_alu_6_out_31,
       n1_bit_alu_6_out_32, n1_bit_alu_6_out_33, n1_bit_alu_6_out_34, n1_bit_alu_6_out_35,
       n1_bit_alu_6_out_36, n1_bit_alu_6_out_37, n1_bit_alu_6_out_38, n1_bit_alu_6_out_39,
       n1_bit_alu_6_out_40, n1_bit_alu_6_out_41, n1_bit_alu_6_out_43, n1_bit_alu_6_out_44, n1_bit_alu_6_slao,
       n1_bit_alu_6_slbo, n1_bit_alu_6_srao, n1_bit_alu_6_srbo, n1_bit_alu_6_x, n1_bit_alu_7_carry_out,
       n1_bit_alu_7_gro, n1_bit_alu_7_lso, n1_bit_alu_7_neo, n1_bit_alu_7_not_zero_out, n1_bit_alu_7_out_31,
       n1_bit_alu_7_out_32, n1_bit_alu_7_out_33, n1_bit_alu_7_out_34, n1_bit_alu_7_out_35,
       n1_bit_alu_7_out_36, n1_bit_alu_7_out_37, n1_bit_alu_7_out_38, n1_bit_alu_7_out_39,
       n1_bit_alu_7_out_40, n1_bit_alu_7_out_41, n1_bit_alu_7_out_43, n1_bit_alu_7_out_44, n1_bit_alu_7_slao,
       n1_bit_alu_7_slbo, n1_bit_alu_7_srao, n1_bit_alu_7_srbo, n1_bit_alu_7_x, n1_bit_alu_8_carry_out,
       n1_bit_alu_8_gro, n1_bit_alu_8_lso, n1_bit_alu_8_neo, n1_bit_alu_8_not_zero_out, n1_bit_alu_8_out_39,
       n1_bit_alu_8_slao, n1_bit_alu_8_srao, n1_bit_alu_8_srbo, n1_bit_alu_8_x, n8_bit_multiplier_1_overflow,
       n8_bit_multiplier_1_x0, n8_bit_multiplier_1_x1, n8_bit_multiplier_1_x2, n8_bit_multiplier_1_x3,
       n8_bit_multiplier_1_x4, n8_bit_multiplier_1_x5, n8_bit_multiplier_1_x6, n8_bit_multiplier_1_x7;

  _8_bit_Multiplier u_8_bit_multiplier_1 (
    .A0(B0), .A1(B1), .A2(B2), .A3(B3), .A4(B4), .A5(B5), .A6(B6), .A7(B7), .X0(n8_bit_multiplier_1_x0),
    .X1(n8_bit_multiplier_1_x1), .X2(n8_bit_multiplier_1_x2), .X3(n8_bit_multiplier_1_x3),
    .X4(n8_bit_multiplier_1_x4), .X5(n8_bit_multiplier_1_x5), .X6(n8_bit_multiplier_1_x6),
    .X7(n8_bit_multiplier_1_x7), .Overflow(n8_bit_multiplier_1_overflow), .B7(A7), .B6(A6), .B5(A5), .B4(A4),
    .B3(A3), .B2(A2), .B1(A1), .B0(A0));
  and and_1 (and_1_out, n1_bit_alu_1_srbo, Shift_Loop);
  and and_2 (and_2_out, n1_bit_alu_1_srao, Shift_Loop);
  and and_3 (and_3_out, Shift_Loop, n1_bit_alu_8_slao);
  and and_4 (and_4_out, Shift_Loop, n1_bit_alu_8_out_39);
  _1_bit_ALU u_1_bit_alu_1 (
    .A_2(A0), .B_2(B0), .X(n1_bit_alu_1_x), .A_invert(A_Invert), .B_invert(B_Invert), .And(AND), .Or(OR),
    .A(A), .B(B), .SRAO(n1_bit_alu_1_srao), .SRBO(n1_bit_alu_1_srbo), .SRA(Shift_A_Right),
    .SRB(Shift_B_Right), .SLAI(and_3_out), .SLBI(and_4_out), .SLA(Shift_A_Left), .SLB(Shift_B_Left),
    .XOr(XOR), .NEO(Not_Equal), .GRO(B_Greater_A), .LSO(A_Greater_B), .Carry_in(Increment), .Add(ADD),
    .X_invert(X_Invert), .out_31(n1_bit_alu_1_out_31), .out_32(n1_bit_alu_1_out_32),
    .out_33(n1_bit_alu_1_out_33), .out_34(n1_bit_alu_1_out_34), .out_35(n1_bit_alu_1_out_35),
    .out_36(n1_bit_alu_1_out_36), .SRAI(n1_bit_alu_2_srao), .SRBI(n1_bit_alu_2_srbo),
    .out_37(n1_bit_alu_1_out_37), .out_38(n1_bit_alu_1_out_38), .SLAO(n1_bit_alu_1_slao),
    .SLBO(n1_bit_alu_1_slbo), .out_39(n1_bit_alu_1_out_39), .out_40(n1_bit_alu_1_out_40),
    .out_41(n1_bit_alu_1_out_41), .NEI(n1_bit_alu_2_neo), .GRI(n1_bit_alu_2_gro), .LSI(n1_bit_alu_2_lso),
    .Carry_out(n1_bit_alu_1_carry_out), .out_43(n1_bit_alu_1_out_43), .out_44(n1_bit_alu_1_out_44),
    .Not_Zero_In(1'b0), .Not_Zero_Out(n1_bit_alu_1_not_zero_out));
  _1_bit_ALU u_1_bit_alu_2 (
    .A_2(A1), .B_2(B1), .X(n1_bit_alu_2_x), .A_invert(n1_bit_alu_1_out_31), .B_invert(n1_bit_alu_1_out_32),
    .And(n1_bit_alu_1_out_33), .Or(n1_bit_alu_1_out_34), .A(n1_bit_alu_1_out_35), .B(n1_bit_alu_1_out_36),
    .SRAO(n1_bit_alu_2_srao), .SRBO(n1_bit_alu_2_srbo), .SRA(n1_bit_alu_1_out_37), .SRB(n1_bit_alu_1_out_38),
    .SLAI(n1_bit_alu_1_slao), .SLBI(n1_bit_alu_1_slbo), .SLA(n1_bit_alu_1_out_39), .SLB(n1_bit_alu_1_out_40),
    .XOr(n1_bit_alu_1_out_41), .NEO(n1_bit_alu_2_neo), .GRO(n1_bit_alu_2_gro), .LSO(n1_bit_alu_2_lso),
    .Carry_in(n1_bit_alu_1_carry_out), .Add(n1_bit_alu_1_out_43), .X_invert(n1_bit_alu_1_out_44),
    .out_31(n1_bit_alu_2_out_31), .out_32(n1_bit_alu_2_out_32), .out_33(n1_bit_alu_2_out_33),
    .out_34(n1_bit_alu_2_out_34), .out_35(n1_bit_alu_2_out_35), .out_36(n1_bit_alu_2_out_36),
    .SRAI(n1_bit_alu_3_srao), .SRBI(n1_bit_alu_3_srbo), .out_37(n1_bit_alu_2_out_37),
    .out_38(n1_bit_alu_2_out_38), .SLAO(n1_bit_alu_2_slao), .SLBO(n1_bit_alu_2_slbo),
    .out_39(n1_bit_alu_2_out_39), .out_40(n1_bit_alu_2_out_40), .out_41(n1_bit_alu_2_out_41),
    .NEI(n1_bit_alu_3_neo), .GRI(n1_bit_alu_3_gro), .LSI(n1_bit_alu_3_lso),
    .Carry_out(n1_bit_alu_2_carry_out), .out_43(n1_bit_alu_2_out_43), .out_44(n1_bit_alu_2_out_44),
    .Not_Zero_In(n1_bit_alu_1_not_zero_out), .Not_Zero_Out(n1_bit_alu_2_not_zero_out));
  _1_bit_ALU u_1_bit_alu_3 (
    .A_2(A2), .B_2(B2), .X(n1_bit_alu_3_x), .A_invert(n1_bit_alu_2_out_31), .B_invert(n1_bit_alu_2_out_32),
    .And(n1_bit_alu_2_out_33), .Or(n1_bit_alu_2_out_34), .A(n1_bit_alu_2_out_35), .B(n1_bit_alu_2_out_36),
    .SRAO(n1_bit_alu_3_srao), .SRBO(n1_bit_alu_3_srbo), .SRA(n1_bit_alu_2_out_37), .SRB(n1_bit_alu_2_out_38),
    .SLAI(n1_bit_alu_2_slao), .SLBI(n1_bit_alu_2_slbo), .SLA(n1_bit_alu_2_out_39), .SLB(n1_bit_alu_2_out_40),
    .XOr(n1_bit_alu_2_out_41), .NEO(n1_bit_alu_3_neo), .GRO(n1_bit_alu_3_gro), .LSO(n1_bit_alu_3_lso),
    .Carry_in(n1_bit_alu_2_carry_out), .Add(n1_bit_alu_2_out_43), .X_invert(n1_bit_alu_2_out_44),
    .out_31(n1_bit_alu_3_out_31), .out_32(n1_bit_alu_3_out_32), .out_33(n1_bit_alu_3_out_33),
    .out_34(n1_bit_alu_3_out_34), .out_35(n1_bit_alu_3_out_35), .out_36(n1_bit_alu_3_out_36),
    .SRAI(n1_bit_alu_4_srao), .SRBI(n1_bit_alu_4_srbo), .out_37(n1_bit_alu_3_out_37),
    .out_38(n1_bit_alu_3_out_38), .SLAO(n1_bit_alu_3_slao), .SLBO(n1_bit_alu_3_slbo),
    .out_39(n1_bit_alu_3_out_39), .out_40(n1_bit_alu_3_out_40), .out_41(n1_bit_alu_3_out_41),
    .NEI(n1_bit_alu_4_neo), .GRI(n1_bit_alu_4_gro), .LSI(n1_bit_alu_4_lso),
    .Carry_out(n1_bit_alu_3_carry_out), .out_43(n1_bit_alu_3_out_43), .out_44(n1_bit_alu_3_out_44),
    .Not_Zero_In(n1_bit_alu_2_not_zero_out), .Not_Zero_Out(n1_bit_alu_3_not_zero_out));
  _1_bit_ALU u_1_bit_alu_4 (
    .A_2(A3), .B_2(B3), .X(n1_bit_alu_4_x), .A_invert(n1_bit_alu_3_out_31), .B_invert(n1_bit_alu_3_out_32),
    .And(n1_bit_alu_3_out_33), .Or(n1_bit_alu_3_out_34), .A(n1_bit_alu_3_out_35), .B(n1_bit_alu_3_out_36),
    .SRAO(n1_bit_alu_4_srao), .SRBO(n1_bit_alu_4_srbo), .SRA(n1_bit_alu_3_out_37), .SRB(n1_bit_alu_3_out_38),
    .SLAI(n1_bit_alu_3_slao), .SLBI(n1_bit_alu_3_slbo), .SLA(n1_bit_alu_3_out_39), .SLB(n1_bit_alu_3_out_40),
    .XOr(n1_bit_alu_3_out_41), .NEO(n1_bit_alu_4_neo), .GRO(n1_bit_alu_4_gro), .LSO(n1_bit_alu_4_lso),
    .Carry_in(n1_bit_alu_3_carry_out), .Add(n1_bit_alu_3_out_43), .X_invert(n1_bit_alu_3_out_44),
    .out_31(n1_bit_alu_4_out_31), .out_32(n1_bit_alu_4_out_32), .out_33(n1_bit_alu_4_out_33),
    .out_34(n1_bit_alu_4_out_34), .out_35(n1_bit_alu_4_out_35), .out_36(n1_bit_alu_4_out_36),
    .SRAI(n1_bit_alu_5_srao), .SRBI(n1_bit_alu_5_srbo), .out_37(n1_bit_alu_4_out_37),
    .out_38(n1_bit_alu_4_out_38), .SLAO(n1_bit_alu_4_slao), .SLBO(n1_bit_alu_4_slbo),
    .out_39(n1_bit_alu_4_out_39), .out_40(n1_bit_alu_4_out_40), .out_41(n1_bit_alu_4_out_41),
    .NEI(n1_bit_alu_5_neo), .GRI(n1_bit_alu_5_gro), .LSI(n1_bit_alu_5_lso),
    .Carry_out(n1_bit_alu_4_carry_out), .out_43(n1_bit_alu_4_out_43), .out_44(n1_bit_alu_4_out_44),
    .Not_Zero_In(n1_bit_alu_3_not_zero_out), .Not_Zero_Out(n1_bit_alu_4_not_zero_out));
  _1_bit_ALU u_1_bit_alu_5 (
    .A_2(A4), .B_2(B4), .X(n1_bit_alu_5_x), .A_invert(n1_bit_alu_4_out_31), .B_invert(n1_bit_alu_4_out_32),
    .And(n1_bit_alu_4_out_33), .Or(n1_bit_alu_4_out_34), .A(n1_bit_alu_4_out_35), .B(n1_bit_alu_4_out_36),
    .SRAO(n1_bit_alu_5_srao), .SRBO(n1_bit_alu_5_srbo), .SRA(n1_bit_alu_4_out_37), .SRB(n1_bit_alu_4_out_38),
    .SLAI(n1_bit_alu_4_slao), .SLBI(n1_bit_alu_4_slbo), .SLA(n1_bit_alu_4_out_39), .SLB(n1_bit_alu_4_out_40),
    .XOr(n1_bit_alu_4_out_41), .NEO(n1_bit_alu_5_neo), .GRO(n1_bit_alu_5_gro), .LSO(n1_bit_alu_5_lso),
    .Carry_in(n1_bit_alu_4_carry_out), .Add(n1_bit_alu_4_out_43), .X_invert(n1_bit_alu_4_out_44),
    .out_31(n1_bit_alu_5_out_31), .out_32(n1_bit_alu_5_out_32), .out_33(n1_bit_alu_5_out_33),
    .out_34(n1_bit_alu_5_out_34), .out_35(n1_bit_alu_5_out_35), .out_36(n1_bit_alu_5_out_36),
    .SRAI(n1_bit_alu_6_srao), .SRBI(n1_bit_alu_6_srbo), .out_37(n1_bit_alu_5_out_37),
    .out_38(n1_bit_alu_5_out_38), .SLAO(n1_bit_alu_5_slao), .SLBO(n1_bit_alu_5_slbo),
    .out_39(n1_bit_alu_5_out_39), .out_40(n1_bit_alu_5_out_40), .out_41(n1_bit_alu_5_out_41),
    .NEI(n1_bit_alu_6_neo), .GRI(n1_bit_alu_6_gro), .LSI(n1_bit_alu_6_lso),
    .Carry_out(n1_bit_alu_5_carry_out), .out_43(n1_bit_alu_5_out_43), .out_44(n1_bit_alu_5_out_44),
    .Not_Zero_In(n1_bit_alu_4_not_zero_out), .Not_Zero_Out(n1_bit_alu_5_not_zero_out));
  _1_bit_ALU u_1_bit_alu_6 (
    .A_2(A5), .B_2(B5), .X(n1_bit_alu_6_x), .A_invert(n1_bit_alu_5_out_31), .B_invert(n1_bit_alu_5_out_32),
    .And(n1_bit_alu_5_out_33), .Or(n1_bit_alu_5_out_34), .A(n1_bit_alu_5_out_35), .B(n1_bit_alu_5_out_36),
    .SRAO(n1_bit_alu_6_srao), .SRBO(n1_bit_alu_6_srbo), .SRA(n1_bit_alu_5_out_37), .SRB(n1_bit_alu_5_out_38),
    .SLAI(n1_bit_alu_5_slao), .SLBI(n1_bit_alu_5_slbo), .SLA(n1_bit_alu_5_out_39), .SLB(n1_bit_alu_5_out_40),
    .XOr(n1_bit_alu_5_out_41), .NEO(n1_bit_alu_6_neo), .GRO(n1_bit_alu_6_gro), .LSO(n1_bit_alu_6_lso),
    .Carry_in(n1_bit_alu_5_carry_out), .Add(n1_bit_alu_5_out_43), .X_invert(n1_bit_alu_5_out_44),
    .out_31(n1_bit_alu_6_out_31), .out_32(n1_bit_alu_6_out_32), .out_33(n1_bit_alu_6_out_33),
    .out_34(n1_bit_alu_6_out_34), .out_35(n1_bit_alu_6_out_35), .out_36(n1_bit_alu_6_out_36),
    .SRAI(n1_bit_alu_7_srao), .SRBI(n1_bit_alu_7_srbo), .out_37(n1_bit_alu_6_out_37),
    .out_38(n1_bit_alu_6_out_38), .SLAO(n1_bit_alu_6_slao), .SLBO(n1_bit_alu_6_slbo),
    .out_39(n1_bit_alu_6_out_39), .out_40(n1_bit_alu_6_out_40), .out_41(n1_bit_alu_6_out_41),
    .NEI(n1_bit_alu_7_neo), .GRI(n1_bit_alu_7_gro), .LSI(n1_bit_alu_7_lso),
    .Carry_out(n1_bit_alu_6_carry_out), .out_43(n1_bit_alu_6_out_43), .out_44(n1_bit_alu_6_out_44),
    .Not_Zero_In(n1_bit_alu_5_not_zero_out), .Not_Zero_Out(n1_bit_alu_6_not_zero_out));
  _1_bit_ALU u_1_bit_alu_7 (
    .A_2(A6), .B_2(B6), .X(n1_bit_alu_7_x), .A_invert(n1_bit_alu_6_out_31), .B_invert(n1_bit_alu_6_out_32),
    .And(n1_bit_alu_6_out_33), .Or(n1_bit_alu_6_out_34), .A(n1_bit_alu_6_out_35), .B(n1_bit_alu_6_out_36),
    .SRAO(n1_bit_alu_7_srao), .SRBO(n1_bit_alu_7_srbo), .SRA(n1_bit_alu_6_out_37), .SRB(n1_bit_alu_6_out_38),
    .SLAI(n1_bit_alu_6_slao), .SLBI(n1_bit_alu_6_slbo), .SLA(n1_bit_alu_6_out_39), .SLB(n1_bit_alu_6_out_40),
    .XOr(n1_bit_alu_6_out_41), .NEO(n1_bit_alu_7_neo), .GRO(n1_bit_alu_7_gro), .LSO(n1_bit_alu_7_lso),
    .Carry_in(n1_bit_alu_6_carry_out), .Add(n1_bit_alu_6_out_43), .X_invert(n1_bit_alu_6_out_44),
    .out_31(n1_bit_alu_7_out_31), .out_32(n1_bit_alu_7_out_32), .out_33(n1_bit_alu_7_out_33),
    .out_34(n1_bit_alu_7_out_34), .out_35(n1_bit_alu_7_out_35), .out_36(n1_bit_alu_7_out_36),
    .SRAI(n1_bit_alu_8_srao), .SRBI(n1_bit_alu_8_srbo), .out_37(n1_bit_alu_7_out_37),
    .out_38(n1_bit_alu_7_out_38), .SLAO(n1_bit_alu_7_slao), .SLBO(n1_bit_alu_7_slbo),
    .out_39(n1_bit_alu_7_out_39), .out_40(n1_bit_alu_7_out_40), .out_41(n1_bit_alu_7_out_41),
    .NEI(n1_bit_alu_8_neo), .GRI(n1_bit_alu_8_gro), .LSI(n1_bit_alu_8_lso),
    .Carry_out(n1_bit_alu_7_carry_out), .out_43(n1_bit_alu_7_out_43), .out_44(n1_bit_alu_7_out_44),
    .Not_Zero_In(n1_bit_alu_6_not_zero_out), .Not_Zero_Out(n1_bit_alu_7_not_zero_out));
  _1_bit_ALU u_1_bit_alu_8 (
    .A_2(A7), .B_2(B7), .X(n1_bit_alu_8_x), .A_invert(n1_bit_alu_7_out_31), .B_invert(n1_bit_alu_7_out_32),
    .And(n1_bit_alu_7_out_33), .Or(n1_bit_alu_7_out_34), .A(n1_bit_alu_7_out_35), .B(n1_bit_alu_7_out_36),
    .SRAO(n1_bit_alu_8_srao), .SRBO(n1_bit_alu_8_srbo), .SRA(n1_bit_alu_7_out_37), .SRB(n1_bit_alu_7_out_38),
    .SLAI(n1_bit_alu_7_slao), .SLBI(n1_bit_alu_7_slbo), .SLA(n1_bit_alu_7_out_39), .SLB(n1_bit_alu_7_out_40),
    .XOr(n1_bit_alu_7_out_41), .NEO(n1_bit_alu_8_neo), .GRO(n1_bit_alu_8_gro), .LSO(n1_bit_alu_8_lso),
    .Carry_in(n1_bit_alu_7_carry_out), .Add(n1_bit_alu_7_out_43), .X_invert(n1_bit_alu_7_out_44),
    .SRAI(and_2_out), .out_37(and_1_out), .SLAO(n1_bit_alu_8_slao), .out_39(n1_bit_alu_8_out_39), .NEI(1'b0),
    .GRI(1'b0), .LSI(1'b0), .Carry_out(n1_bit_alu_8_carry_out), .Not_Zero_In(n1_bit_alu_7_not_zero_out),
    .Not_Zero_Out(n1_bit_alu_8_not_zero_out));  // open: out_31, out_32, out_33, out_34, out_35, out_36, SRBI, out_38, SLBO, out_40, out_41, out_43, out_44
  not not_1 (Zero, n1_bit_alu_8_not_zero_out);
  or or_1 (Overflow, n1_bit_alu_8_carry_out, n8_bit_multiplier_1_overflow);
  _2_Way_Multiplexor u_2_way_multiplexor_1 (
    ._0(n1_bit_alu_1_x), ._1(n1_bit_alu_2_x), ._2(n1_bit_alu_3_x), ._3(n1_bit_alu_4_x), ._4(n1_bit_alu_5_x),
    ._5(n1_bit_alu_6_x), ._6(n1_bit_alu_7_x), ._7(n1_bit_alu_8_x), ._0_2(n8_bit_multiplier_1_x0),
    ._1_2(n8_bit_multiplier_1_x1), ._2_2(n8_bit_multiplier_1_x2), ._3_2(n8_bit_multiplier_1_x3),
    ._4_2(n8_bit_multiplier_1_x4), ._5_2(n8_bit_multiplier_1_x5), ._6_2(n8_bit_multiplier_1_x6),
    ._7_2(n8_bit_multiplier_1_x7), .S(Multiply), ._0_3(X0), ._1_3(X1), ._2_3(X2), ._3_3(X3), ._4_3(X4),
    ._5_3(X5), ._6_3(X6), ._7_3(X7));
endmodule

module D_Latch (
  input  Clock,
  input  Data,
  output Out
);

  wire and_1_out, and_2_out, not_1_out, not_2_out, not_3_out, or_1_out, or_2_out, undriven, undriven_2;

  D_Flip_Flop #(.trigger("high")) d_ff_1 (.clk(Clock), .D(Data), .Q(Out));  // open: Qn, preset, en, reset
  not not_1 (not_1_out, undriven_2);
  and and_1 (and_1_out, undriven, undriven_2);
  or or_1 (or_1_out, and_1_out, not_3_out);
  not not_2 (not_2_out, or_1_out);
  not not_3 (not_3_out, or_2_out);
  or or_2 (or_2_out, not_2_out, and_2_out);
  and and_2 (and_2_out, not_1_out, undriven);
endmodule

module _4_bit_Decoder (
  input  _0,
  input  _1,
  input  _2,
  input  _3,
  output _0_2,
  output _1_2,
  output _2_2,
  output _3_2,
  output _4,
  output _5,
  output _6,
  output _7,
  output _8,
  output _9,
  output _10,
  output _11,
  output _12,
  output _13,
  output _14,
  output _15
);

  wire and_1_out, and_3_out, and_4_out, and_6_out, and_7_out, and_9_out, and_10_out, and_12_out, and_13_out,
       and_15_out, and_16_out, and_18_out, and_19_out, and_21_out, and_22_out, and_24_out, and_25_out,
       and_27_out, and_28_out, and_30_out, and_31_out, and_33_out, and_34_out, and_36_out, and_37_out,
       and_39_out, and_40_out, and_42_out, and_43_out, and_45_out, and_46_out, and_48_out, not_1_out,
       not_2_out, not_3_out, not_4_out, not_5_out, not_6_out, not_7_out, not_8_out, not_9_out, not_10_out,
       not_11_out, not_12_out, not_13_out, not_14_out, not_15_out, not_16_out, not_17_out, not_18_out,
       not_19_out, not_20_out, not_21_out, not_22_out, not_23_out, not_24_out, not_25_out, not_26_out,
       not_27_out, not_28_out, not_29_out, not_30_out, not_31_out, not_32_out;

  and and_1 (and_1_out, not_2_out, not_1_out);
  not not_1 (not_1_out, _2);
  not not_2 (not_2_out, _3);
  and and_2 (_0_2, and_1_out, and_3_out);
  and and_3 (and_3_out, not_6_out, not_4_out);
  and and_4 (and_4_out, not_5_out, not_3_out);
  not not_3 (not_3_out, _2);
  not not_4 (not_4_out, _0);
  not not_5 (not_5_out, _3);
  not not_6 (not_6_out, _1);
  and and_5 (_1_2, and_4_out, and_6_out);
  and and_6 (and_6_out, not_7_out, _0);
  and and_7 (and_7_out, not_8_out, not_9_out);
  not not_7 (not_7_out, _1);
  not not_8 (not_8_out, _3);
  not not_9 (not_9_out, _2);
  and and_8 (_2_2, and_7_out, and_9_out);
  and and_9 (and_9_out, _1, not_10_out);
  and and_10 (and_10_out, not_11_out, not_12_out);
  not not_10 (not_10_out, _0);
  not not_11 (not_11_out, _3);
  not not_12 (not_12_out, _2);
  and and_11 (_3_2, and_10_out, and_13_out);
  and and_12 (and_12_out, not_13_out, _2);
  and and_13 (and_13_out, _1, _0);
  not not_13 (not_13_out, _3);
  and and_14 (_4, and_12_out, and_15_out);
  and and_15 (and_15_out, not_16_out, not_15_out);
  and and_16 (and_16_out, not_14_out, _2);
  not not_14 (not_14_out, _3);
  not not_15 (not_15_out, _0);
  not not_16 (not_16_out, _1);
  and and_17 (_5, and_16_out, and_19_out);
  and and_18 (and_18_out, not_18_out, _2);
  and and_19 (and_19_out, not_17_out, _0);
  not not_17 (not_17_out, _1);
  not not_18 (not_18_out, _3);
  and and_20 (_6, and_18_out, and_21_out);
  and and_21 (and_21_out, _1, not_19_out);
  and and_22 (and_22_out, not_20_out, _2);
  not not_19 (not_19_out, _0);
  not not_20 (not_20_out, _3);
  and and_23 (_7, and_22_out, and_24_out);
  and and_24 (and_24_out, _1, _0);
  and and_25 (and_25_out, _3, not_21_out);
  not not_21 (not_21_out, _2);
  and and_26 (_8, and_25_out, and_28_out);
  and and_27 (and_27_out, _3, not_24_out);
  and and_28 (and_28_out, not_23_out, not_22_out);
  not not_22 (not_22_out, _0);
  not not_23 (not_23_out, _1);
  not not_24 (not_24_out, _2);
  and and_29 (_9, and_27_out, and_31_out);
  and and_30 (and_30_out, _3, not_26_out);
  and and_31 (and_31_out, not_25_out, _0);
  not not_25 (not_25_out, _1);
  not not_26 (not_26_out, _2);
  and and_32 (_10, and_30_out, and_33_out);
  and and_33 (and_33_out, _1, not_28_out);
  and and_34 (and_34_out, _3, not_27_out);
  not not_27 (not_27_out, _2);
  not not_28 (not_28_out, _0);
  and and_35 (_11, and_34_out, and_37_out);
  and and_36 (and_36_out, _3, _2);
  and and_37 (and_37_out, _1, _0);
  and and_38 (_12, and_36_out, and_40_out);
  and and_39 (and_39_out, _3, _2);
  and and_40 (and_40_out, not_29_out, not_30_out);
  not not_29 (not_29_out, _1);
  not not_30 (not_30_out, _0);
  and and_41 (_13, and_39_out, and_42_out);
  and and_42 (and_42_out, not_31_out, _0);
  and and_43 (and_43_out, _3, _2);
  not not_31 (not_31_out, _1);
  and and_44 (_14, and_43_out, and_45_out);
  and and_45 (and_45_out, _1, not_32_out);
  and and_46 (and_46_out, _3, _2);
  not not_32 (not_32_out, _0);
  and and_47 (_15, and_46_out, and_48_out);
  and and_48 (and_48_out, _1, _0);
endmodule

module _8_bit_Register (
  input  [7:0] in_1,
  input  _0,
  input  _1,
  input  _2,
  input  _3,
  input  _4,
  input  _5,
  input  _6,
  input  _7,
  input  Reset,
  input  Clock,
  input  Enable,
  output [7:0] _0_2,
  output _0_3,
  output _1_2,
  output _2_2,
  output _3_2,
  output _4_2,
  output _5_2,
  output _6_2,
  output _7_2
);

  wire and_1_out, and_2_out, and_3_out, and_4_out, and_5_out, and_6_out, and_7_out, and_8_out, and_9_out,
       and_10_out, and_11_out, and_12_out, and_13_out, and_14_out, and_15_out, and_16_out, and_17_out,
       not_1_out, or_1_out, or_2_out, or_3_out, or_4_out, or_5_out, or_6_out, or_7_out, or_8_out, or_9_out;

  not not_1 (not_1_out, Reset);
  and and_1 (and_1_out, _0, not_1_out);
  and and_2 (and_2_out, _1, not_1_out);
  and and_3 (and_3_out, _2, not_1_out);
  and and_4 (and_4_out, _3, not_1_out);
  and and_5 (and_5_out, _4, not_1_out);
  and and_6 (and_6_out, _5, not_1_out);
  and and_7 (and_7_out, _6, not_1_out);
  and and_8 (and_8_out, _7, not_1_out);
  and and_9 (and_9_out, in_1[0], Reset);
  or or_1 (or_1_out, and_9_out, and_1_out);
  and and_10 (and_10_out, in_1[1], Reset);
  or or_2 (or_2_out, and_10_out, and_2_out);
  and and_11 (and_11_out, in_1[2], Reset);
  or or_3 (or_3_out, and_11_out, and_3_out);
  and and_12 (and_12_out, in_1[3], Reset);
  or or_4 (or_4_out, and_12_out, and_4_out);
  and and_13 (and_13_out, in_1[4], Reset);
  or or_5 (or_5_out, and_13_out, and_5_out);
  and and_14 (and_14_out, in_1[5], Reset);
  or or_6 (or_6_out, and_14_out, and_6_out);
  and and_15 (and_15_out, in_1[6], Reset);
  or or_7 (or_7_out, and_15_out, and_7_out);
  and and_16 (and_16_out, in_1[7], Reset);
  or or_8 (or_8_out, and_16_out, and_8_out);
  or or_9 (or_9_out, Reset, and_17_out);
  and and_17 (and_17_out, Clock, Enable);
  D_Latch d_latch_1 (.Clock(or_9_out), .Data(or_1_out), .Out(_0_2[0]));
  D_Latch d_latch_2 (.Clock(or_9_out), .Data(or_2_out), .Out(_0_2[1]));
  D_Latch d_latch_3 (.Clock(or_9_out), .Data(or_3_out), .Out(_0_2[2]));
  D_Latch d_latch_4 (.Clock(or_9_out), .Data(or_4_out), .Out(_0_2[3]));
  D_Latch d_latch_5 (.Clock(or_9_out), .Data(or_5_out), .Out(_0_2[4]));
  D_Latch d_latch_6 (.Clock(or_9_out), .Data(or_6_out), .Out(_0_2[5]));
  D_Latch d_latch_7 (.Clock(or_9_out), .Data(or_7_out), .Out(_0_2[6]));
  D_Latch d_latch_8 (.Clock(or_9_out), .Data(or_8_out), .Out(_0_2[7]));

  assign _0_3 = _0_2[0];
  assign _1_2 = _0_2[1];
  assign _2_2 = _0_2[2];
  assign _3_2 = _0_2[3];
  assign _4_2 = _0_2[4];
  assign _5_2 = _0_2[5];
  assign _6_2 = _0_2[6];
  assign _7_2 = _0_2[7];
endmodule

module Register (
  input  Data,
  input  Clock,
  output Clock_Out,
  output X
);

  wire d_latch_1_out;

  D_Latch d_latch_1 (.Clock(Clock), .Data(Data), .Out(d_latch_1_out));
  and and_1 (X, Clock, d_latch_1_out);

  assign Clock_Out = Clock;
endmodule

module _8_bit_Adder (
  input  Increment,
  input  A0,
  input  B0,
  input  A1,
  input  B1,
  input  A2,
  input  B2,
  input  A3,
  input  B3,
  input  A4,
  input  B4,
  input  A5,
  input  B5,
  input  A6,
  input  B6,
  input  A7,
  input  B7,
  output X0,
  output X1,
  output X2,
  output X3,
  output X4,
  output X5,
  output X6,
  output X7,
  output Carry_Out
);

  wire full_adder_1_carry_out, full_adder_2_carry_out, full_adder_3_carry_out, full_adder_4_carry_out,
       full_adder_5_carry_out, full_adder_6_carry_out, full_adder_7_carry_out;

  Full_Adder full_adder_1 (.A(A0), .B(B0), .X(X0), .Carry_In(Increment), .Carry_Out(full_adder_1_carry_out));
  Full_Adder full_adder_2 (
    .A(A1), .B(B1), .X(X1), .Carry_In(full_adder_1_carry_out), .Carry_Out(full_adder_2_carry_out));
  Full_Adder full_adder_3 (
    .A(A2), .B(B2), .X(X2), .Carry_In(full_adder_2_carry_out), .Carry_Out(full_adder_3_carry_out));
  Full_Adder full_adder_4 (
    .A(A3), .B(B3), .X(X3), .Carry_In(full_adder_3_carry_out), .Carry_Out(full_adder_4_carry_out));
  Full_Adder full_adder_5 (
    .A(A4), .B(B4), .X(X4), .Carry_In(full_adder_4_carry_out), .Carry_Out(full_adder_5_carry_out));
  Full_Adder full_adder_6 (
    .A(A5), .B(B5), .X(X5), .Carry_In(full_adder_5_carry_out), .Carry_Out(full_adder_6_carry_out));
  Full_Adder full_adder_7 (
    .A(A6), .B(B6), .X(X6), .Carry_In(full_adder_6_carry_out), .Carry_Out(full_adder_7_carry_out));
  Full_Adder full_adder_8 (.A(A7), .B(B7), .X(X7), .Carry_In(full_adder_7_carry_out), .Carry_Out(Carry_Out));
endmodule

module Full_Adder (
  input  Carry_In,
  input  A,
  input  B,
  output X,
  output Carry_Out
);

  wire and_1_out, and_2_out, and_3_out, not_1_out, not_2_out, or_1_out, or_3_out;

  or or_1 (or_1_out, A, B);
  and and_1 (and_1_out, B, A);
  and and_2 (and_2_out, or_1_out, not_1_out);
  not not_1 (not_1_out, and_1_out);
  or or_2 (Carry_Out, and_1_out, and_3_out);
  or or_3 (or_3_out, Carry_In, and_2_out);
  not not_2 (not_2_out, and_3_out);
  and and_3 (and_3_out, and_2_out, Carry_In);
  and and_4 (X, or_3_out, not_2_out);
endmodule

module _8_bit_Counter__Adding (
  input  Reset,
  input  Count,
  input  Set,
  input  _7,
  input  _5,
  input  _3,
  input  _1,
  input  _6,
  input  _4,
  input  _2,
  input  _0,
  output _0_2,
  output _1_2,
  output _2_2,
  output _3_2,
  output _4_2,
  output _5_2,
  output _6_2,
  output _7_2,
  output Carry_Out
);

  wire n2_way_multiplexor_1__0_3, n2_way_multiplexor_1__1_3, n2_way_multiplexor_1__2_3,
       n2_way_multiplexor_1__3_3, n2_way_multiplexor_1__4_3, n2_way_multiplexor_1__5_3,
       n2_way_multiplexor_1__6_3, n2_way_multiplexor_1__7_3, n8_bit_adder_1_x0, n8_bit_adder_1_x1,
       n8_bit_adder_1_x2, n8_bit_adder_1_x3, n8_bit_adder_1_x4, n8_bit_adder_1_x5, n8_bit_adder_1_x6,
       n8_bit_adder_1_x7, n8_bit_register_1_p10, n8_bit_register_1_p11, n8_bit_register_1_p12,
       n8_bit_register_1_p13, n8_bit_register_1_p14, n8_bit_register_1_p15, n8_bit_register_1_p16,
       n8_bit_register_1_p17, n8_bit_register_1_p18, n8_bit_register_2_p10;

  // _8_bit_Register 8_bit_register_1: pin names not known; wires that end beside it: _0_2, _1_2, _2_2, _3_2, _4_2, _5_2, _6_2, _7_2, Reset, n8_bit_register_1_p10, n8_bit_register_1_p11, n8_bit_register_1_p12, n8_bit_register_1_p13, n8_bit_register_1_p14, n8_bit_register_1_p15, n8_bit_register_1_p16, n8_bit_register_1_p17, n8_bit_register_1_p18
  _8_bit_Adder u_8_bit_adder_1 (
    .A0(n8_bit_register_1_p11), .B0(1'b0), .A1(n8_bit_register_1_p12), .B1(1'b0), .A2(n8_bit_register_1_p13),
    .B2(1'b0), .A3(n8_bit_register_1_p14), .B3(1'b0), .A4(n8_bit_register_1_p15), .B4(1'b0),
    .A5(n8_bit_register_1_p16), .B5(1'b0), .A6(n8_bit_register_1_p17), .B6(1'b0), .A7(n8_bit_register_1_p18),
    .B7(1'b0), .X0(n8_bit_adder_1_x0), .X1(n8_bit_adder_1_x1), .X2(n8_bit_adder_1_x2),
    .X3(n8_bit_adder_1_x3), .X4(n8_bit_adder_1_x4), .X5(n8_bit_adder_1_x5), .X6(n8_bit_adder_1_x6),
    .X7(n8_bit_adder_1_x7), .Increment(1'b1), .Carry_Out(Carry_Out));
  _2_Way_Multiplexor u_2_way_multiplexor_1 (
    ._0(n8_bit_adder_1_x0), ._1(n8_bit_adder_1_x1), ._2(n8_bit_adder_1_x2), ._3(n8_bit_adder_1_x3),
    ._4(n8_bit_adder_1_x4), ._5(n8_bit_adder_1_x5), ._6(n8_bit_adder_1_x6), ._7(n8_bit_adder_1_x7),
    ._0_2(_0), ._1_2(_1), ._2_2(_2), ._3_2(_3), ._4_2(_4), ._5_2(_5), ._6_2(_6), ._7_2(_7), .S(Set),
    ._0_3(n2_way_multiplexor_1__0_3), ._1_3(n2_way_multiplexor_1__1_3), ._2_3(n2_way_multiplexor_1__2_3),
    ._3_3(n2_way_multiplexor_1__3_3), ._4_3(n2_way_multiplexor_1__4_3), ._5_3(n2_way_multiplexor_1__5_3),
    ._6_3(n2_way_multiplexor_1__6_3), ._7_3(n2_way_multiplexor_1__7_3));
  // _8_bit_Register 8_bit_register_2: pin names not known; wires that end beside it: n2_way_multiplexor_1__0_3, n2_way_multiplexor_1__1_3, n2_way_multiplexor_1__2_3, n2_way_multiplexor_1__3_3, n2_way_multiplexor_1__4_3, n2_way_multiplexor_1__5_3, n2_way_multiplexor_1__6_3, n2_way_multiplexor_1__7_3, Reset, n8_bit_register_2_p10, _0_2, _1_2, _2_2, _3_2, _4_2, _5_2, _6_2, _7_2
  not not_1 (n8_bit_register_2_p10, n8_bit_register_1_p10);
  or or_1 (n8_bit_register_1_p10, Count, Set);
endmodule

module _2_Way_Multiplexor (
  input  _0,
  input  _1,
  input  _2,
  input  _3,
  input  _4,
  input  _5,
  input  _6,
  input  _7,
  input  S,
  input  _7_2,
  input  _6_2,
  input  _5_2,
  input  _4_2,
  input  _3_2,
  input  _2_2,
  input  _1_2,
  input  _0_2,
  output _0_3,
  output _1_3,
  output _2_3,
  output _3_3,
  output _4_3,
  output _5_3,
  output _6_3,
  output _7_3
);

  wire and_1_out, and_2_out, and_3_out, and_4_out, and_5_out, and_6_out, and_7_out, and_8_out, and_9_out,
       and_10_out, and_11_out, and_12_out, and_13_out, and_14_out, and_15_out, and_16_out, not_1_out;

  and and_1 (and_1_out, _0, not_1_out);
  and and_2 (and_2_out, _1, not_1_out);
  and and_3 (and_3_out, _2, not_1_out);
  and and_4 (and_4_out, _3, not_1_out);
  and and_5 (and_5_out, _4, not_1_out);
  and and_6 (and_6_out, _5, not_1_out);
  and and_7 (and_7_out, _6, not_1_out);
  and and_8 (and_8_out, _7, not_1_out);
  not not_1 (not_1_out, S);
  or or_1 (_7_3, and_8_out, and_10_out);
  and and_9 (and_9_out, _6_2, S);
  and and_10 (and_10_out, _7_2, S);
  or or_2 (_5_3, and_6_out, and_11_out);
  or or_3 (_6_3, and_7_out, and_9_out);
  and and_11 (and_11_out, _5_2, S);
  and and_12 (and_12_out, _4_2, S);
  or or_4 (_3_3, and_4_out, and_13_out);
  or or_5 (_4_3, and_5_out, and_12_out);
  and and_13 (and_13_out, _3_2, S);
  and and_14 (and_14_out, _2_2, S);
  or or_6 (_1_3, and_2_out, and_16_out);
  or or_7 (_2_3, and_3_out, and_14_out);
  and and_15 (and_15_out, _0_2, S);
  and and_16 (and_16_out, _1_2, S);
  or or_8 (_0_3, and_1_out, and_15_out);
endmodule

module _8_bit_Flip (
  input  _0,
  input  _0_2,
  input  _1,
  input  _1_2,
  input  _2,
  input  _2_2,
  input  _3,
  input  _3_2,
  input  _4,
  input  _4_2,
  input  _5,
  input  _5_2,
  input  _6,
  input  _6_2,
  input  _6_3,
  input  _6_4,
  output _0_3,
  output _0_4,
  output _1_3,
  output _1_4,
  output _2_3,
  output _2_4,
  output _3_3,
  output _3_4,
  output _4_3,
  output _4_4,
  output _5_3,
  output _5_4,
  output _6_5,
  output _6_6,
  output _6_7,
  output _6_8
);


  assign _0_3 = _0;
  assign _0_4 = _0_2;
  assign _1_3 = _1;
  assign _1_4 = _1_2;
  assign _2_3 = _2;
  assign _2_4 = _2_2;
  assign _3_3 = _3;
  assign _3_4 = _3_2;
  assign _4_3 = _4;
  assign _4_4 = _4_2;
  assign _5_3 = _5;
  assign _5_4 = _5_2;
  assign _6_5 = _6;
  assign _6_6 = _6_2;
  assign _6_7 = _6_3;
  assign _6_8 = _6_4;
endmodule

module _3_Way_Demultiplexer (
  input  _0,
  input  _1,
  input  _2,
  input  _3,
  input  _4,
  input  _5,
  input  _6,
  input  _7,
  input  S0,
  input  S1,
  output _7_2,
  output _6_2,
  output _5_2,
  output _4_2,
  output _3_2,
  output _2_2,
  output _1_2,
  output _0_2,
  output _0_3,
  output _1_3,
  output _2_3,
  output _3_3,
  output _4_3,
  output _5_3,
  output _6_3,
  output _7_3,
  output _7_4,
  output _6_4,
  output _5_4,
  output _4_4,
  output _3_4,
  output _2_4,
  output _1_4,
  output _0_4
);

  wire and_2_out, and_3_out, and_7_out, and_8_out, and_9_out, and_10_out, and_15_out, and_16_out, and_17_out,
       and_18_out, and_23_out, and_24_out, and_25_out, and_26_out, and_30_out, and_31_out, and_34_out,
       and_36_out, and_38_out, and_40_out, and_42_out, and_44_out, and_46_out, and_48_out, not_1_out,
       not_2_out, not_3_out;

  and and_1 (_7_2, not_3_out, and_2_out);
  and and_2 (and_2_out, _7, not_1_out);
  and and_3 (and_3_out, _7, S0);
  and and_4 (_7_4, S1, and_3_out);
  and and_5 (_6_2, not_3_out, and_8_out);
  and and_6 (_5_2, not_3_out, and_7_out);
  and and_7 (and_7_out, _5, not_1_out);
  and and_8 (and_8_out, _6, not_1_out);
  and and_9 (and_9_out, _5, S0);
  and and_10 (and_10_out, _6, S0);
  and and_11 (_6_4, S1, and_10_out);
  and and_12 (_5_4, S1, and_9_out);
  and and_13 (_3_2, not_3_out, and_16_out);
  and and_14 (_4_2, not_3_out, and_15_out);
  and and_15 (and_15_out, _4, not_1_out);
  and and_16 (and_16_out, _3, not_1_out);
  and and_17 (and_17_out, _3, S0);
  and and_18 (and_18_out, _4, S0);
  and and_19 (_3_4, S1, and_17_out);
  and and_20 (_4_4, S1, and_18_out);
  and and_21 (_2_2, not_3_out, and_24_out);
  and and_22 (_1_2, not_3_out, and_23_out);
  and and_23 (and_23_out, _1, not_1_out);
  and and_24 (and_24_out, _2, not_1_out);
  and and_25 (and_25_out, _1, S0);
  and and_26 (and_26_out, _2, S0);
  and and_27 (_1_4, S1, and_25_out);
  and and_28 (_2_4, S1, and_26_out);
  and and_29 (_0_2, not_3_out, and_30_out);
  and and_30 (and_30_out, _0, not_1_out);
  not not_1 (not_1_out, not_2_out);
  not not_2 (not_2_out, S0);
  and and_31 (and_31_out, _0, S0);
  and and_32 (_0_4, S1, and_31_out);
  not not_3 (not_3_out, S1);
  and and_33 (_0_3, S1, and_34_out);
  and and_34 (and_34_out, _0, not_2_out);
  and and_35 (_1_3, S1, and_36_out);
  and and_36 (and_36_out, _1, not_2_out);
  and and_37 (_2_3, S1, and_38_out);
  and and_38 (and_38_out, _2, not_2_out);
  and and_39 (_3_3, S1, and_40_out);
  and and_40 (and_40_out, _3, not_2_out);
  and and_41 (_4_3, S1, and_42_out);
  and and_42 (and_42_out, _4, not_2_out);
  and and_43 (_5_3, S1, and_44_out);
  and and_44 (and_44_out, _5, not_2_out);
  and and_45 (_6_3, S1, and_46_out);
  and and_46 (and_46_out, _6, not_2_out);
  and and_47 (_7_3, S1, and_48_out);
  and and_48 (and_48_out, _7, not_2_out);
endmodule

module X (
  input  _7,
  input  _6,
  input  _5,
  input  _4,
  input  _3,
  input  _2,
  input  _1,
  input  _0,
  output _0_2,
  output _1_2,
  output _2_2,
  output _3_2,
  output _4_2,
  output _5_2,
  output _6_2,
  output _7_2
);


  assign _0_2 = _0;
  assign _1_2 = _1;
  assign _2_2 = _2;
  assign _3_2 = _3;
  assign _4_2 = _4;
  assign _5_2 = _5;
  assign _6_2 = _6;
  assign _7_2 = _7;
endmodule

module Control_Unit (
  input  Not_Equal,
  input  _7,
  input  _6,
  input  _5,
  input  _4,
  input  _3,
  input  _2,
  input  _1,
  input  _0,
  input  B_Greater_A,
  input  A_Greater_B,
  input  Carry_Out,
  input  Nero,
  input  Input_Available,
  input  Negative,
  input  Reset,
  input  One_by_One,
  input  Clock,
  input  Next_Instruction,
  output M_Clock,
  output Display_Clock,
  output MP_MAR_S2,
  output MP_MAR_S1,
  output MP_MAR_S0,
  output IR_Reset,
  output IR_Clock,
  output Reset_IO,
  output Read_Input,
  output MP_ALU_A_S0,
  output MP_ALU_A_S1,
  output MP_ALU_B_S0,
  output MP_ALU_B_S1,
  output PC_Set,
  output PC_Count,
  output Set_MAR_Add_MBR,
  output Clock_B_Greater_A,
  output Clock_CCR,
  output Set_Carry_Selector,
  output Set_Carry_Data,
  output MP_PC_S0,
  output MAR_Clock,
  output MBR_Clock,
  output MP_PC_S1,
  output Acc_X_Clock,
  output Acc_A_Clock,
  output Acc_B_Clock,
  output Acc_Y_Clock,
  output A_Clock,
  output Stack_Pop,
  output Stack_Push,
  output Stack_Reset,
  output MAR_Reset,
  output MBR_Reset,
  output AX_Reset,
  output AA_Reset,
  output AB_Reset,
  output AY_Reset,
  output A_Reset,
  output A_Invert,
  output B_Invert,
  output AND,
  output OR,
  output A,
  output B,
  output Shift_A_Right,
  output Shift_B_Right,
  output Shift_Loop,
  output Shift_A_Left,
  output Shift_B_Left,
  output XOR,
  output Increment,
  output ADD,
  output X_Invert,
  output Multiply
);

  wire and_1_out, and_2_out, and_3_out, and_4_out, and_5_out, and_6_out, and_7_out, and_8_out, and_9_out,
       and_11_out, and_12_out, and_13_out, and_14_out, and_15_out, and_16_out, and_17_out, button_1_out,
       button_2_out, Condition_x, d_ff_5_q, d_ff_6_q, d_ff_7_q, n1_bit_counter_2_increment_out,
       n1_bit_counter_2_set_out, n1_bit_counter_3_increment_out, n1_bit_counter_3_set_out,
       n1_bit_counter_4_increment_out, n1_bit_counter_4_set_out, n1_bit_counter_5_increment_out,
       n1_bit_counter_5_set_out, n1_bit_counter_6_increment_out, n1_bit_counter_6_set_out,
       n1_bit_counter_7_increment_out, n1_bit_counter_7_set_out, n1_bit_equator_1_x, n1_bit_equator_2_x,
       n1_bit_equator_3_x, n1_bit_equator_4_x, n1_bit_equator_5_x, n2_bit_equator_1_equal,
       n3_bit_demultiplexer_1__0_2, n3_bit_demultiplexer_1__0_3, n3_bit_demultiplexer_1__1_2,
       n3_bit_demultiplexer_1__1_3, n3_bit_demultiplexer_1__2_2, n3_bit_demultiplexer_1__2_3,
       n3_bit_equator_1_equal, n8_bit_register_1__0_3, n8_bit_register_1__1_2, n8_bit_register_1__2_2,
       n8_bit_register_1__3_2, n8_bit_register_1__4_2, n8_bit_register_1__5_2, n8_bit_register_1__6_2,
       n8_way_demultiplex_1__1, n8_way_demultiplex_1__2, n8_way_demultiplex_1__3, n8_way_demultiplex_1__4,
       n8_way_demultiplex_1__5, n8_way_demultiplex_1__7, not_1_out, not_2_out, not_4_out, or_2_out, or_3_out,
       or_4_out, or_5_out, or_6_out, or_7_out, or_8_out, or_9_out, or_10_out, or_11_out, or_12_out,
       or_13_out, or_14_out, or_15_out, or_16_out, or_17_out, or_18_out, or_19_out, or_20_out, or_22_out,
       Target_x;
  wire [6:0] n1_bit_counter_7_out;
  wire [7:0] n8_bit_register_1__0_2;
  wire [31:0] rom_1_data;
  wire [31:1] and_10_out;
  wire [31:16] rom_2_data;
  wire [31:31] not_3_out;

  or or_1 (A_Reset, Reset, and_10_out[15]);
  D_Latch d_latch_1 (.Clock(or_3_out), .Data(rom_2_data[27]), .Out(MP_ALU_A_S0));
  D_Latch d_latch_2 (.Clock(or_3_out), .Data(rom_2_data[28]), .Out(MP_ALU_A_S1));
  D_Latch d_latch_3 (.Clock(or_3_out), .Data(rom_2_data[25]), .Out(MP_ALU_B_S0));
  D_Latch d_latch_4 (.Clock(or_3_out), .Data(rom_2_data[26]), .Out(MP_ALU_B_S1));
  D_Flip_Flop d_ff_1 (.Q(Set_MAR_Add_MBR), .preset(and_10_out[18]), .reset(or_2_out));  // open: clk, D, Qn, en
  or or_2 (or_2_out, Reset, MBR_Clock);
  or or_3 (or_3_out, Reset, and_10_out[5]);
  // Probe on n8_bit_register_1__0_2
  _8_bit_Register u_8_bit_register_1 (
    ._6(and_10_out[25]), ._5(and_10_out[26]), ._4(and_10_out[27]), ._3(and_10_out[28]), ._2(and_10_out[29]),
    ._1(and_10_out[30]), ._0(and_10_out[31]), ._0_3(n8_bit_register_1__0_3), ._1_2(n8_bit_register_1__1_2),
    ._2_2(n8_bit_register_1__2_2), ._3_2(n8_bit_register_1__3_2), ._4_2(n8_bit_register_1__4_2),
    ._5_2(n8_bit_register_1__5_2), ._6_2(n8_bit_register_1__6_2), ._0_2(n8_bit_register_1__0_2),
    .in_1({8{1'b0}}), .Clock(or_6_out), .Enable(not_1_out));  // open: _7_2, _7, Reset
  D_Flip_Flop d_ff_2 (.Q(MP_MAR_S2), .preset(n3_bit_demultiplexer_1__2_2), .reset(or_4_out));  // open: clk, D, Qn, en
  _1_bit_Counter u_1_bit_counter_1 (
    .Increment(n1_bit_counter_3_increment_out), .Set(n1_bit_counter_3_set_out),
    .Out(n1_bit_counter_7_out[6]), .Data(and_1_out));  // open: Increment_Out, Set_Out
  and and_1 (and_1_out, n8_bit_register_1__0_3, not_2_out);
  and and_2 (and_2_out, n8_bit_register_1__1_2, not_2_out);
  D_Flip_Flop d_ff_3 (.Q(MP_MAR_S1), .preset(n3_bit_demultiplexer_1__1_2), .reset(or_4_out));  // open: clk, D, Qn, en
  _8_way_Demultiplex Terget (
    .Data(and_10_out[10]), ._1(Acc_A_Clock), ._2(Acc_B_Clock), ._3(Acc_X_Clock), ._4(Acc_Y_Clock),
    ._5(M_Clock), ._7(Display_Clock), .S2(rom_2_data[24]), .S1(rom_2_data[23]), .S0(rom_2_data[22]));  // open: _0, _6
  _1_bit_Counter u_1_bit_counter_2 (
    .Increment_Out(n1_bit_counter_2_increment_out), .Set_Out(n1_bit_counter_2_set_out),
    .Increment(n1_bit_counter_5_increment_out), .Set(n1_bit_counter_5_set_out),
    .Out(n1_bit_counter_7_out[3]), .Data(and_3_out));
  _1_bit_Counter u_1_bit_counter_3 (
    .Increment_Out(n1_bit_counter_3_increment_out), .Set_Out(n1_bit_counter_3_set_out),
    .Increment(n1_bit_counter_4_increment_out), .Set(n1_bit_counter_4_set_out),
    .Out(n1_bit_counter_7_out[5]), .Data(and_2_out));
  _1_bit_Counter u_1_bit_counter_4 (
    .Increment_Out(n1_bit_counter_4_increment_out), .Set_Out(n1_bit_counter_4_set_out),
    .Increment(n1_bit_counter_2_increment_out), .Set(n1_bit_counter_2_set_out),
    .Out(n1_bit_counter_7_out[4]), .Data(and_4_out));
  and and_3 (and_3_out, n8_bit_register_1__3_2, not_2_out);
  and and_4 (and_4_out, n8_bit_register_1__2_2, not_2_out);
  D_Flip_Flop d_ff_4 (.Q(MP_MAR_S0), .preset(n3_bit_demultiplexer_1__0_2), .reset(or_4_out));  // open: clk, D, Qn, en
  or or_4 (or_4_out, Reset, and_5_out);
  and and_5 (and_5_out, and_9_out, n3_bit_demultiplexer_1__1_2);
  _1_bit_Counter u_1_bit_counter_5 (
    .Increment_Out(n1_bit_counter_5_increment_out), .Set_Out(n1_bit_counter_5_set_out),
    .Increment(n1_bit_counter_6_increment_out), .Set(n1_bit_counter_6_set_out),
    .Out(n1_bit_counter_7_out[2]), .Data(and_8_out));
  _1_bit_Counter u_1_bit_counter_6 (
    .Increment_Out(n1_bit_counter_6_increment_out), .Set_Out(n1_bit_counter_6_set_out),
    .Increment(n1_bit_counter_7_increment_out), .Set(n1_bit_counter_7_set_out),
    .Out(n1_bit_counter_7_out[1]), .Data(and_7_out));
  _1_bit_Counter u_1_bit_counter_7 (
    .Increment_Out(n1_bit_counter_7_increment_out), .Set_Out(n1_bit_counter_7_set_out),
    .Increment(and_14_out), .Set(or_5_out), .Out(n1_bit_counter_7_out[0]), .Data(and_6_out));
  and and_6 (and_6_out, n8_bit_register_1__6_2, not_2_out);
  and and_7 (and_7_out, n8_bit_register_1__5_2, not_2_out);
  and and_8 (and_8_out, n8_bit_register_1__4_2, not_2_out);
  and and_9 (and_9_out, n3_bit_demultiplexer_1__2_2, n3_bit_demultiplexer_1__0_2);
  _3_bit_Demultiplexer u_3_bit_demultiplexer_1 (
    ._0_3(n3_bit_demultiplexer_1__0_3), ._1_3(n3_bit_demultiplexer_1__1_3),
    ._2_3(n3_bit_demultiplexer_1__2_3), ._2_2(n3_bit_demultiplexer_1__2_2),
    ._1_2(n3_bit_demultiplexer_1__1_2), ._0_2(n3_bit_demultiplexer_1__0_2), ._2(and_10_out[9]),
    ._1(and_10_out[8]), ._0(and_10_out[7]), .S(and_10_out[6]));
  not not_1 (not_1_out, and_14_out);
  not not_2 (not_2_out, or_6_out);
  assign {and_10_out[31:17], Read_Input, and_10_out[15], A_Clock, MBR_Clock, MAR_Clock, and_10_out[11:5], IR_Clock, Stack_Pop, Stack_Push, and_10_out[1], PC_Count} = rom_1_data & {32{not_3_out[31]}};  // AND_Gate and_10, 32 bits wide
  ROM #(.addrWidth(7), .dataWidth(32)) rom_1 (.addr(n1_bit_counter_7_out), .data(rom_1_data));  // open: sel
  or or_5 (or_5_out, and_11_out, or_6_out);
  or or_6 (or_6_out, button_1_out, Reset);
  and and_11 (and_11_out, and_14_out, or_16_out);
  not not_3 (not_3_out[31], and_14_out);
  and and_12 (and_12_out, and_10_out[11], One_by_One);
  Button button_1 (.out(button_1_out));
  or or_7 (or_7_out, rom_2_data[24], rom_2_data[23]);
  _8_way_Demultiplex u_8_way_demultiplex_1 (
    .Data(1'b1), ._1(n8_way_demultiplex_1__1), ._2(n8_way_demultiplex_1__2), ._3(n8_way_demultiplex_1__3),
    ._4(n8_way_demultiplex_1__4), ._5(n8_way_demultiplex_1__5), ._7(n8_way_demultiplex_1__7),
    .S2(and_10_out[21]), .S1(and_10_out[20]), .S0(and_10_out[19]));  // open: _0, _6
  and and_13 (and_13_out, d_ff_6_q, and_15_out);
  and and_14 (and_14_out, and_13_out, d_ff_5_q);
  D_Flip_Flop d_ff_5 (.clk(and_12_out), .D(1'b0), .Q(d_ff_5_q), .preset(or_8_out));  // open: Qn, en, reset
  or or_8 (or_8_out, Next_Instruction, Reset);
  or or_9 (or_9_out, or_7_out, rom_2_data[22]);
  _2_bit_Equator u_2_bit_equator_1 (
    .Active(n8_way_demultiplex_1__1), .A0(and_10_out[22]), .A1(and_10_out[23]),
    .Equal(n2_bit_equator_1_equal), .B1(rom_2_data[20]), .B0(rom_2_data[19]));
  _1_bit_Equator Target (._1(and_10_out[24]), ._0(or_9_out), .Active(n8_way_demultiplex_1__4), .X(Target_x));
  _1_bit_Equator Condition (._1(and_10_out[24]), ._0(or_19_out), .Active(n8_way_demultiplex_1__5), .X(Condition_x));
  D_Flip_Flop d_ff_6 (.clk(and_10_out[17]), .D(1'b0), .Q(d_ff_6_q), .preset(or_10_out));  // open: Qn, en, reset
  or or_10 (or_10_out, Input_Available, Reset);
  and and_15 (and_15_out, or_11_out, d_ff_7_q);
  D_Flip_Flop d_ff_7 (.Q(d_ff_7_q), .preset(Reset), .reset(and_17_out));  // open: clk, D, Qn, en
  ROM #(.dataWidth(32)) rom_2 (
    .addr({_7, _6, _5, _4, _3, _2, _1, _0}),
    .data({rom_2_data, Multiply, A_Invert, B_Invert, AND, OR, A, B, Shift_A_Right, Shift_B_Right, Shift_Loop, Shift_A_Left, Shift_B_Left, XOR, Increment, ADD, X_Invert}));  // open: sel
  _3_bit_Equator u_3_bit_equator_1 (
    .Active(n8_way_demultiplex_1__2), .A0(and_10_out[22]), .A1(and_10_out[23]), .A2(and_10_out[24]),
    .Equal(n3_bit_equator_1_equal), .B2(rom_2_data[31]), .B1(rom_2_data[30]), .B0(rom_2_data[29]));
  Button button_2 (.out(button_2_out));
  or or_11 (or_11_out, button_2_out, Clock);
  _1_bit_Equator u_1_bit_equator_1 (
    ._1(and_10_out[22]), ._0(rom_2_data[21]), .Active(n8_way_demultiplex_1__3), .X(n1_bit_equator_1_x));
  or or_12 (or_12_out, n3_bit_equator_1_equal, n2_bit_equator_1_equal);
  or or_13 (or_13_out, n1_bit_equator_1_x, or_12_out);
  or or_14 (or_14_out, Condition_x, or_13_out);
  or or_15 (or_15_out, n8_way_demultiplex_1__7, or_14_out);
  or or_16 (or_16_out, Target_x, or_15_out);
  and and_16 (and_16_out, rom_2_data[30], rom_2_data[31]);
  and and_17 (and_17_out, rom_2_data[29], and_16_out);
  _1_bit_Equator u_1_bit_equator_2 (._1(XOR), ._0(B_Greater_A), .Active(Increment), .X(n1_bit_equator_2_x));
  _1_bit_Equator u_1_bit_equator_3 (._1(Shift_A_Left), ._0(A_Greater_B), .Active(Shift_B_Left), .X(n1_bit_equator_3_x));
  _1_bit_Equator u_1_bit_equator_4 (._1(Shift_B_Right), ._0(Carry_Out), .Active(Shift_Loop), .X(n1_bit_equator_4_x));
  or or_17 (or_17_out, n1_bit_equator_4_x, n1_bit_equator_3_x);
  or or_18 (or_18_out, Shift_A_Right, or_17_out);
  or or_19 (or_19_out, or_18_out, or_20_out);
  _1_bit_Equator u_1_bit_equator_5 (._1(ADD), ._0(not_4_out), .Active(X_Invert), .X(n1_bit_equator_5_x));
  or or_20 (or_20_out, n1_bit_equator_2_x, n1_bit_equator_5_x);
  not not_4 (not_4_out, Not_Equal);
  or or_21 (Clock_CCR, A_Clock, Reset);
  or or_22 (or_22_out, n3_bit_demultiplexer_1__2_3, Reset);
  or or_23 (PC_Set, Reset, and_10_out[1]);
  D_Flip_Flop d_ff_8 (.Q(MP_PC_S0), .preset(n3_bit_demultiplexer_1__0_3), .reset(or_22_out));  // open: clk, D, Qn, en
  D_Flip_Flop d_ff_9 (.Q(MP_PC_S1), .preset(n3_bit_demultiplexer_1__1_3), .reset(or_22_out));  // open: clk, D, Qn, en

  assign AA_Reset = Reset;
  assign AB_Reset = Reset;
  assign AX_Reset = Reset;
  assign AY_Reset = Reset;
  assign IR_Reset = Reset;
  assign MAR_Reset = Reset;
  assign MBR_Reset = Reset;
  assign Reset_IO = Reset;
  assign Stack_Reset = Reset;

  // Notes on the sheet:
  //   contents of rom_1 (hex, n*v repeats v):
  //   380 200 1000 2000 10 36080000 1 1000 2000 18880000 20c80000 28380000 380 100 40000 28380000 380 280
  //   40000 0 1000 2000 36180000 380 80 1000 2000 20 7a100000 46500000 4a900000 5ed00000 6b100000 77500000
  //   0 4000 7a380000 1 7a280000 380 200 1000 2000 240 140 2 7e380000 1 4 240 140 2 7e380000 8 240 1c0 2 0
  //   7e380000 10000 20000 400 1 8000 800 380000
  //   contents of rom_2 (hex, n*v repeats v):
  //   0 60080000 60280000 80000000 e0000000 2e408000 2e808000 32c08000 33008000 2a408000 2b008000 36c08000
  //   36808000 2c488000 2c688000 2c508000 2c588000 2e400002 2e800002 32c00002 33000002 2a400002 2b000002
  //   36c00002 36800002 2c480002 2c680002 2c500002 2c580002 2e402006 2e804006 32c02006 33004006 2c682006
  //   2c482006 2c502006 2c582006 28400006 26800006 30c00006 23000006 23680006 23500006 23580006 28402002
  //   26804002 30c02002 23004002 25684002 25504002 25584002 24480200 24680200 24500200 24580200 24880200
  //   24a80200 24900200 24980200 24c80200 24e80200 24d00200 24d80200 25080200 25280200 25100200 25180200
  //   29680400 27680200 31680400 23680200 29500400 27500200 31500400 23500200 29580400 27580200 31580400
  //   23580200 29c00400 27c00200 31c00400 23c00200 25c80200 25e80200 25d00200 25d80200 38400400 38800200
  //   a0000000 28800400 26400200 31000400 22c00200 28c00400 30400400 27000200 22800200 29000400 22400200
  //   30800400 26c00200 28400100 28400020 26800080 26800010 28400140 28400060 268000c0 26800050 0 0
  //   2e000000 32000000 2c080000 2c280000 2c100000 2c180000 40000100 40000000 40000000 40000003 40000001
  //   4000000c 40000030 4000000f 40000033 28404400 26802200 30c04400 23002200 25682200 25502200 25582200
  //   28404003 26802003 30c04003 23002003 25682003 25502003 25582003 2e401000 2e400800 2e400008 32c01000
  //   32c00800 32c00008 20400000 20800000 20c00000 21000000 21680000 21500000 21580000 20000000
endmodule

module _3_Way_Multiplexor (
  input  _7,
  input  _6,
  input  _5,
  input  _4,
  input  _3,
  input  _2,
  input  _1,
  input  _0,
  input  _0_2,
  input  _0_3,
  input  _1_2,
  input  _1_3,
  input  _2_2,
  input  _2_3,
  input  _3_2,
  input  _3_3,
  input  _4_2,
  input  _4_3,
  input  _5_2,
  input  _5_3,
  input  _6_2,
  input  _6_3,
  input  _7_2,
  input  _7_3,
  input  S0,
  input  S1,
  output _7_4,
  output _6_4,
  output _5_4,
  output _4_4,
  output _3_4,
  output _2_4,
  output _1_4,
  output _0_4
);

  wire and_1_out, and_2_out, and_3_out, and_4_out, and_5_out, and_6_out, and_7_out, and_8_out, and_9_out,
       and_10_out, and_11_out, and_12_out, and_13_out, and_14_out, and_15_out, and_16_out, and_17_out,
       and_18_out, and_19_out, and_20_out, and_21_out, and_22_out, and_23_out, and_24_out, and_25_out,
       and_26_out, and_27_out, and_28_out, and_29_out, and_30_out, and_31_out, and_32_out, and_33_out,
       and_34_out, and_35_out, and_36_out, and_37_out, and_38_out, and_39_out, and_40_out, and_41_out,
       and_42_out, and_43_out, and_44_out, and_45_out, and_46_out, and_47_out, and_48_out, not_1_out,
       not_2_out, not_3_out, or_1_out, or_3_out, or_4_out, or_7_out, or_8_out, or_11_out, or_12_out,
       or_15_out;

  not not_1 (not_1_out, S1);
  and and_1 (and_1_out, _0_2, not_1_out);
  and and_2 (and_2_out, _1_2, not_1_out);
  and and_3 (and_3_out, _2_2, not_1_out);
  and and_4 (and_4_out, _3_2, not_1_out);
  and and_5 (and_5_out, _4_2, not_1_out);
  and and_6 (and_6_out, _5_2, not_1_out);
  and and_7 (and_7_out, _6_2, not_1_out);
  and and_8 (and_8_out, _7_2, not_1_out);
  not not_2 (not_2_out, not_3_out);
  and and_9 (and_9_out, not_3_out, and_18_out);
  and and_10 (and_10_out, not_2_out, and_1_out);
  and and_11 (and_11_out, not_2_out, and_2_out);
  and and_12 (and_12_out, not_2_out, and_3_out);
  and and_13 (and_13_out, not_2_out, and_4_out);
  and and_14 (and_14_out, not_2_out, and_5_out);
  and and_15 (and_15_out, not_2_out, and_6_out);
  and and_16 (and_16_out, not_2_out, and_7_out);
  and and_17 (and_17_out, not_2_out, and_8_out);
  or or_1 (or_1_out, and_40_out, and_9_out);
  or or_2 (_7_4, and_17_out, or_1_out);
  and and_18 (and_18_out, _7, S1);
  and and_19 (and_19_out, _6, S1);
  and and_20 (and_20_out, not_3_out, and_19_out);
  and and_21 (and_21_out, not_3_out, and_23_out);
  or or_3 (or_3_out, and_38_out, and_21_out);
  or or_4 (or_4_out, and_39_out, and_20_out);
  or or_5 (_6_4, and_16_out, or_4_out);
  or or_6 (_5_4, and_15_out, or_3_out);
  and and_22 (and_22_out, _4, S1);
  and and_23 (and_23_out, _5, S1);
  and and_24 (and_24_out, not_3_out, and_27_out);
  and and_25 (and_25_out, not_3_out, and_22_out);
  or or_7 (or_7_out, and_36_out, and_24_out);
  or or_8 (or_8_out, and_37_out, and_25_out);
  or or_9 (_3_4, and_13_out, or_7_out);
  or or_10 (_4_4, and_14_out, or_8_out);
  and and_26 (and_26_out, _2, S1);
  and and_27 (and_27_out, _3, S1);
  and and_28 (and_28_out, not_3_out, and_26_out);
  and and_29 (and_29_out, not_3_out, and_31_out);
  or or_11 (or_11_out, and_34_out, and_29_out);
  or or_12 (or_12_out, and_35_out, and_28_out);
  or or_13 (_2_4, and_12_out, or_12_out);
  or or_14 (_1_4, and_11_out, or_11_out);
  and and_30 (and_30_out, _0, S1);
  and and_31 (and_31_out, _1, S1);
  and and_32 (and_32_out, not_3_out, and_30_out);
  and and_33 (and_33_out, S0, and_41_out);
  and and_34 (and_34_out, S0, and_42_out);
  and and_35 (and_35_out, S0, and_43_out);
  and and_36 (and_36_out, S0, and_44_out);
  and and_37 (and_37_out, S0, and_45_out);
  and and_38 (and_38_out, S0, and_46_out);
  and and_39 (and_39_out, S0, and_47_out);
  and and_40 (and_40_out, S0, and_48_out);
  or or_15 (or_15_out, and_33_out, and_32_out);
  or or_16 (_0_4, and_10_out, or_15_out);
  not not_3 (not_3_out, S0);
  and and_41 (and_41_out, _0_3, S1);
  and and_42 (and_42_out, _1_3, S1);
  and and_43 (and_43_out, _2_3, S1);
  and and_44 (and_44_out, _3_3, S1);
  and and_45 (and_45_out, _4_3, S1);
  and and_46 (and_46_out, _5_3, S1);
  and and_47 (and_47_out, _6_3, S1);
  and and_48 (and_48_out, _7_3, S1);
endmodule

module _8_bit_Counter (
  input  Decrement_Mode,
  input  Count,
  input  Set,
  input  _7,
  input  _6,
  input  _5,
  input  _4,
  input  _3,
  input  _2,
  input  _1,
  input  _0,
  output _7_2,
  output _6_2,
  output _5_2,
  output _4_2,
  output _3_2,
  output _2_2,
  output _1_2,
  output _0_2,
  output Decrement_Mode_Carry,
  output Count_Out,
  output Set_Carry
);

  wire and_1_out, and_2_out, and_3_out, and_4_out, and_5_out, and_6_out, and_7_out, and_8_out, and_9_out,
       and_10_out, and_11_out, and_12_out, and_13_out, and_14_out, and_15_out, and_16_out, and_17_out,
       and_18_out, and_19_out, and_20_out, and_21_out, and_22_out, and_23_out, and_24_out, and_25_out,
       and_26_out, and_27_out, and_28_out, and_29_out, and_30_out, and_31_out, and_32_out, and_33_out,
       and_34_out, and_35_out, and_36_out, and_37_out, and_38_out, and_39_out, and_41_out, and_42_out,
       and_43_out, and_44_out, and_46_out, and_47_out, and_48_out, and_49_out, and_50_out, not_1_out,
       not_2_out, not_3_out, not_4_out, not_5_out, not_6_out, not_7_out, not_8_out, not_9_out, not_10_out,
       not_11_out, not_12_out, not_13_out, not_14_out, not_15_out, not_16_out, not_17_out, not_18_out,
       not_19_out, not_20_out, not_21_out, not_22_out, not_23_out, not_24_out, not_25_out, or_2_out,
       or_3_out, or_4_out, or_5_out, or_6_out, or_7_out, or_8_out, t_ff_1_qn, t_ff_2_qn, t_ff_3_qn,
       t_ff_4_qn, t_ff_5_qn, t_ff_6_qn, t_ff_7_qn, t_ff_8_qn;

  and and_1 (and_1_out, and_3_out, not_25_out);
  and and_2 (and_2_out, Decrement_Mode, and_4_out);
  or or_1 (Count_Out, and_1_out, and_2_out);
  and and_3 (and_3_out, t_ff_1_qn, not_1_out);
  not not_1 (not_1_out, t_ff_1_qn);
  and and_4 (and_4_out, _7_2, not_2_out);
  not not_2 (not_2_out, _7_2);
  and and_5 (and_5_out, and_9_out, not_25_out);
  and and_6 (and_6_out, Decrement_Mode, and_10_out);
  or or_2 (or_2_out, and_5_out, and_6_out);
  T_Flip_Flop t_ff_1 (
    .clk(or_2_out), .T(1'b1), .Q(_7_2), .Qn(t_ff_1_qn), .preset(and_7_out), .reset(and_8_out));  // open: en
  and and_7 (and_7_out, Set, _7);
  and and_8 (and_8_out, not_3_out, Set);
  not not_3 (not_3_out, _7);
  or or_3 (or_3_out, and_13_out, and_14_out);
  and and_9 (and_9_out, t_ff_2_qn, not_6_out);
  and and_10 (and_10_out, _6_2, not_4_out);
  not not_4 (not_4_out, _6_2);
  and and_11 (and_11_out, Set, _6);
  not not_5 (not_5_out, _6);
  and and_12 (and_12_out, t_ff_3_qn, not_7_out);
  and and_13 (and_13_out, and_12_out, not_25_out);
  and and_14 (and_14_out, Decrement_Mode, and_15_out);
  and and_15 (and_15_out, _5_2, not_8_out);
  not not_6 (not_6_out, t_ff_2_qn);
  and and_16 (and_16_out, and_23_out, not_25_out);
  and and_17 (and_17_out, Decrement_Mode, and_24_out);
  or or_4 (or_4_out, and_16_out, and_17_out);
  T_Flip_Flop t_ff_2 (
    .clk(or_3_out), .T(1'b1), .Q(_6_2), .Qn(t_ff_2_qn), .preset(and_11_out), .reset(and_18_out));  // open: en
  and and_18 (and_18_out, not_5_out, Set);
  and and_19 (and_19_out, Set, _5);
  not not_7 (not_7_out, t_ff_3_qn);
  not not_8 (not_8_out, _5_2);
  or or_5 (or_5_out, and_21_out, and_22_out);
  T_Flip_Flop t_ff_3 (
    .clk(or_4_out), .T(1'b1), .Q(_5_2), .Qn(t_ff_3_qn), .preset(and_19_out), .reset(and_20_out));  // open: en
  and and_20 (and_20_out, not_9_out, Set);
  not not_9 (not_9_out, _5);
  and and_21 (and_21_out, and_27_out, not_25_out);
  and and_22 (and_22_out, Decrement_Mode, and_28_out);
  and and_23 (and_23_out, t_ff_4_qn, not_10_out);
  not not_10 (not_10_out, t_ff_4_qn);
  and and_24 (and_24_out, _4_2, not_11_out);
  not not_11 (not_11_out, _4_2);
  T_Flip_Flop t_ff_4 (
    .clk(or_5_out), .T(1'b1), .Q(_4_2), .Qn(t_ff_4_qn), .preset(and_25_out), .reset(and_26_out));  // open: en
  and and_25 (and_25_out, Set, _4);
  and and_26 (and_26_out, not_12_out, Set);
  not not_12 (not_12_out, _4);
  and and_27 (and_27_out, t_ff_5_qn, not_13_out);
  not not_13 (not_13_out, t_ff_5_qn);
  and and_28 (and_28_out, _3_2, not_14_out);
  not not_14 (not_14_out, _3_2);
  and and_29 (and_29_out, and_33_out, not_25_out);
  and and_30 (and_30_out, Decrement_Mode, and_34_out);
  or or_6 (or_6_out, and_29_out, and_30_out);
  T_Flip_Flop t_ff_5 (
    .clk(or_6_out), .T(1'b1), .Q(_3_2), .Qn(t_ff_5_qn), .preset(and_32_out), .reset(and_31_out));  // open: en
  and and_31 (and_31_out, not_15_out, Set);
  and and_32 (and_32_out, Set, _3);
  not not_15 (not_15_out, _3);
  or or_7 (or_7_out, and_37_out, and_38_out);
  and and_33 (and_33_out, t_ff_6_qn, not_18_out);
  and and_34 (and_34_out, _2_2, not_16_out);
  not not_16 (not_16_out, _2_2);
  and and_35 (and_35_out, Set, _2);
  not not_17 (not_17_out, _2);
  and and_36 (and_36_out, t_ff_7_qn, not_19_out);
  and and_37 (and_37_out, and_36_out, not_25_out);
  and and_38 (and_38_out, Decrement_Mode, and_39_out);
  and and_39 (and_39_out, _1_2, not_20_out);
  // AND_Gate and_40 is placed but not wired
  not not_18 (not_18_out, t_ff_6_qn);
  and and_41 (and_41_out, and_47_out, not_25_out);
  and and_42 (and_42_out, Decrement_Mode, and_48_out);
  or or_8 (or_8_out, and_41_out, and_42_out);
  T_Flip_Flop t_ff_6 (
    .clk(or_7_out), .T(1'b1), .Q(_2_2), .Qn(t_ff_6_qn), .preset(and_35_out), .reset(and_43_out));  // open: en
  and and_43 (and_43_out, not_17_out, Set);
  and and_44 (and_44_out, Set, _1);
  not not_19 (not_19_out, t_ff_7_qn);
  not not_20 (not_20_out, _1_2);
  // AND_Gate and_45 is placed but not wired
  T_Flip_Flop t_ff_7 (
    .clk(or_8_out), .T(1'b1), .Q(_1_2), .Qn(t_ff_7_qn), .preset(and_44_out), .reset(and_46_out));  // open: en
  and and_46 (and_46_out, not_21_out, Set);
  not not_21 (not_21_out, _1);
  and and_47 (and_47_out, t_ff_8_qn, not_22_out);
  not not_22 (not_22_out, t_ff_8_qn);
  and and_48 (and_48_out, _0_2, not_23_out);
  not not_23 (not_23_out, _0_2);
  T_Flip_Flop t_ff_8 (
    .clk(Count), .T(1'b1), .Q(_0_2), .Qn(t_ff_8_qn), .preset(and_49_out), .reset(and_50_out));  // open: en
  and and_49 (and_49_out, Set, _0);
  and and_50 (and_50_out, not_24_out, Set);
  not not_24 (not_24_out, _0);
  not not_25 (not_25_out, Decrement_Mode);

  assign Decrement_Mode_Carry = Decrement_Mode;
  assign Set_Carry = Set;
endmodule

module S_R_Latch (
  input  Set,
  input  Data,
  input  Reset,
  input  Clock,
  output X
);

  wire and_1_out, and_2_out, and_3_out, and_4_out, not_1_out, not_2_out, not_3_out, or_1_out, or_2_out,
       or_3_out, or_4_out, or_5_out;

  not not_1 (not_1_out, Data);
  not not_2 (not_2_out, or_1_out);
  or or_1 (or_1_out, Set, Reset);
  or or_2 (or_2_out, Set, and_1_out);
  and and_1 (and_1_out, Data, not_2_out);
  and and_2 (and_2_out, not_2_out, not_1_out);
  or or_3 (or_3_out, and_2_out, Reset);
  and and_3 (and_3_out, Clock, or_2_out);
  or or_4 (or_4_out, and_3_out, X);
  or or_5 (or_5_out, not_3_out, and_4_out);
  and and_4 (and_4_out, or_3_out, Clock);
  not not_3 (not_3_out, or_4_out);
  not not_4 (X, or_5_out);
endmodule

module bit_Multiplexor (
  input  _1,
  input  _0,
  input  S,
  output X
);

  wire and_1_out, and_2_out;

  and and_1 (and_1_out, _1, S);
  and and_2 (and_2_out, _0, S);
  or or_1 (X, and_1_out, and_2_out);
endmodule

// C
module _1_bit_Counter (
  input  Increment,
  input  Set,
  input  Data,
  output Out,
  output Increment_Out,
  output Set_Out
);

  wire and_1_out, and_2_out, not_1_out;

  T_Flip_Flop t_ff_1 (
    .clk(Increment), .T(Increment), .Q(Out), .Qn(Increment_Out), .preset(and_1_out), .reset(and_2_out));  // open: en
  and and_1 (and_1_out, Set, Data);
  and and_2 (and_2_out, not_1_out, Set);
  not not_1 (not_1_out, Data);

  assign Set_Out = Set;
endmodule

module _8_bit_Stack (
  input  Reset,
  input  Push,
  input  _7,
  input  _5,
  input  _3,
  input  _1,
  input  Pop,
  input  _6,
  input  _4,
  input  _2,
  input  _0,
  output _0_2,
  output _1_2,
  output _2_2,
  output _3_2,
  output _4_2,
  output _5_2,
  output _6_2,
  output _7_2
);

  wire not_1_out;
  wire [7:0] n8_bit_counter_inc_dec_1__0;

  _8_bit_Counter__Inc_Dec u_8_bit_counter_inc_dec_1 (
    ._0(n8_bit_counter_inc_dec_1__0[0]), ._1(n8_bit_counter_inc_dec_1__0[1]),
    ._2(n8_bit_counter_inc_dec_1__0[2]), ._3(n8_bit_counter_inc_dec_1__0[3]),
    ._4(n8_bit_counter_inc_dec_1__0[4]), ._5(n8_bit_counter_inc_dec_1__0[5]),
    ._6(n8_bit_counter_inc_dec_1__0[6]), ._7(n8_bit_counter_inc_dec_1__0[7]), .Reset(Reset),
    .Increment(Push), .Decrement(Pop));  // open: Carry_Out
  RAM #(.bus("separate")) ram_1 (
    .addr(n8_bit_counter_inc_dec_1__0), .din({_7, _6, _5, _4, _3, _2, _1, _0}),
    .data({_7_2, _6_2, _5_2, _4_2, _3_2, _2_2, _1_2, _0_2}), .clk(Push), .ld(not_1_out), .clr(Reset));  // open: str, sel
  not not_1 (not_1_out, Push);
endmodule

module _8_bit_Counter__Inc_Dec (
  input  Reset,
  input  Increment,
  input  Decrement,
  output _0,
  output _1,
  output _2,
  output _3,
  output _4,
  output _5,
  output _6,
  output _7,
  output Carry_Out
);

  wire n8_bit_adder_1_x0, n8_bit_adder_1_x1, n8_bit_adder_1_x2, n8_bit_adder_1_x3, n8_bit_adder_1_x4,
       n8_bit_adder_1_x5, n8_bit_adder_1_x6, n8_bit_adder_1_x7, n8_bit_register_1__0_3,
       n8_bit_register_1__1_2, n8_bit_register_1__2_2, n8_bit_register_1__3_2, n8_bit_register_1__4_2,
       n8_bit_register_1__5_2, n8_bit_register_1__6_2, n8_bit_register_1__7_2, not_1_out, or_1_out;
  wire [7:0] undriven, undriven_2;

  _8_bit_Register u_8_bit_register_1 (
    ._6(_6), ._5(_5), ._4(_4), ._3(_3), ._2(_2), ._1(_1), ._0(_0), ._0_3(n8_bit_register_1__0_3),
    ._1_2(n8_bit_register_1__1_2), ._2_2(n8_bit_register_1__2_2), ._3_2(n8_bit_register_1__3_2),
    ._4_2(n8_bit_register_1__4_2), ._5_2(n8_bit_register_1__5_2), ._6_2(n8_bit_register_1__6_2),
    .in_1(undriven), ._7_2(n8_bit_register_1__7_2), ._7(_7), .Clock(Reset), .Enable(not_1_out));  // open: _0_2, Reset
  // Probe on undriven
  not not_1 (not_1_out, or_1_out);
  _8_bit_Adder u_8_bit_adder_1 (
    .A0(n8_bit_register_1__0_3), .B0(Decrement), .A1(n8_bit_register_1__1_2), .B1(Decrement),
    .A2(n8_bit_register_1__2_2), .B2(Decrement), .A3(n8_bit_register_1__3_2), .B3(Decrement),
    .A4(n8_bit_register_1__4_2), .B4(Decrement), .A5(n8_bit_register_1__5_2), .B5(Decrement),
    .A6(n8_bit_register_1__6_2), .B6(Decrement), .A7(n8_bit_register_1__7_2), .B7(Decrement),
    .X0(n8_bit_adder_1_x0), .X1(n8_bit_adder_1_x1), .X2(n8_bit_adder_1_x2), .X3(n8_bit_adder_1_x3),
    .X4(n8_bit_adder_1_x4), .X5(n8_bit_adder_1_x5), .X6(n8_bit_adder_1_x6), .X7(n8_bit_adder_1_x7),
    .Increment(Increment), .Carry_Out(Carry_Out));
  _8_bit_Register u_8_bit_register_2 (
    ._6(n8_bit_adder_1_x6), ._5(n8_bit_adder_1_x5), ._4(n8_bit_adder_1_x4), ._3(n8_bit_adder_1_x3),
    ._2(n8_bit_adder_1_x2), ._1(n8_bit_adder_1_x1), ._0(n8_bit_adder_1_x0), ._0_3(_0), ._1_2(_1), ._2_2(_2),
    ._3_2(_3), ._4_2(_4), ._5_2(_5), ._6_2(_6), .in_1(undriven_2), ._7_2(_7), ._7(n8_bit_adder_1_x7),
    .Clock(Reset), .Enable(or_1_out));  // open: _0_2, Reset
  // Probe on undriven_2
  or or_1 (or_1_out, Increment, Decrement);
endmodule

// Demultiplexor
module _4_way_Demultiplex (
  input  Data,
  input  S1,
  input  S0,
  output _0,
  output _1,
  output _2,
  output _3
);

  wire and_2_out, and_4_out, and_6_out, and_8_out, not_1_out, not_2_out, not_3_out, not_4_out;

  not not_1 (not_1_out, S1);
  not not_2 (not_2_out, S0);
  not not_3 (not_3_out, S1);
  not not_4 (not_4_out, S0);
  and and_1 (_0, Data, and_2_out);
  and and_2 (and_2_out, not_1_out, not_2_out);
  and and_3 (_1, Data, and_4_out);
  and and_4 (and_4_out, not_3_out, S0);
  and and_5 (_2, Data, and_6_out);
  and and_6 (and_6_out, S1, not_4_out);
  and and_7 (_3, Data, and_8_out);
  and and_8 (and_8_out, S1, S0);
endmodule

// Demultiplexor
module _8_way_Demultiplex (
  input  Data,
  input  S2,
  input  S1,
  input  S0,
  output _0,
  output _1,
  output _2,
  output _3,
  output _4,
  output _5,
  output _6,
  output _7
);

  wire and_1_out, and_2_out, and_3_out, and_4_out, and_5_out, and_6_out, and_7_out, and_8_out, and_10_out,
       and_12_out, and_14_out, and_16_out, and_18_out, and_20_out, and_22_out, and_24_out, not_1_out,
       not_2_out, not_3_out, not_4_out, not_5_out, not_6_out, not_7_out, not_8_out, not_9_out, not_10_out,
       not_11_out, not_12_out;

  not not_1 (not_1_out, S2);
  not not_2 (not_2_out, S1);
  not not_3 (not_3_out, S0);
  and and_1 (and_1_out, not_2_out, not_3_out);
  not not_4 (not_4_out, S2);
  not not_5 (not_5_out, S1);
  and and_2 (and_2_out, not_5_out, S0);
  not not_6 (not_6_out, S2);
  and and_3 (and_3_out, S1, not_7_out);
  not not_7 (not_7_out, S0);
  not not_8 (not_8_out, S2);
  and and_4 (and_4_out, S1, S0);
  not not_9 (not_9_out, S1);
  and and_5 (and_5_out, not_9_out, not_10_out);
  not not_10 (not_10_out, S0);
  not not_11 (not_11_out, S1);
  and and_6 (and_6_out, not_11_out, S0);
  and and_7 (and_7_out, S1, not_12_out);
  not not_12 (not_12_out, S0);
  and and_8 (and_8_out, S1, S0);
  and and_9 (_0, Data, and_10_out);
  and and_10 (and_10_out, not_1_out, and_1_out);
  and and_11 (_1, Data, and_12_out);
  and and_12 (and_12_out, not_4_out, and_2_out);
  and and_13 (_2, Data, and_14_out);
  and and_14 (and_14_out, not_6_out, and_3_out);
  and and_15 (_3, Data, and_16_out);
  and and_16 (and_16_out, not_8_out, and_4_out);
  and and_17 (_4, Data, and_18_out);
  and and_18 (and_18_out, S2, and_5_out);
  and and_19 (_5, Data, and_20_out);
  and and_20 (and_20_out, S2, and_6_out);
  and and_21 (_6, Data, and_22_out);
  and and_22 (and_22_out, S2, and_7_out);
  and and_23 (_7, Data, and_24_out);
  and and_24 (and_24_out, S2, and_8_out);
endmodule

// Eq
module _1_bit_Equator (
  input  _0,
  input  _1,
  input  Active,
  output X
);

  wire and_1_out, not_1_out, or_1_out, or_2_out;

  and and_1 (and_1_out, _1, _0);
  or or_1 (or_1_out, _0, _1);
  not not_1 (not_1_out, or_1_out);
  or or_2 (or_2_out, and_1_out, not_1_out);
  and and_2 (X, or_2_out, Active);
endmodule

// Equator
module _3_bit_Equator (
  input  B2,
  input  B1,
  input  B0,
  input  Active,
  input  A0,
  input  A1,
  input  A2,
  output Equal
);

  wire and_1_out, n1_bit_equator_1_x, n1_bit_equator_2_x, n1_bit_equator_3_x;

  _1_bit_Equator u_1_bit_equator_1 (._1(A2), ._0(B2), .Active(Active), .X(n1_bit_equator_1_x));
  _1_bit_Equator u_1_bit_equator_2 (._1(A0), ._0(B0), .Active(Active), .X(n1_bit_equator_2_x));
  _1_bit_Equator u_1_bit_equator_3 (._1(A1), ._0(B1), .Active(Active), .X(n1_bit_equator_3_x));
  and and_1 (and_1_out, n1_bit_equator_2_x, n1_bit_equator_3_x);
  and and_2 (Equal, and_1_out, n1_bit_equator_1_x);
endmodule
// Multiplexor
module _2_bit_Multiplexor (
  input  _0,
  input  _1,
  input  S,
  input  _1_2,
  input  _0_2,
  output _0_3,
  output _1_3
);

  wire and_1_out, and_2_out, and_3_out, and_4_out, not_1_out;

  and and_1 (and_1_out, _0, not_1_out);
  and and_2 (and_2_out, _1, not_1_out);
  not not_1 (not_1_out, S);
  or or_1 (_1_3, and_2_out, and_3_out);
  and and_3 (and_3_out, _1_2, S);
  and and_4 (and_4_out, _0_2, S);
  or or_2 (_0_3, and_1_out, and_4_out);
endmodule

// DMP
module _3_bit_Demultiplexer (
  input  _2,
  input  _1,
  input  _0,
  input  S,
  output _2_2,
  output _1_2,
  output _0_2,
  output _0_3,
  output _1_3,
  output _2_3
);

  wire not_1_out;

  and and_1 (_2_2, not_1_out, _2);
  and and_2 (_0_2, not_1_out, _0);
  and and_3 (_1_2, not_1_out, _1);
  not not_1 (not_1_out, S);
  and and_4 (_0_3, _0, S);
  and and_5 (_1_3, _1, S);
  and and_6 (_2_3, _2, S);
endmodule

// Multiplexer
module _5_Way_Multiplexer (
  input  _0,
  input  _0_2,
  input  _1,
  input  _1_2,
  input  _2,
  input  _2_2,
  input  _3,
  input  _3_2,
  input  _4,
  input  _4_2,
  input  _5,
  input  _5_2,
  input  _6,
  input  _6_2,
  input  _7,
  input  _7_2,
  input  _0_3,
  input  _0_4,
  input  _1_3,
  input  _1_4,
  input  _2_3,
  input  _2_4,
  input  _3_3,
  input  _3_4,
  input  _4_3,
  input  _4_4,
  input  _5_3,
  input  _5_4,
  input  _6_3,
  input  _6_4,
  input  _7_3,
  input  _7_4,
  input  _7_5,
  input  _6_5,
  input  _5_5,
  input  _4_5,
  input  _3_5,
  input  _2_5,
  input  _1_5,
  input  _0_5,
  input  S2,
  input  S1,
  input  S0,
  output _7_6,
  output _6_6,
  output _5_6,
  output _4_6,
  output _3_6,
  output _2_6,
  output _1_6,
  output _0_6
);

  wire and_1_out, and_2_out, and_3_out, and_4_out, and_5_out, and_6_out, and_7_out, and_8_out, and_9_out,
       and_10_out, and_11_out, and_12_out, and_13_out, and_14_out, and_15_out, and_16_out, and_17_out,
       and_18_out, and_19_out, and_20_out, and_21_out, and_22_out, and_23_out, and_24_out, and_25_out,
       and_26_out, and_27_out, and_28_out, and_29_out, and_30_out, and_31_out, and_32_out, and_33_out,
       and_34_out, and_35_out, and_36_out, and_37_out, and_38_out, and_39_out, and_40_out, and_41_out,
       and_42_out, and_43_out, and_44_out, and_45_out, and_46_out, and_47_out, and_48_out, and_49_out,
       and_50_out, and_51_out, and_52_out, and_53_out, and_54_out, and_55_out, and_56_out, and_57_out,
       and_58_out, and_59_out, and_60_out, and_61_out, and_62_out, and_63_out, and_64_out, and_65_out,
       and_66_out, and_67_out, and_68_out, and_69_out, and_70_out, and_71_out, and_72_out, and_73_out,
       and_74_out, and_75_out, and_76_out, and_77_out, and_78_out, and_79_out, and_80_out, and_81_out,
       and_82_out, and_83_out, and_84_out, and_85_out, and_86_out, and_87_out, and_88_out, and_89_out,
       and_90_out, and_91_out, and_92_out, and_93_out, and_94_out, and_95_out, and_96_out, and_97_out,
       and_98_out, and_99_out, and_100_out, and_101_out, and_102_out, and_103_out, and_104_out, and_105_out,
       and_106_out, and_107_out, and_108_out, and_109_out, and_110_out, and_111_out, and_112_out,
       and_113_out, and_114_out, and_115_out, and_116_out, and_117_out, and_118_out, and_119_out,
       and_120_out, not_1_out, not_2_out, not_3_out, not_4_out, not_5_out, not_6_out, not_7_out, not_8_out,
       or_2_out, or_3_out, or_6_out, or_7_out, or_8_out, or_9_out, or_10_out, or_11_out, or_14_out,
       or_15_out, or_16_out, or_17_out, or_18_out, or_19_out, or_22_out, or_23_out, or_24_out, or_25_out,
       or_26_out, or_27_out, or_29_out, or_30_out, or_31_out, or_32_out;

  not not_1 (not_1_out, not_7_out);
  and and_1 (and_1_out, _0, not_1_out);
  and and_2 (and_2_out, _1, not_1_out);
  and and_3 (and_3_out, _2, not_1_out);
  and and_4 (and_4_out, _3, not_1_out);
  and and_5 (and_5_out, _4, not_1_out);
  and and_6 (and_6_out, _5, not_1_out);
  and and_7 (and_7_out, _6, not_1_out);
  and and_8 (and_8_out, _7, not_1_out);
  not not_2 (not_2_out, not_1_out);
  and and_9 (and_9_out, _0_3, not_2_out);
  and and_10 (and_10_out, _1_3, not_2_out);
  and and_11 (and_11_out, _2_3, not_2_out);
  and and_12 (and_12_out, _3_3, not_2_out);
  and and_13 (and_13_out, _4_3, not_2_out);
  and and_14 (and_14_out, _5_3, not_2_out);
  and and_15 (and_15_out, _6_3, not_2_out);
  and and_16 (and_16_out, _7_3, not_2_out);
  not not_3 (not_3_out, S2);
  not not_4 (not_4_out, not_8_out);
  and and_17 (and_17_out, not_4_out, and_1_out);
  and and_18 (and_18_out, not_4_out, and_2_out);
  and and_19 (and_19_out, not_4_out, and_3_out);
  and and_20 (and_20_out, not_4_out, and_4_out);
  and and_21 (and_21_out, not_4_out, and_5_out);
  and and_22 (and_22_out, not_4_out, and_6_out);
  and and_23 (and_23_out, not_4_out, and_7_out);
  and and_24 (and_24_out, not_4_out, and_8_out);
  and and_25 (and_25_out, not_4_out, and_9_out);
  and and_26 (and_26_out, not_4_out, and_10_out);
  and and_27 (and_27_out, not_4_out, and_11_out);
  and and_28 (and_28_out, not_4_out, and_12_out);
  and and_29 (and_29_out, not_4_out, and_13_out);
  and and_30 (and_30_out, not_4_out, and_14_out);
  and and_31 (and_31_out, not_4_out, and_15_out);
  and and_32 (and_32_out, not_4_out, and_16_out);
  or or_1 (_7_6, or_2_out, or_3_out);
  or or_2 (or_2_out, and_40_out, and_77_out);
  and and_33 (and_33_out, and_17_out, not_3_out);
  and and_34 (and_34_out, and_18_out, not_3_out);
  and and_35 (and_35_out, and_19_out, not_3_out);
  and and_36 (and_36_out, and_20_out, not_3_out);
  and and_37 (and_37_out, and_21_out, not_3_out);
  and and_38 (and_38_out, and_22_out, not_3_out);
  and and_39 (and_39_out, and_23_out, not_3_out);
  and and_40 (and_40_out, and_24_out, not_3_out);
  or or_3 (or_3_out, and_49_out, or_10_out);
  and and_41 (and_41_out, and_25_out, not_3_out);
  and and_42 (and_42_out, and_26_out, not_3_out);
  and and_43 (and_43_out, and_27_out, not_3_out);
  and and_44 (and_44_out, and_28_out, not_3_out);
  and and_45 (and_45_out, and_29_out, not_3_out);
  and and_46 (and_46_out, and_30_out, not_3_out);
  and and_47 (and_47_out, and_31_out, not_3_out);
  and and_48 (and_48_out, and_32_out, not_3_out);
  and and_49 (and_49_out, not_3_out, and_50_out);
  and and_50 (and_50_out, and_51_out, not_5_out);
  not not_5 (not_5_out, not_4_out);
  and and_51 (and_51_out, not_6_out, _7_5);
  not not_6 (not_6_out, not_2_out);
  or or_4 (_6_6, or_7_out, or_8_out);
  or or_5 (_5_6, or_6_out, or_9_out);
  or or_6 (or_6_out, and_38_out, and_75_out);
  or or_7 (or_7_out, and_39_out, and_76_out);
  or or_8 (or_8_out, and_52_out, or_11_out);
  or or_9 (or_9_out, and_53_out, or_19_out);
  or or_10 (or_10_out, and_48_out, and_85_out);
  or or_11 (or_11_out, and_47_out, and_84_out);
  and and_52 (and_52_out, not_3_out, and_54_out);
  and and_53 (and_53_out, not_3_out, and_55_out);
  and and_54 (and_54_out, and_57_out, not_5_out);
  and and_55 (and_55_out, and_56_out, not_5_out);
  and and_56 (and_56_out, not_6_out, _5_5);
  and and_57 (and_57_out, not_6_out, _6_5);
  or or_12 (_4_6, or_14_out, or_16_out);
  or or_13 (_3_6, or_15_out, or_17_out);
  or or_14 (or_14_out, and_37_out, and_74_out);
  or or_15 (or_15_out, and_36_out, and_73_out);
  or or_16 (or_16_out, and_58_out, or_18_out);
  or or_17 (or_17_out, and_59_out, or_26_out);
  or or_18 (or_18_out, and_45_out, and_82_out);
  or or_19 (or_19_out, and_46_out, and_83_out);
  and and_58 (and_58_out, not_3_out, and_60_out);
  and and_59 (and_59_out, not_3_out, and_61_out);
  and and_60 (and_60_out, and_63_out, not_5_out);
  and and_61 (and_61_out, and_62_out, not_5_out);
  and and_62 (and_62_out, not_6_out, _3_5);
  and and_63 (and_63_out, not_6_out, _4_5);
  or or_20 (_2_6, or_22_out, or_25_out);
  or or_21 (_1_6, or_23_out, or_24_out);
  or or_22 (or_22_out, and_35_out, and_72_out);
  or or_23 (or_23_out, and_34_out, and_71_out);
  or or_24 (or_24_out, and_64_out, or_31_out);
  or or_25 (or_25_out, and_65_out, or_27_out);
  or or_26 (or_26_out, and_44_out, and_81_out);
  or or_27 (or_27_out, and_43_out, and_80_out);
  and and_64 (and_64_out, not_3_out, and_66_out);
  and and_65 (and_65_out, not_3_out, and_67_out);
  and and_66 (and_66_out, and_69_out, not_5_out);
  and and_67 (and_67_out, and_68_out, not_5_out);
  and and_68 (and_68_out, not_6_out, _2_5);
  and and_69 (and_69_out, not_6_out, _1_5);
  or or_28 (_0_6, or_29_out, or_30_out);
  or or_29 (or_29_out, and_33_out, and_70_out);
  and and_70 (and_70_out, and_89_out, S2);
  and and_71 (and_71_out, and_90_out, S2);
  and and_72 (and_72_out, and_91_out, S2);
  and and_73 (and_73_out, and_92_out, S2);
  and and_74 (and_74_out, and_93_out, S2);
  and and_75 (and_75_out, and_94_out, S2);
  and and_76 (and_76_out, and_95_out, S2);
  and and_77 (and_77_out, and_96_out, S2);
  or or_30 (or_30_out, and_86_out, or_32_out);
  or or_31 (or_31_out, and_42_out, and_79_out);
  or or_32 (or_32_out, and_41_out, and_78_out);
  and and_78 (and_78_out, and_97_out, S2);
  and and_79 (and_79_out, and_98_out, S2);
  and and_80 (and_80_out, and_99_out, S2);
  and and_81 (and_81_out, and_100_out, S2);
  and and_82 (and_82_out, and_101_out, S2);
  and and_83 (and_83_out, and_102_out, S2);
  and and_84 (and_84_out, and_103_out, S2);
  and and_85 (and_85_out, and_104_out, S2);
  and and_86 (and_86_out, not_3_out, and_87_out);
  and and_87 (and_87_out, and_88_out, not_5_out);
  and and_88 (and_88_out, not_6_out, _0_5);
  and and_89 (and_89_out, not_8_out, and_105_out);
  and and_90 (and_90_out, not_8_out, and_106_out);
  and and_91 (and_91_out, not_8_out, and_107_out);
  and and_92 (and_92_out, not_8_out, and_108_out);
  and and_93 (and_93_out, not_8_out, and_109_out);
  and and_94 (and_94_out, not_8_out, and_110_out);
  and and_95 (and_95_out, not_8_out, and_111_out);
  and and_96 (and_96_out, not_8_out, and_112_out);
  and and_97 (and_97_out, not_8_out, and_113_out);
  and and_98 (and_98_out, not_8_out, and_114_out);
  and and_99 (and_99_out, not_8_out, and_115_out);
  and and_100 (and_100_out, not_8_out, and_116_out);
  and and_101 (and_101_out, not_8_out, and_117_out);
  and and_102 (and_102_out, not_8_out, and_118_out);
  and and_103 (and_103_out, not_8_out, and_119_out);
  and and_104 (and_104_out, not_8_out, and_120_out);
  and and_105 (and_105_out, _0_2, not_7_out);
  and and_106 (and_106_out, _1_2, not_7_out);
  and and_107 (and_107_out, _2_2, not_7_out);
  and and_108 (and_108_out, _3_2, not_7_out);
  and and_109 (and_109_out, _4_2, not_7_out);
  and and_110 (and_110_out, _5_2, not_7_out);
  and and_111 (and_111_out, _6_2, not_7_out);
  and and_112 (and_112_out, _7_2, not_7_out);
  not not_7 (not_7_out, S0);
  and and_113 (and_113_out, _0_4, S0);
  and and_114 (and_114_out, _1_4, S0);
  and and_115 (and_115_out, _2_4, S0);
  and and_116 (and_116_out, _3_4, S0);
  and and_117 (and_117_out, _4_4, S0);
  and and_118 (and_118_out, _5_4, S0);
  and and_119 (and_119_out, _6_4, S0);
  and and_120 (and_120_out, _7_4, S0);
  not not_8 (not_8_out, S1);
endmodule

// Equator
module _2_bit_Equator (
  input  B1,
  input  B0,
  input  Active,
  input  A0,
  input  A1,
  output Equal
);

  wire n1_bit_equator_1_x, n1_bit_equator_2_x;

  _1_bit_Equator u_1_bit_equator_1 (._1(A0), ._0(B0), .Active(Active), .X(n1_bit_equator_1_x));
  _1_bit_Equator u_1_bit_equator_2 (._1(A1), ._0(B1), .Active(Active), .X(n1_bit_equator_2_x));
  and and_1 (Equal, n1_bit_equator_1_x, n1_bit_equator_2_x);
endmodule

module Control_Panel (
  input  Pregram_Reset,
  input  Write_Byte,
  input  Enable_Program_Write,
  input  Reset,
  input  Tick,
  input  Enable_Auto_Clock,
  input  One_by_One,
  input  Next_Instruction,
  output Program_Reset_Out,
  output Write_Next_Byte,
  output Enable_Write,
  output Reset_Out,
  output System_Clock,
  output Clock,
  output One_by_One_2,
  output Next_Instruction_2
);

  wire or_1_out, or_2_out, or_3_out;

  and and_1 (Write_Next_Byte, or_3_out, Enable_Program_Write);
  or or_1 (or_1_out, System_Clock, Tick);
  and and_2 (Clock, or_1_out, or_2_out);
  or or_2 (or_2_out, Tick, Enable_Auto_Clock);
  or or_3 (or_3_out, System_Clock, Write_Byte);
  Clock clock_1 (.out(System_Clock));

  assign Enable_Write = Enable_Program_Write;
  assign Next_Instruction_2 = Next_Instruction;
  assign One_by_One_2 = One_by_One;
  assign Program_Reset_Out = Pregram_Reset;
  assign Reset_Out = Reset;
endmodule

// Buffer
module Controlled_Buffer (
  input  Control,
  input  A7,
  input  A6,
  input  A5,
  input  A4,
  input  A3,
  input  A2,
  input  A1,
  input  A0,
  output X7,
  output X6,
  output X5,
  output X4,
  output X3,
  output X2,
  output X1,
  output X0
);

  and and_1 (X7, Control, A7);
  and and_2 (X5, Control, A5);
  and and_3 (X6, Control, A6);
  and and_4 (X4, Control, A4);
  and and_5 (X3, Control, A3);
  and and_6 (X2, Control, A2);
  and and_7 (X1, Control, A1);
  and and_8 (X0, Control, A0);
endmodule

module Condition_Code_Register (
  input  Clear_Finished,
  input  Clear_Wait,
  input  Clock,
  input  Not_Equal,
  input  B_Greater_A,
  input  A_Greater_B,
  input  Overflow,
  input  Zero,
  input  Negative,
  input  Waiting,
  input  Finished,
  output Not_Equal_2,
  output B_Greater_A_2,
  output A_Greater_B_2,
  output Overflow_2,
  output Zero_2,
  output Negative_2,
  output Waiting_2,
  output Finished_2
);

  D_Latch d_latch_1 (.Clock(Clock), .Data(Not_Equal), .Out(Not_Equal_2));
  D_Latch d_latch_2 (.Clock(Clock), .Data(B_Greater_A), .Out(B_Greater_A_2));
  D_Latch d_latch_3 (.Clock(Clock), .Data(A_Greater_B), .Out(A_Greater_B_2));
  D_Latch d_latch_4 (.Clock(Clock), .Data(Overflow), .Out(Overflow_2));
  D_Latch d_latch_5 (.Clock(Clock), .Data(Zero), .Out(Zero_2));
  D_Latch d_latch_6 (.Clock(Clock), .Data(Negative), .Out(Negative_2));
  D_Flip_Flop d_ff_1 (.clk(Clock), .D(Waiting), .Q(Waiting_2), .reset(Clear_Wait));  // open: Qn, preset, en
  D_Flip_Flop d_ff_2 (.clk(Clock), .D(Finished), .Q(Finished_2), .reset(Clear_Finished));  // open: Qn, preset, en
endmodule

module _8_bit_Multiplier (
  input  A0,
  input  A1,
  input  A2,
  input  A3,
  input  A4,
  input  A5,
  input  A6,
  input  A7,
  input  B7,
  input  B6,
  input  B5,
  input  B4,
  input  B3,
  input  B2,
  input  B1,
  input  B0,
  output X0,
  output X1,
  output X2,
  output X3,
  output X4,
  output X5,
  output X6,
  output X7,
  output Overflow
);

  wire n8_bit_adder_1_carry_out, n8_bit_adder_1_x0, n8_bit_adder_1_x1, n8_bit_adder_1_x2, n8_bit_adder_1_x3,
       n8_bit_adder_1_x4, n8_bit_adder_1_x5, n8_bit_adder_1_x6, n8_bit_adder_1_x7, n8_bit_adder_2_carry_out,
       n8_bit_adder_2_x0, n8_bit_adder_2_x1, n8_bit_adder_2_x2, n8_bit_adder_2_x3, n8_bit_adder_2_x4,
       n8_bit_adder_2_x5, n8_bit_adder_2_x6, n8_bit_adder_2_x7, n8_bit_adder_3_carry_out, n8_bit_adder_3_x0,
       n8_bit_adder_3_x1, n8_bit_adder_3_x2, n8_bit_adder_3_x3, n8_bit_adder_3_x4, n8_bit_adder_3_x5,
       n8_bit_adder_3_x6, n8_bit_adder_3_x7, n8_bit_adder_4_carry_out, n8_bit_adder_4_x0, n8_bit_adder_4_x1,
       n8_bit_adder_4_x2, n8_bit_adder_4_x3, n8_bit_adder_4_x4, n8_bit_adder_4_x5, n8_bit_adder_4_x6,
       n8_bit_adder_4_x7, n8_bit_adder_5_carry_out, n8_bit_adder_5_x0, n8_bit_adder_5_x1, n8_bit_adder_5_x2,
       n8_bit_adder_5_x3, n8_bit_adder_5_x4, n8_bit_adder_5_x5, n8_bit_adder_5_x6, n8_bit_adder_5_x7,
       n8_bit_adder_6_carry_out, n8_bit_adder_6_x0, n8_bit_adder_6_x1, n8_bit_adder_6_x2, n8_bit_adder_6_x3,
       n8_bit_adder_6_x4, n8_bit_adder_6_x5, n8_bit_adder_6_x6, n8_bit_adder_6_x7, n8_bit_adder_7_carry_out,
       n8_bit_adder_7_x0, n8_bit_adder_7_x1, n8_bit_adder_7_x2, n8_bit_adder_7_x3, n8_bit_adder_7_x4,
       n8_bit_adder_7_x5, n8_bit_adder_7_x6, n8_bit_adder_7_x7, n8_bit_adder_8_carry_out,
       n8_bit_control_1__0_2, n8_bit_control_1__1_2, n8_bit_control_1__2_2, n8_bit_control_1__3_2,
       n8_bit_control_1__4_2, n8_bit_control_1__5_2, n8_bit_control_1__6_2, n8_bit_control_1__7_2,
       n8_bit_control_2__0_2, n8_bit_control_2__1_2, n8_bit_control_2__2_2, n8_bit_control_2__3_2,
       n8_bit_control_2__4_2, n8_bit_control_2__5_2, n8_bit_control_2__6_2, n8_bit_control_2__7_2,
       n8_bit_control_3__0_2, n8_bit_control_3__1_2, n8_bit_control_3__2_2, n8_bit_control_3__3_2,
       n8_bit_control_3__4_2, n8_bit_control_3__5_2, n8_bit_control_3__6_2, n8_bit_control_3__7_2,
       n8_bit_control_4__0_2, n8_bit_control_4__1_2, n8_bit_control_4__2_2, n8_bit_control_4__3_2,
       n8_bit_control_4__4_2, n8_bit_control_4__5_2, n8_bit_control_4__6_2, n8_bit_control_4__7_2,
       n8_bit_control_5__0_2, n8_bit_control_5__1_2, n8_bit_control_5__2_2, n8_bit_control_5__3_2,
       n8_bit_control_5__4_2, n8_bit_control_5__5_2, n8_bit_control_5__6_2, n8_bit_control_5__7_2,
       n8_bit_control_6__0_2, n8_bit_control_6__1_2, n8_bit_control_6__2_2, n8_bit_control_6__3_2,
       n8_bit_control_6__4_2, n8_bit_control_6__5_2, n8_bit_control_6__6_2, n8_bit_control_6__7_2,
       n8_bit_control_7__0_2, n8_bit_control_7__1_2, n8_bit_control_7__2_2, n8_bit_control_7__3_2,
       n8_bit_control_7__4_2, n8_bit_control_7__5_2, n8_bit_control_7__6_2, n8_bit_control_7__7_2,
       n8_bit_control_8__0_2, n8_bit_control_8__1_2, n8_bit_control_8__2_2, n8_bit_control_8__3_2,
       n8_bit_control_8__4_2, n8_bit_control_8__5_2, n8_bit_control_8__6_2, n8_bit_control_8__7_2, or_1_out,
       or_2_out, or_3_out, or_4_out, or_5_out, or_6_out, or_7_out, or_8_out, or_9_out, or_10_out, or_11_out,
       or_12_out, or_13_out, or_14_out, or_15_out, or_16_out, or_17_out, or_18_out, or_19_out, or_20_out,
       or_21_out, or_22_out, or_23_out, or_24_out, or_25_out, or_26_out, or_27_out, or_28_out, or_29_out,
       or_30_out, or_31_out, or_32_out, or_33_out, or_34_out;

  or or_1 (or_1_out, or_2_out, n8_bit_control_1__4_2);
  or or_2 (or_2_out, or_3_out, n8_bit_control_1__5_2);
  or or_3 (or_3_out, n8_bit_control_1__7_2, n8_bit_control_1__6_2);
  _8_bit_Control u_8_bit_control_1 (
    .Control(B7), ._0_2(n8_bit_control_1__0_2), ._1_2(n8_bit_control_1__1_2), ._2_2(n8_bit_control_1__2_2),
    ._3_2(n8_bit_control_1__3_2), ._4_2(n8_bit_control_1__4_2), ._5_2(n8_bit_control_1__5_2),
    ._6_2(n8_bit_control_1__6_2), ._7_2(n8_bit_control_1__7_2), ._7(A7), ._6(A6), ._5(A5), ._4(A4), ._3(A3),
    ._2(A2), ._1(A1), ._0(A0));
  _8_bit_Adder u_8_bit_adder_1 (
    .A0(1'b0), .B0(1'b0), .A1(1'b0), .B1(1'b0), .A2(1'b0), .B2(1'b0), .A3(1'b0), .B3(1'b0), .A4(1'b0),
    .B4(1'b0), .A5(1'b0), .B5(1'b0), .A6(1'b0), .B6(1'b0), .A7(1'b0), .B7(n8_bit_control_1__0_2),
    .X0(n8_bit_adder_1_x0), .X1(n8_bit_adder_1_x1), .X2(n8_bit_adder_1_x2), .X3(n8_bit_adder_1_x3),
    .X4(n8_bit_adder_1_x4), .X5(n8_bit_adder_1_x5), .X6(n8_bit_adder_1_x6), .X7(n8_bit_adder_1_x7),
    .Increment(1'b0), .Carry_Out(n8_bit_adder_1_carry_out));
  or or_4 (or_4_out, or_5_out, n8_bit_control_1__1_2);
  or or_5 (or_5_out, or_6_out, n8_bit_control_1__2_2);
  or or_6 (or_6_out, or_1_out, n8_bit_control_1__3_2);
  or or_7 (or_7_out, n8_bit_adder_1_carry_out, or_8_out);
  or or_8 (or_8_out, or_4_out, or_9_out);
  or or_9 (or_9_out, or_10_out, n8_bit_control_2__2_2);
  or or_10 (or_10_out, or_11_out, n8_bit_control_2__3_2);
  or or_11 (or_11_out, or_12_out, n8_bit_control_2__4_2);
  or or_12 (or_12_out, or_13_out, n8_bit_control_2__5_2);
  or or_13 (or_13_out, n8_bit_control_2__7_2, n8_bit_control_2__6_2);
  _8_bit_Control u_8_bit_control_2 (
    .Control(B6), ._0_2(n8_bit_control_2__0_2), ._1_2(n8_bit_control_2__1_2), ._2_2(n8_bit_control_2__2_2),
    ._3_2(n8_bit_control_2__3_2), ._4_2(n8_bit_control_2__4_2), ._5_2(n8_bit_control_2__5_2),
    ._6_2(n8_bit_control_2__6_2), ._7_2(n8_bit_control_2__7_2), ._7(A7), ._6(A6), ._5(A5), ._4(A4), ._3(A3),
    ._2(A2), ._1(A1), ._0(A0));
  _8_bit_Adder u_8_bit_adder_2 (
    .A0(n8_bit_adder_1_x0), .B0(1'b0), .A1(n8_bit_adder_1_x1), .B1(1'b0), .A2(n8_bit_adder_1_x2), .B2(1'b0),
    .A3(n8_bit_adder_1_x3), .B3(1'b0), .A4(n8_bit_adder_1_x4), .B4(1'b0), .A5(n8_bit_adder_1_x5), .B5(1'b0),
    .A6(n8_bit_adder_1_x6), .B6(n8_bit_control_2__0_2), .A7(n8_bit_adder_1_x7), .B7(n8_bit_control_2__1_2),
    .X0(n8_bit_adder_2_x0), .X1(n8_bit_adder_2_x1), .X2(n8_bit_adder_2_x2), .X3(n8_bit_adder_2_x3),
    .X4(n8_bit_adder_2_x4), .X5(n8_bit_adder_2_x5), .X6(n8_bit_adder_2_x6), .X7(n8_bit_adder_2_x7),
    .Increment(1'b0), .Carry_Out(n8_bit_adder_2_carry_out));
  or or_14 (or_14_out, or_7_out, or_17_out);
  or or_15 (or_15_out, n8_bit_control_3__7_2, n8_bit_control_3__6_2);
  _8_bit_Control u_8_bit_control_3 (
    .Control(B5), ._0_2(n8_bit_control_3__0_2), ._1_2(n8_bit_control_3__1_2), ._2_2(n8_bit_control_3__2_2),
    ._3_2(n8_bit_control_3__3_2), ._4_2(n8_bit_control_3__4_2), ._5_2(n8_bit_control_3__5_2),
    ._6_2(n8_bit_control_3__6_2), ._7_2(n8_bit_control_3__7_2), ._7(A7), ._6(A6), ._5(A5), ._4(A4), ._3(A3),
    ._2(A2), ._1(A1), ._0(A0));
  _8_bit_Adder u_8_bit_adder_3 (
    .A0(n8_bit_adder_2_x0), .B0(1'b0), .A1(n8_bit_adder_2_x1), .B1(1'b0), .A2(n8_bit_adder_2_x2), .B2(1'b0),
    .A3(n8_bit_adder_2_x3), .B3(1'b0), .A4(n8_bit_adder_2_x4), .B4(1'b0), .A5(n8_bit_adder_2_x5),
    .B5(n8_bit_control_3__0_2), .A6(n8_bit_adder_2_x6), .B6(n8_bit_control_3__1_2), .A7(n8_bit_adder_2_x7),
    .B7(n8_bit_control_3__2_2), .X0(n8_bit_adder_3_x0), .X1(n8_bit_adder_3_x1), .X2(n8_bit_adder_3_x2),
    .X3(n8_bit_adder_3_x3), .X4(n8_bit_adder_3_x4), .X5(n8_bit_adder_3_x5), .X6(n8_bit_adder_3_x6),
    .X7(n8_bit_adder_3_x7), .Increment(1'b0), .Carry_Out(n8_bit_adder_3_carry_out));
  or or_16 (or_16_out, n8_bit_adder_2_carry_out, or_14_out);
  or or_17 (or_17_out, or_18_out, n8_bit_control_3__3_2);
  or or_18 (or_18_out, or_19_out, n8_bit_control_3__4_2);
  or or_19 (or_19_out, or_15_out, n8_bit_control_3__5_2);
  or or_20 (or_20_out, n8_bit_adder_3_carry_out, or_21_out);
  or or_21 (or_21_out, or_16_out, or_22_out);
  or or_22 (or_22_out, or_23_out, n8_bit_control_4__4_2);
  or or_23 (or_23_out, or_24_out, n8_bit_control_4__5_2);
  or or_24 (or_24_out, n8_bit_control_4__7_2, n8_bit_control_4__6_2);
  _8_bit_Control u_8_bit_control_4 (
    .Control(B4), ._0_2(n8_bit_control_4__0_2), ._1_2(n8_bit_control_4__1_2), ._2_2(n8_bit_control_4__2_2),
    ._3_2(n8_bit_control_4__3_2), ._4_2(n8_bit_control_4__4_2), ._5_2(n8_bit_control_4__5_2),
    ._6_2(n8_bit_control_4__6_2), ._7_2(n8_bit_control_4__7_2), ._7(A7), ._6(A6), ._5(A5), ._4(A4), ._3(A3),
    ._2(A2), ._1(A1), ._0(A0));
  _8_bit_Adder u_8_bit_adder_4 (
    .A0(n8_bit_adder_3_x0), .B0(1'b0), .A1(n8_bit_adder_3_x1), .B1(1'b0), .A2(n8_bit_adder_3_x2), .B2(1'b0),
    .A3(n8_bit_adder_3_x3), .B3(1'b0), .A4(n8_bit_adder_3_x4), .B4(n8_bit_control_4__0_2),
    .A5(n8_bit_adder_3_x5), .B5(n8_bit_control_4__1_2), .A6(n8_bit_adder_3_x6), .B6(n8_bit_control_4__2_2),
    .A7(n8_bit_adder_3_x7), .B7(n8_bit_control_4__3_2), .X0(n8_bit_adder_4_x0), .X1(n8_bit_adder_4_x1),
    .X2(n8_bit_adder_4_x2), .X3(n8_bit_adder_4_x3), .X4(n8_bit_adder_4_x4), .X5(n8_bit_adder_4_x5),
    .X6(n8_bit_adder_4_x6), .X7(n8_bit_adder_4_x7), .Increment(1'b0), .Carry_Out(n8_bit_adder_4_carry_out));
  or or_25 (or_25_out, or_20_out, or_27_out);
  _8_bit_Adder u_8_bit_adder_5 (
    .A0(n8_bit_adder_4_x0), .B0(1'b0), .A1(n8_bit_adder_4_x1), .B1(1'b0), .A2(n8_bit_adder_4_x2), .B2(1'b0),
    .A3(n8_bit_adder_4_x3), .B3(n8_bit_control_5__0_2), .A4(n8_bit_adder_4_x4), .B4(n8_bit_control_5__1_2),
    .A5(n8_bit_adder_4_x5), .B5(n8_bit_control_5__2_2), .A6(n8_bit_adder_4_x6), .B6(n8_bit_control_5__3_2),
    .A7(n8_bit_adder_4_x7), .B7(n8_bit_control_5__4_2), .X0(n8_bit_adder_5_x0), .X1(n8_bit_adder_5_x1),
    .X2(n8_bit_adder_5_x2), .X3(n8_bit_adder_5_x3), .X4(n8_bit_adder_5_x4), .X5(n8_bit_adder_5_x5),
    .X6(n8_bit_adder_5_x6), .X7(n8_bit_adder_5_x7), .Increment(1'b0), .Carry_Out(n8_bit_adder_5_carry_out));
  or or_26 (or_26_out, n8_bit_adder_4_carry_out, or_25_out);
  or or_27 (or_27_out, or_28_out, n8_bit_control_5__5_2);
  or or_28 (or_28_out, n8_bit_control_5__7_2, n8_bit_control_5__6_2);
  _8_bit_Control u_8_bit_control_5 (
    .Control(B3), ._0_2(n8_bit_control_5__0_2), ._1_2(n8_bit_control_5__1_2), ._2_2(n8_bit_control_5__2_2),
    ._3_2(n8_bit_control_5__3_2), ._4_2(n8_bit_control_5__4_2), ._5_2(n8_bit_control_5__5_2),
    ._6_2(n8_bit_control_5__6_2), ._7_2(n8_bit_control_5__7_2), ._7(A7), ._6(A6), ._5(A5), ._4(A4), ._3(A3),
    ._2(A2), ._1(A1), ._0(A0));
  or or_29 (or_29_out, n8_bit_adder_5_carry_out, or_30_out);
  or or_30 (or_30_out, or_26_out, or_31_out);
  or or_31 (or_31_out, n8_bit_control_6__7_2, n8_bit_control_6__6_2);
  _8_bit_Control u_8_bit_control_6 (
    .Control(B2), ._0_2(n8_bit_control_6__0_2), ._1_2(n8_bit_control_6__1_2), ._2_2(n8_bit_control_6__2_2),
    ._3_2(n8_bit_control_6__3_2), ._4_2(n8_bit_control_6__4_2), ._5_2(n8_bit_control_6__5_2),
    ._6_2(n8_bit_control_6__6_2), ._7_2(n8_bit_control_6__7_2), ._7(A7), ._6(A6), ._5(A5), ._4(A4), ._3(A3),
    ._2(A2), ._1(A1), ._0(A0));
  _8_bit_Adder u_8_bit_adder_6 (
    .A0(n8_bit_adder_5_x0), .B0(1'b0), .A1(n8_bit_adder_5_x1), .B1(1'b0), .A2(n8_bit_adder_5_x2),
    .B2(n8_bit_control_6__0_2), .A3(n8_bit_adder_5_x3), .B3(n8_bit_control_6__1_2), .A4(n8_bit_adder_5_x4),
    .B4(n8_bit_control_6__2_2), .A5(n8_bit_adder_5_x5), .B5(n8_bit_control_6__3_2), .A6(n8_bit_adder_5_x6),
    .B6(n8_bit_control_6__4_2), .A7(n8_bit_adder_5_x7), .B7(n8_bit_control_6__5_2), .X0(n8_bit_adder_6_x0),
    .X1(n8_bit_adder_6_x1), .X2(n8_bit_adder_6_x2), .X3(n8_bit_adder_6_x3), .X4(n8_bit_adder_6_x4),
    .X5(n8_bit_adder_6_x5), .X6(n8_bit_adder_6_x6), .X7(n8_bit_adder_6_x7), .Increment(1'b0),
    .Carry_Out(n8_bit_adder_6_carry_out));
  or or_32 (or_32_out, or_29_out, n8_bit_control_7__7_2);
  _8_bit_Adder u_8_bit_adder_7 (
    .A0(n8_bit_adder_6_x0), .B0(1'b0), .A1(n8_bit_adder_6_x1), .B1(n8_bit_control_7__0_2),
    .A2(n8_bit_adder_6_x2), .B2(n8_bit_control_7__1_2), .A3(n8_bit_adder_6_x3), .B3(n8_bit_control_7__2_2),
    .A4(n8_bit_adder_6_x4), .B4(n8_bit_control_7__3_2), .A5(n8_bit_adder_6_x5), .B5(n8_bit_control_7__4_2),
    .A6(n8_bit_adder_6_x6), .B6(n8_bit_control_7__5_2), .A7(n8_bit_adder_6_x7), .B7(n8_bit_control_7__6_2),
    .X0(n8_bit_adder_7_x0), .X1(n8_bit_adder_7_x1), .X2(n8_bit_adder_7_x2), .X3(n8_bit_adder_7_x3),
    .X4(n8_bit_adder_7_x4), .X5(n8_bit_adder_7_x5), .X6(n8_bit_adder_7_x6), .X7(n8_bit_adder_7_x7),
    .Increment(1'b0), .Carry_Out(n8_bit_adder_7_carry_out));
  or or_33 (or_33_out, n8_bit_adder_6_carry_out, or_32_out);
  _8_bit_Control u_8_bit_control_7 (
    .Control(B1), ._0_2(n8_bit_control_7__0_2), ._1_2(n8_bit_control_7__1_2), ._2_2(n8_bit_control_7__2_2),
    ._3_2(n8_bit_control_7__3_2), ._4_2(n8_bit_control_7__4_2), ._5_2(n8_bit_control_7__5_2),
    ._6_2(n8_bit_control_7__6_2), ._7_2(n8_bit_control_7__7_2), ._7(A7), ._6(A6), ._5(A5), ._4(A4), ._3(A3),
    ._2(A2), ._1(A1), ._0(A0));
  or or_34 (or_34_out, n8_bit_adder_7_carry_out, or_33_out);
  _8_bit_Control u_8_bit_control_8 (
    .Control(B0), ._0_2(n8_bit_control_8__0_2), ._1_2(n8_bit_control_8__1_2), ._2_2(n8_bit_control_8__2_2),
    ._3_2(n8_bit_control_8__3_2), ._4_2(n8_bit_control_8__4_2), ._5_2(n8_bit_control_8__5_2),
    ._6_2(n8_bit_control_8__6_2), ._7_2(n8_bit_control_8__7_2), ._7(A7), ._6(A6), ._5(A5), ._4(A4), ._3(A3),
    ._2(A2), ._1(A1), ._0(A0));
  _8_bit_Adder u_8_bit_adder_8 (
    .A0(n8_bit_adder_7_x0), .B0(n8_bit_control_8__0_2), .A1(n8_bit_adder_7_x1), .B1(n8_bit_control_8__1_2),
    .A2(n8_bit_adder_7_x2), .B2(n8_bit_control_8__2_2), .A3(n8_bit_adder_7_x3), .B3(n8_bit_control_8__3_2),
    .A4(n8_bit_adder_7_x4), .B4(n8_bit_control_8__4_2), .A5(n8_bit_adder_7_x5), .B5(n8_bit_control_8__5_2),
    .A6(n8_bit_adder_7_x6), .B6(n8_bit_control_8__6_2), .A7(n8_bit_adder_7_x7), .B7(n8_bit_control_8__7_2),
    .X0(X0), .X1(X1), .X2(X2), .X3(X3), .X4(X4), .X5(X5), .X6(X6), .X7(X7), .Increment(1'b0),
    .Carry_Out(n8_bit_adder_8_carry_out));
  or or_35 (Overflow, n8_bit_adder_8_carry_out, or_34_out);
endmodule

module _8_bit_Control (
  input  Control,
  input  _7,
  input  _6,
  input  _5,
  input  _4,
  input  _3,
  input  _2,
  input  _1,
  input  _0,
  output _7_2,
  output _6_2,
  output _5_2,
  output _4_2,
  output _3_2,
  output _2_2,
  output _1_2,
  output _0_2
);

  and and_1 (_5_2, Control, _5);
  and and_2 (_6_2, Control, _6);
  and and_3 (_7_2, Control, _7);
  and and_4 (_4_2, Control, _4);
  and and_5 (_3_2, Control, _3);
  and and_6 (_0_2, Control, _0);
  and and_7 (_2_2, Control, _2);
  and and_8 (_1_2, Control, _1);
endmodule

module _15_Way_Multiplexor (
  input  S3,
  input  S2,
  input  S1,
  input  S0,
  input  A0,
  input  _1,
  input  _2,
  input  _3,
  input  _4,
  input  _5,
  input  _6,
  input  _7,
  input  B0,
  input  _1_2,
  input  _2_2,
  input  _3_2,
  input  _4_2,
  input  _5_2,
  input  _6_2,
  input  _7_2,
  input  C0,
  input  _1_3,
  input  _2_3,
  input  _3_3,
  input  _4_3,
  input  _5_3,
  input  _6_3,
  input  _7_3,
  input  D0,
  input  _1_4,
  input  _2_4,
  input  _3_4,
  input  _4_4,
  input  _5_4,
  input  _6_4,
  input  _7_4,
  input  E0,
  input  _1_5,
  input  _2_5,
  input  _3_5,
  input  _4_5,
  input  _5_5,
  input  _6_5,
  input  _7_5,
  input  F0,
  input  _1_6,
  input  _2_6,
  input  _3_6,
  input  _4_6,
  input  _5_6,
  input  _6_6,
  input  _7_6,
  input  G0,
  input  _1_7,
  input  _2_7,
  input  _3_7,
  input  _4_7,
  input  _5_7,
  input  _6_7,
  input  _7_7,
  input  H0,
  input  _1_8,
  input  _2_8,
  input  _3_8,
  input  _4_8,
  input  _5_8,
  input  _6_8,
  input  _7_8,
  input  I0,
  input  _1_9,
  input  _2_9,
  input  _3_9,
  input  _4_9,
  input  _5_9,
  input  _6_9,
  input  _7_9,
  input  J0,
  input  _1_10,
  input  _2_10,
  input  _3_10,
  input  _4_10,
  input  _5_10,
  input  _6_10,
  input  _7_10,
  input  K0,
  input  _1_11,
  input  _2_11,
  input  _3_11,
  input  _4_11,
  input  _5_11,
  input  _6_11,
  input  _7_11,
  input  L0,
  input  _1_12,
  input  _2_12,
  input  _3_12,
  input  _4_12,
  input  _5_12,
  input  _6_12,
  input  _7_12,
  input  M0,
  input  _1_13,
  input  _2_13,
  input  _3_13,
  input  _4_13,
  input  _5_13,
  input  _6_13,
  input  _7_13,
  input  N0,
  input  _1_14,
  input  _2_14,
  input  _3_14,
  input  _4_14,
  input  _5_14,
  input  _6_14,
  input  _7_14,
  input  O0,
  input  _1_15,
  input  _2_15,
  input  _3_15,
  input  _4_15,
  input  _5_15,
  input  _6_15,
  input  _7_15,
  output _7_16,
  output _6_16,
  output _5_16,
  output _4_16,
  output _3_16,
  output _2_16,
  output _1_16,
  output _0
);

  wire and_1_out, and_2_out, and_3_out, and_4_out, and_5_out, and_6_out, and_7_out, and_8_out, and_9_out,
       and_10_out, and_11_out, and_12_out, and_13_out, and_14_out, and_15_out, and_16_out, and_17_out,
       and_18_out, and_19_out, and_20_out, and_21_out, and_22_out, and_23_out, and_24_out, and_25_out,
       and_26_out, and_27_out, and_28_out, and_29_out, and_30_out, and_31_out, and_32_out, and_33_out,
       and_34_out, and_35_out, and_36_out, and_37_out, and_38_out, and_39_out, and_40_out, and_41_out,
       and_42_out, and_43_out, and_44_out, and_45_out, and_46_out, and_47_out, and_48_out, and_49_out,
       and_50_out, and_51_out, and_52_out, and_53_out, and_54_out, and_55_out, and_56_out, and_57_out,
       and_58_out, and_59_out, and_60_out, and_61_out, and_62_out, and_63_out, and_64_out, and_65_out,
       and_66_out, and_67_out, and_68_out, and_69_out, and_70_out, and_71_out, and_72_out, and_73_out,
       and_74_out, and_75_out, and_76_out, and_77_out, and_78_out, and_79_out, and_80_out, and_81_out,
       and_82_out, and_83_out, and_84_out, and_85_out, and_86_out, and_87_out, and_88_out, and_89_out,
       and_90_out, and_91_out, and_92_out, and_93_out, and_94_out, and_95_out, and_96_out, and_97_out,
       and_98_out, and_99_out, and_100_out, and_101_out, and_102_out, and_103_out, and_104_out, and_105_out,
       and_106_out, and_107_out, and_108_out, and_109_out, and_110_out, and_111_out, and_112_out,
       and_113_out, and_114_out, and_115_out, and_116_out, and_117_out, and_118_out, and_119_out,
       and_120_out, and_121_out, and_122_out, and_123_out, and_124_out, and_125_out, and_126_out,
       and_127_out, and_128_out, and_129_out, and_130_out, and_131_out, and_132_out, and_133_out,
       and_134_out, and_135_out, and_136_out, and_137_out, and_138_out, and_139_out, and_140_out,
       and_141_out, and_142_out, and_143_out, and_144_out, and_145_out, and_146_out, and_147_out,
       and_148_out, and_149_out, and_150_out, and_151_out, and_152_out, and_153_out, and_154_out,
       and_155_out, and_156_out, and_157_out, and_158_out, and_159_out, and_160_out, and_161_out,
       and_162_out, and_163_out, and_164_out, and_165_out, and_166_out, and_167_out, and_168_out,
       and_169_out, and_170_out, and_171_out, and_172_out, and_173_out, and_174_out, and_175_out,
       and_176_out, and_177_out, and_178_out, and_179_out, and_180_out, and_181_out, and_182_out,
       and_183_out, and_184_out, and_185_out, and_186_out, and_187_out, and_188_out, and_189_out,
       and_190_out, and_191_out, and_192_out, and_193_out, and_194_out, and_195_out, and_196_out,
       and_197_out, and_198_out, and_199_out, and_200_out, and_201_out, and_202_out, and_203_out,
       and_204_out, and_205_out, and_206_out, and_207_out, and_208_out, and_209_out, and_210_out,
       and_211_out, and_212_out, and_213_out, and_214_out, and_215_out, and_216_out, and_217_out,
       and_218_out, and_219_out, and_220_out, and_221_out, and_222_out, and_223_out, and_224_out,
       and_225_out, and_226_out, and_227_out, and_228_out, and_229_out, and_230_out, and_231_out,
       and_232_out, and_233_out, and_234_out, and_235_out, and_236_out, and_237_out, and_238_out,
       and_239_out, and_240_out, and_241_out, and_242_out, and_243_out, and_244_out, and_245_out,
       and_246_out, and_247_out, and_248_out, and_249_out, and_250_out, and_251_out, and_252_out,
       and_253_out, and_254_out, and_255_out, and_256_out, and_257_out, and_258_out, and_259_out,
       and_260_out, and_261_out, and_262_out, and_263_out, and_264_out, and_265_out, and_266_out,
       and_267_out, and_268_out, and_269_out, and_270_out, and_271_out, and_272_out, and_273_out,
       and_274_out, and_275_out, and_276_out, and_277_out, and_278_out, and_279_out, and_280_out,
       and_281_out, and_282_out, and_283_out, and_284_out, and_285_out, and_286_out, and_287_out,
       and_288_out, and_289_out, and_290_out, and_291_out, and_292_out, and_293_out, and_294_out,
       and_295_out, and_296_out, and_297_out, and_298_out, and_299_out, and_300_out, and_301_out,
       and_302_out, and_303_out, and_304_out, and_305_out, and_306_out, and_307_out, and_308_out,
       and_309_out, and_310_out, and_311_out, and_312_out, and_313_out, and_314_out, and_315_out,
       and_316_out, and_317_out, and_318_out, and_319_out, and_320_out, and_321_out, and_322_out,
       and_323_out, and_324_out, and_325_out, and_326_out, and_327_out, and_328_out, and_329_out,
       and_330_out, and_331_out, and_332_out, and_333_out, and_334_out, and_335_out, and_336_out,
       and_337_out, and_338_out, and_339_out, and_340_out, and_341_out, and_342_out, and_343_out,
       and_344_out, and_345_out, and_346_out, and_347_out, and_348_out, and_349_out, and_350_out,
       and_351_out, and_352_out, and_353_out, and_354_out, and_355_out, and_356_out, and_357_out,
       and_358_out, and_359_out, and_360_out, and_361_out, and_362_out, and_363_out, and_364_out,
       and_365_out, and_366_out, and_367_out, and_368_out, and_369_out, and_370_out, and_371_out,
       and_372_out, and_373_out, and_374_out, and_375_out, and_376_out, and_377_out, and_378_out,
       and_379_out, and_380_out, and_381_out, and_382_out, and_383_out, and_384_out, and_385_out,
       and_386_out, and_387_out, and_388_out, and_389_out, and_390_out, and_391_out, and_392_out,
       and_393_out, and_394_out, and_395_out, and_396_out, and_397_out, and_398_out, and_399_out,
       and_400_out, and_401_out, and_402_out, and_403_out, and_404_out, and_405_out, and_406_out,
       and_407_out, and_408_out, and_409_out, and_410_out, and_411_out, and_412_out, and_413_out,
       and_414_out, and_415_out, and_416_out, and_417_out, and_418_out, and_419_out, and_420_out,
       and_421_out, and_422_out, and_423_out, and_424_out, and_425_out, and_426_out, and_427_out,
       and_428_out, and_429_out, and_430_out, and_431_out, and_432_out, and_433_out, and_434_out,
       and_435_out, and_436_out, and_437_out, and_438_out, and_439_out, and_440_out, and_441_out,
       and_442_out, and_443_out, and_444_out, and_445_out, and_446_out, and_447_out, and_448_out,
       and_449_out, and_450_out, and_451_out, and_452_out, and_453_out, and_454_out, and_455_out,
       and_456_out, and_457_out, and_458_out, and_459_out, and_460_out, and_461_out, and_462_out,
       and_463_out, and_464_out, and_465_out, and_466_out, and_467_out, and_468_out, and_469_out,
       and_470_out, and_471_out, and_472_out, and_473_out, and_474_out, and_475_out, and_476_out,
       and_477_out, and_478_out, and_479_out, and_480_out, not_1_out, not_2_out, not_3_out, not_4_out,
       not_5_out, not_6_out, not_7_out, not_8_out, not_9_out, not_10_out, not_11_out, not_12_out, not_13_out,
       not_14_out, not_15_out, not_16_out, not_17_out, not_18_out, not_19_out, not_20_out, not_21_out,
       not_22_out, not_23_out, not_24_out, not_25_out, not_26_out, not_27_out, not_28_out, or_5_out,
       or_6_out, or_7_out, or_8_out, or_9_out, or_10_out, or_11_out, or_12_out, or_13_out, or_14_out,
       or_15_out, or_16_out, or_17_out, or_18_out, or_19_out, or_20_out, or_21_out, or_22_out, or_23_out,
       or_24_out, or_25_out, or_26_out, or_27_out, or_28_out, or_29_out, or_30_out, or_31_out, or_32_out,
       or_33_out, or_34_out, or_35_out, or_36_out, or_37_out, or_38_out, or_39_out, or_40_out, or_41_out,
       or_42_out, or_43_out, or_44_out, or_45_out, or_46_out, or_47_out, or_48_out, or_49_out, or_50_out,
       or_51_out, or_52_out, or_53_out, or_54_out, or_55_out, or_56_out, or_61_out, or_62_out, or_63_out,
       or_64_out, or_65_out, or_66_out, or_67_out, or_68_out, or_69_out, or_70_out, or_71_out, or_72_out,
       or_73_out, or_74_out, or_75_out, or_76_out, or_77_out, or_78_out, or_79_out, or_80_out, or_81_out,
       or_82_out, or_83_out, or_84_out, or_85_out, or_86_out, or_87_out, or_88_out, or_89_out, or_90_out,
       or_91_out, or_92_out, or_93_out, or_94_out, or_95_out, or_96_out, or_97_out, or_98_out, or_99_out,
       or_100_out, or_101_out, or_102_out, or_103_out, or_104_out, or_105_out, or_106_out, or_107_out,
       or_108_out, or_109_out, or_110_out, or_111_out, or_112_out;

  not not_1 (not_1_out, S3);
  and and_1 (and_1_out, A0, not_1_out);
  and and_2 (and_2_out, _1, not_1_out);
  and and_3 (and_3_out, _2, not_1_out);
  and and_4 (and_4_out, _3, not_1_out);
  and and_5 (and_5_out, _4, not_1_out);
  and and_6 (and_6_out, _5, not_1_out);
  and and_7 (and_7_out, _6, not_1_out);
  and and_8 (and_8_out, _7, not_1_out);
  and and_9 (and_9_out, B0, not_1_out);
  and and_10 (and_10_out, _1_2, not_1_out);
  and and_11 (and_11_out, _2_2, not_1_out);
  and and_12 (and_12_out, _3_2, not_1_out);
  and and_13 (and_13_out, _4_2, not_1_out);
  and and_14 (and_14_out, _5_2, not_1_out);
  and and_15 (and_15_out, _6_2, not_1_out);
  and and_16 (and_16_out, _7_2, not_1_out);
  and and_17 (and_17_out, C0, not_1_out);
  and and_18 (and_18_out, _1_3, not_1_out);
  and and_19 (and_19_out, _2_3, not_1_out);
  and and_20 (and_20_out, _3_3, not_1_out);
  and and_21 (and_21_out, _4_3, not_1_out);
  and and_22 (and_22_out, _5_3, not_1_out);
  and and_23 (and_23_out, _6_3, not_1_out);
  and and_24 (and_24_out, _7_3, not_1_out);
  and and_25 (and_25_out, D0, not_1_out);
  and and_26 (and_26_out, _1_4, not_1_out);
  and and_27 (and_27_out, _2_4, not_1_out);
  and and_28 (and_28_out, _3_4, not_1_out);
  and and_29 (and_29_out, _4_4, not_1_out);
  and and_30 (and_30_out, _5_4, not_1_out);
  and and_31 (and_31_out, _6_4, not_1_out);
  and and_32 (and_32_out, _7_4, not_1_out);
  and and_33 (and_33_out, E0, not_1_out);
  and and_34 (and_34_out, _1_5, not_1_out);
  and and_35 (and_35_out, _2_5, not_1_out);
  and and_36 (and_36_out, _3_5, not_1_out);
  and and_37 (and_37_out, _4_5, not_1_out);
  and and_38 (and_38_out, _5_5, not_1_out);
  and and_39 (and_39_out, _6_5, not_1_out);
  and and_40 (and_40_out, _7_5, not_1_out);
  and and_41 (and_41_out, F0, not_1_out);
  and and_42 (and_42_out, _1_6, not_1_out);
  and and_43 (and_43_out, _2_6, not_1_out);
  and and_44 (and_44_out, _3_6, not_1_out);
  and and_45 (and_45_out, _4_6, not_1_out);
  and and_46 (and_46_out, _5_6, not_1_out);
  and and_47 (and_47_out, _6_6, not_1_out);
  and and_48 (and_48_out, _7_6, not_1_out);
  and and_49 (and_49_out, G0, not_1_out);
  and and_50 (and_50_out, _1_7, not_1_out);
  and and_51 (and_51_out, _2_7, not_1_out);
  and and_52 (and_52_out, _3_7, not_1_out);
  and and_53 (and_53_out, _4_7, not_1_out);
  and and_54 (and_54_out, _5_7, not_1_out);
  and and_55 (and_55_out, _6_7, not_1_out);
  and and_56 (and_56_out, _7_7, not_1_out);
  not not_2 (not_2_out, not_1_out);
  and and_57 (and_57_out, H0, not_2_out);
  and and_58 (and_58_out, _1_8, not_2_out);
  and and_59 (and_59_out, _2_8, not_2_out);
  and and_60 (and_60_out, _3_8, not_2_out);
  and and_61 (and_61_out, _4_8, not_2_out);
  and and_62 (and_62_out, _5_8, not_2_out);
  and and_63 (and_63_out, _6_8, not_2_out);
  and and_64 (and_64_out, _7_8, not_2_out);
  and and_65 (and_65_out, I0, not_2_out);
  and and_66 (and_66_out, _1_9, not_2_out);
  and and_67 (and_67_out, _2_9, not_2_out);
  and and_68 (and_68_out, _3_9, not_2_out);
  and and_69 (and_69_out, _4_9, not_2_out);
  and and_70 (and_70_out, _5_9, not_2_out);
  and and_71 (and_71_out, _6_9, not_2_out);
  and and_72 (and_72_out, _7_9, not_2_out);
  and and_73 (and_73_out, J0, not_2_out);
  and and_74 (and_74_out, _1_10, not_2_out);
  and and_75 (and_75_out, _2_10, not_2_out);
  and and_76 (and_76_out, _3_10, not_2_out);
  and and_77 (and_77_out, _4_10, not_2_out);
  and and_78 (and_78_out, _5_10, not_2_out);
  and and_79 (and_79_out, _6_10, not_2_out);
  and and_80 (and_80_out, _7_10, not_2_out);
  and and_81 (and_81_out, K0, not_2_out);
  and and_82 (and_82_out, _1_11, not_2_out);
  and and_83 (and_83_out, _2_11, not_2_out);
  and and_84 (and_84_out, _3_11, not_2_out);
  and and_85 (and_85_out, _4_11, not_2_out);
  and and_86 (and_86_out, _5_11, not_2_out);
  and and_87 (and_87_out, _6_11, not_2_out);
  and and_88 (and_88_out, _7_11, not_2_out);
  and and_89 (and_89_out, L0, not_2_out);
  and and_90 (and_90_out, _1_12, not_2_out);
  and and_91 (and_91_out, _2_12, not_2_out);
  and and_92 (and_92_out, _3_12, not_2_out);
  and and_93 (and_93_out, _4_12, not_2_out);
  and and_94 (and_94_out, _5_12, not_2_out);
  and and_95 (and_95_out, _6_12, not_2_out);
  and and_96 (and_96_out, _7_12, not_2_out);
  and and_97 (and_97_out, M0, not_2_out);
  and and_98 (and_98_out, _1_13, not_2_out);
  and and_99 (and_99_out, _2_13, not_2_out);
  and and_100 (and_100_out, _3_13, not_2_out);
  and and_101 (and_101_out, _4_13, not_2_out);
  and and_102 (and_102_out, _5_13, not_2_out);
  and and_103 (and_103_out, _6_13, not_2_out);
  and and_104 (and_104_out, _7_13, not_2_out);
  and and_105 (and_105_out, N0, not_2_out);
  and and_106 (and_106_out, _1_14, not_2_out);
  and and_107 (and_107_out, _2_14, not_2_out);
  and and_108 (and_108_out, _3_14, not_2_out);
  and and_109 (and_109_out, _4_14, not_2_out);
  and and_110 (and_110_out, _5_14, not_2_out);
  and and_111 (and_111_out, _6_14, not_2_out);
  and and_112 (and_112_out, _7_14, not_2_out);
  and and_113 (and_113_out, O0, not_2_out);
  and and_114 (and_114_out, _1_15, not_2_out);
  and and_115 (and_115_out, _2_15, not_2_out);
  and and_116 (and_116_out, _3_15, not_2_out);
  and and_117 (and_117_out, _4_15, not_2_out);
  and and_118 (and_118_out, _5_15, not_2_out);
  and and_119 (and_119_out, _6_15, not_2_out);
  and and_120 (and_120_out, _7_15, not_2_out);
  not not_3 (not_3_out, S2);
  not not_4 (not_4_out, S1);
  and and_121 (and_121_out, and_1_out, not_3_out);
  and and_122 (and_122_out, and_2_out, not_3_out);
  and and_123 (and_123_out, and_3_out, not_3_out);
  and and_124 (and_124_out, and_4_out, not_3_out);
  and and_125 (and_125_out, and_5_out, not_3_out);
  and and_126 (and_126_out, and_6_out, not_3_out);
  and and_127 (and_127_out, and_7_out, not_3_out);
  and and_128 (and_128_out, and_8_out, not_3_out);
  not not_5 (not_5_out, not_4_out);
  and and_129 (and_129_out, and_9_out, not_3_out);
  and and_130 (and_130_out, and_10_out, not_3_out);
  and and_131 (and_131_out, and_11_out, not_3_out);
  and and_132 (and_132_out, and_12_out, not_3_out);
  and and_133 (and_133_out, and_13_out, not_3_out);
  and and_134 (and_134_out, and_14_out, not_3_out);
  and and_135 (and_135_out, and_15_out, not_3_out);
  and and_136 (and_136_out, and_16_out, not_3_out);
  and and_137 (and_137_out, and_17_out, not_3_out);
  and and_138 (and_138_out, and_18_out, not_3_out);
  and and_139 (and_139_out, and_19_out, not_3_out);
  and and_140 (and_140_out, and_20_out, not_3_out);
  and and_141 (and_141_out, and_21_out, not_3_out);
  and and_142 (and_142_out, and_22_out, not_3_out);
  and and_143 (and_143_out, and_23_out, not_3_out);
  and and_144 (and_144_out, and_24_out, not_3_out);
  not not_6 (not_6_out, not_3_out);
  not not_7 (not_7_out, not_5_out);
  and and_145 (and_145_out, and_25_out, not_6_out);
  and and_146 (and_146_out, and_26_out, not_6_out);
  and and_147 (and_147_out, and_27_out, not_6_out);
  and and_148 (and_148_out, and_28_out, not_6_out);
  and and_149 (and_149_out, and_29_out, not_6_out);
  and and_150 (and_150_out, and_30_out, not_6_out);
  and and_151 (and_151_out, and_31_out, not_6_out);
  and and_152 (and_152_out, and_32_out, not_6_out);
  and and_153 (and_153_out, and_33_out, not_6_out);
  and and_154 (and_154_out, and_34_out, not_6_out);
  and and_155 (and_155_out, and_35_out, not_6_out);
  and and_156 (and_156_out, and_36_out, not_6_out);
  and and_157 (and_157_out, and_37_out, not_6_out);
  and and_158 (and_158_out, and_38_out, not_6_out);
  and and_159 (and_159_out, and_39_out, not_6_out);
  and and_160 (and_160_out, and_40_out, not_6_out);
  not not_8 (not_8_out, not_7_out);
  and and_161 (and_161_out, and_41_out, not_6_out);
  and and_162 (and_162_out, and_42_out, not_6_out);
  and and_163 (and_163_out, and_43_out, not_6_out);
  and and_164 (and_164_out, and_44_out, not_6_out);
  and and_165 (and_165_out, and_45_out, not_6_out);
  and and_166 (and_166_out, and_46_out, not_6_out);
  and and_167 (and_167_out, and_47_out, not_6_out);
  and and_168 (and_168_out, and_48_out, not_6_out);
  and and_169 (and_169_out, and_49_out, not_6_out);
  and and_170 (and_170_out, and_50_out, not_6_out);
  and and_171 (and_171_out, and_51_out, not_6_out);
  and and_172 (and_172_out, and_52_out, not_6_out);
  and and_173 (and_173_out, and_53_out, not_6_out);
  and and_174 (and_174_out, and_54_out, not_6_out);
  and and_175 (and_175_out, and_55_out, not_6_out);
  and and_176 (and_176_out, and_56_out, not_6_out);
  not not_9 (not_9_out, not_8_out);
  not not_10 (not_10_out, not_6_out);
  and and_177 (and_177_out, and_57_out, not_10_out);
  and and_178 (and_178_out, and_58_out, not_10_out);
  and and_179 (and_179_out, and_59_out, not_10_out);
  and and_180 (and_180_out, and_60_out, not_10_out);
  and and_181 (and_181_out, and_61_out, not_10_out);
  and and_182 (and_182_out, and_62_out, not_10_out);
  and and_183 (and_183_out, and_63_out, not_10_out);
  and and_184 (and_184_out, and_64_out, not_10_out);
  and and_185 (and_185_out, and_65_out, not_10_out);
  and and_186 (and_186_out, and_66_out, not_10_out);
  and and_187 (and_187_out, and_67_out, not_10_out);
  and and_188 (and_188_out, and_68_out, not_10_out);
  and and_189 (and_189_out, and_69_out, not_10_out);
  and and_190 (and_190_out, and_70_out, not_10_out);
  and and_191 (and_191_out, and_71_out, not_10_out);
  and and_192 (and_192_out, and_72_out, not_10_out);
  not not_11 (not_11_out, not_9_out);
  and and_193 (and_193_out, and_73_out, not_10_out);
  and and_194 (and_194_out, and_74_out, not_10_out);
  and and_195 (and_195_out, and_75_out, not_10_out);
  and and_196 (and_196_out, and_76_out, not_10_out);
  and and_197 (and_197_out, and_77_out, not_10_out);
  and and_198 (and_198_out, and_78_out, not_10_out);
  and and_199 (and_199_out, and_79_out, not_10_out);
  and and_200 (and_200_out, and_80_out, not_10_out);
  and and_201 (and_201_out, and_81_out, not_10_out);
  and and_202 (and_202_out, and_82_out, not_10_out);
  and and_203 (and_203_out, and_83_out, not_10_out);
  and and_204 (and_204_out, and_84_out, not_10_out);
  and and_205 (and_205_out, and_85_out, not_10_out);
  and and_206 (and_206_out, and_86_out, not_10_out);
  and and_207 (and_207_out, and_87_out, not_10_out);
  and and_208 (and_208_out, and_88_out, not_10_out);
  not not_12 (not_12_out, not_11_out);
  not not_13 (not_13_out, not_10_out);
  and and_209 (and_209_out, and_89_out, not_13_out);
  and and_210 (and_210_out, and_90_out, not_13_out);
  and and_211 (and_211_out, and_91_out, not_13_out);
  and and_212 (and_212_out, and_92_out, not_13_out);
  and and_213 (and_213_out, and_93_out, not_13_out);
  and and_214 (and_214_out, and_94_out, not_13_out);
  and and_215 (and_215_out, and_95_out, not_13_out);
  and and_216 (and_216_out, and_96_out, not_13_out);
  and and_217 (and_217_out, and_97_out, not_13_out);
  and and_218 (and_218_out, and_98_out, not_13_out);
  and and_219 (and_219_out, and_99_out, not_13_out);
  and and_220 (and_220_out, and_100_out, not_13_out);
  and and_221 (and_221_out, and_101_out, not_13_out);
  and and_222 (and_222_out, and_102_out, not_13_out);
  and and_223 (and_223_out, and_103_out, not_13_out);
  and and_224 (and_224_out, and_104_out, not_13_out);
  not not_14 (not_14_out, not_12_out);
  and and_225 (and_225_out, and_105_out, not_13_out);
  and and_226 (and_226_out, and_106_out, not_13_out);
  and and_227 (and_227_out, and_107_out, not_13_out);
  and and_228 (and_228_out, and_108_out, not_13_out);
  and and_229 (and_229_out, and_109_out, not_13_out);
  and and_230 (and_230_out, and_110_out, not_13_out);
  and and_231 (and_231_out, and_111_out, not_13_out);
  and and_232 (and_232_out, and_112_out, not_13_out);
  and and_233 (and_233_out, and_113_out, not_13_out);
  and and_234 (and_234_out, and_114_out, not_13_out);
  and and_235 (and_235_out, and_115_out, not_13_out);
  and and_236 (and_236_out, and_116_out, not_13_out);
  and and_237 (and_237_out, and_117_out, not_13_out);
  and and_238 (and_238_out, and_118_out, not_13_out);
  and and_239 (and_239_out, and_119_out, not_13_out);
  and and_240 (and_240_out, and_120_out, not_13_out);
  and and_241 (and_241_out, not_4_out, and_121_out);
  and and_242 (and_242_out, and_241_out, S0);
  and and_243 (and_243_out, not_4_out, and_122_out);
  and and_244 (and_244_out, and_243_out, S0);
  and and_245 (and_245_out, not_4_out, and_123_out);
  and and_246 (and_246_out, and_245_out, S0);
  and and_247 (and_247_out, not_4_out, and_124_out);
  and and_248 (and_248_out, and_247_out, S0);
  and and_249 (and_249_out, not_4_out, and_125_out);
  and and_250 (and_250_out, and_249_out, S0);
  and and_251 (and_251_out, not_4_out, and_126_out);
  and and_252 (and_252_out, and_251_out, S0);
  and and_253 (and_253_out, not_4_out, and_127_out);
  and and_254 (and_254_out, and_253_out, S0);
  and and_255 (and_255_out, not_4_out, and_128_out);
  and and_256 (and_256_out, and_255_out, S0);
  not not_15 (not_15_out, S0);
  and and_257 (and_257_out, not_5_out, and_129_out);
  and and_258 (and_258_out, and_257_out, not_15_out);
  and and_259 (and_259_out, not_5_out, and_130_out);
  and and_260 (and_260_out, and_259_out, not_15_out);
  and and_261 (and_261_out, not_5_out, and_131_out);
  and and_262 (and_262_out, and_261_out, not_15_out);
  and and_263 (and_263_out, not_5_out, and_132_out);
  and and_264 (and_264_out, and_263_out, not_15_out);
  and and_265 (and_265_out, not_5_out, and_133_out);
  and and_266 (and_266_out, and_265_out, not_15_out);
  and and_267 (and_267_out, not_5_out, and_134_out);
  and and_268 (and_268_out, and_267_out, not_15_out);
  and and_269 (and_269_out, not_5_out, and_135_out);
  and and_270 (and_270_out, and_269_out, not_15_out);
  and and_271 (and_271_out, not_5_out, and_136_out);
  and and_272 (and_272_out, and_271_out, not_15_out);
  not not_16 (not_16_out, not_15_out);
  and and_273 (and_273_out, not_5_out, and_137_out);
  and and_274 (and_274_out, and_273_out, not_16_out);
  and and_275 (and_275_out, not_5_out, and_138_out);
  and and_276 (and_276_out, and_275_out, not_16_out);
  and and_277 (and_277_out, not_5_out, and_139_out);
  and and_278 (and_278_out, and_277_out, not_16_out);
  and and_279 (and_279_out, not_5_out, and_140_out);
  and and_280 (and_280_out, and_279_out, not_16_out);
  and and_281 (and_281_out, not_5_out, and_141_out);
  and and_282 (and_282_out, and_281_out, not_16_out);
  and and_283 (and_283_out, not_5_out, and_142_out);
  and and_284 (and_284_out, and_283_out, not_16_out);
  and and_285 (and_285_out, not_5_out, and_143_out);
  and and_286 (and_286_out, and_285_out, not_16_out);
  and and_287 (and_287_out, not_5_out, and_144_out);
  and and_288 (and_288_out, and_287_out, not_16_out);
  not not_17 (not_17_out, not_16_out);
  and and_289 (and_289_out, not_7_out, and_145_out);
  and and_290 (and_290_out, and_289_out, not_17_out);
  and and_291 (and_291_out, not_7_out, and_146_out);
  and and_292 (and_292_out, and_291_out, not_17_out);
  and and_293 (and_293_out, not_7_out, and_147_out);
  and and_294 (and_294_out, and_293_out, not_17_out);
  and and_295 (and_295_out, not_7_out, and_148_out);
  and and_296 (and_296_out, and_295_out, not_17_out);
  and and_297 (and_297_out, not_7_out, and_149_out);
  and and_298 (and_298_out, and_297_out, not_17_out);
  and and_299 (and_299_out, not_7_out, and_150_out);
  and and_300 (and_300_out, and_299_out, not_17_out);
  and and_301 (and_301_out, not_7_out, and_151_out);
  and and_302 (and_302_out, and_301_out, not_17_out);
  and and_303 (and_303_out, not_7_out, and_152_out);
  and and_304 (and_304_out, and_303_out, not_17_out);
  not not_18 (not_18_out, not_17_out);
  and and_305 (and_305_out, not_7_out, and_153_out);
  and and_306 (and_306_out, and_305_out, not_18_out);
  and and_307 (and_307_out, not_7_out, and_154_out);
  and and_308 (and_308_out, and_307_out, not_18_out);
  and and_309 (and_309_out, not_7_out, and_155_out);
  and and_310 (and_310_out, and_309_out, not_18_out);
  and and_311 (and_311_out, not_7_out, and_156_out);
  and and_312 (and_312_out, and_311_out, not_18_out);
  and and_313 (and_313_out, not_7_out, and_157_out);
  and and_314 (and_314_out, and_313_out, not_18_out);
  and and_315 (and_315_out, not_7_out, and_158_out);
  and and_316 (and_316_out, and_315_out, not_18_out);
  and and_317 (and_317_out, not_7_out, and_159_out);
  and and_318 (and_318_out, and_317_out, not_18_out);
  and and_319 (and_319_out, not_7_out, and_160_out);
  and and_320 (and_320_out, and_319_out, not_18_out);
  not not_19 (not_19_out, not_18_out);
  and and_321 (and_321_out, not_8_out, and_161_out);
  and and_322 (and_322_out, and_321_out, not_19_out);
  and and_323 (and_323_out, not_8_out, and_162_out);
  and and_324 (and_324_out, and_323_out, not_19_out);
  and and_325 (and_325_out, not_8_out, and_163_out);
  and and_326 (and_326_out, and_325_out, not_19_out);
  and and_327 (and_327_out, not_8_out, and_164_out);
  and and_328 (and_328_out, and_327_out, not_19_out);
  and and_329 (and_329_out, not_8_out, and_165_out);
  and and_330 (and_330_out, and_329_out, not_19_out);
  and and_331 (and_331_out, not_8_out, and_166_out);
  and and_332 (and_332_out, and_331_out, not_19_out);
  and and_333 (and_333_out, not_8_out, and_167_out);
  and and_334 (and_334_out, and_333_out, not_19_out);
  and and_335 (and_335_out, not_8_out, and_168_out);
  and and_336 (and_336_out, and_335_out, not_19_out);
  not not_20 (not_20_out, not_19_out);
  and and_337 (and_337_out, not_8_out, and_169_out);
  and and_338 (and_338_out, and_337_out, not_20_out);
  and and_339 (and_339_out, not_8_out, and_170_out);
  and and_340 (and_340_out, and_339_out, not_20_out);
  and and_341 (and_341_out, not_8_out, and_171_out);
  and and_342 (and_342_out, and_341_out, not_20_out);
  and and_343 (and_343_out, not_8_out, and_172_out);
  and and_344 (and_344_out, and_343_out, not_20_out);
  and and_345 (and_345_out, not_8_out, and_173_out);
  and and_346 (and_346_out, and_345_out, not_20_out);
  and and_347 (and_347_out, not_8_out, and_174_out);
  and and_348 (and_348_out, and_347_out, not_20_out);
  and and_349 (and_349_out, not_8_out, and_175_out);
  and and_350 (and_350_out, and_349_out, not_20_out);
  and and_351 (and_351_out, not_8_out, and_176_out);
  and and_352 (and_352_out, and_351_out, not_20_out);
  not not_21 (not_21_out, not_20_out);
  and and_353 (and_353_out, not_9_out, and_177_out);
  and and_354 (and_354_out, and_353_out, not_21_out);
  and and_355 (and_355_out, not_9_out, and_178_out);
  and and_356 (and_356_out, and_355_out, not_21_out);
  and and_357 (and_357_out, not_9_out, and_179_out);
  and and_358 (and_358_out, and_357_out, not_21_out);
  and and_359 (and_359_out, not_9_out, and_180_out);
  and and_360 (and_360_out, and_359_out, not_21_out);
  and and_361 (and_361_out, not_9_out, and_181_out);
  and and_362 (and_362_out, and_361_out, not_21_out);
  and and_363 (and_363_out, not_9_out, and_182_out);
  and and_364 (and_364_out, and_363_out, not_21_out);
  and and_365 (and_365_out, not_9_out, and_183_out);
  and and_366 (and_366_out, and_365_out, not_21_out);
  and and_367 (and_367_out, not_9_out, and_184_out);
  and and_368 (and_368_out, and_367_out, not_21_out);
  not not_22 (not_22_out, not_21_out);
  and and_369 (and_369_out, not_9_out, and_185_out);
  and and_370 (and_370_out, and_369_out, not_22_out);
  and and_371 (and_371_out, not_9_out, and_186_out);
  and and_372 (and_372_out, and_371_out, not_22_out);
  and and_373 (and_373_out, not_9_out, and_187_out);
  and and_374 (and_374_out, and_373_out, not_22_out);
  and and_375 (and_375_out, not_9_out, and_188_out);
  and and_376 (and_376_out, and_375_out, not_22_out);
  and and_377 (and_377_out, not_9_out, and_189_out);
  and and_378 (and_378_out, and_377_out, not_22_out);
  and and_379 (and_379_out, not_9_out, and_190_out);
  and and_380 (and_380_out, and_379_out, not_22_out);
  and and_381 (and_381_out, not_9_out, and_191_out);
  and and_382 (and_382_out, and_381_out, not_22_out);
  and and_383 (and_383_out, not_9_out, and_192_out);
  and and_384 (and_384_out, and_383_out, not_22_out);
  not not_23 (not_23_out, not_22_out);
  and and_385 (and_385_out, not_11_out, and_193_out);
  and and_386 (and_386_out, and_385_out, not_23_out);
  and and_387 (and_387_out, not_11_out, and_194_out);
  and and_388 (and_388_out, and_387_out, not_23_out);
  and and_389 (and_389_out, not_11_out, and_195_out);
  and and_390 (and_390_out, and_389_out, not_23_out);
  and and_391 (and_391_out, not_11_out, and_196_out);
  and and_392 (and_392_out, and_391_out, not_23_out);
  and and_393 (and_393_out, not_11_out, and_197_out);
  and and_394 (and_394_out, and_393_out, not_23_out);
  and and_395 (and_395_out, not_11_out, and_198_out);
  and and_396 (and_396_out, and_395_out, not_23_out);
  and and_397 (and_397_out, not_11_out, and_199_out);
  and and_398 (and_398_out, and_397_out, not_23_out);
  and and_399 (and_399_out, not_11_out, and_200_out);
  and and_400 (and_400_out, and_399_out, not_23_out);
  not not_24 (not_24_out, not_23_out);
  and and_401 (and_401_out, not_11_out, and_201_out);
  and and_402 (and_402_out, and_401_out, not_24_out);
  and and_403 (and_403_out, not_11_out, and_202_out);
  and and_404 (and_404_out, and_403_out, not_24_out);
  and and_405 (and_405_out, not_11_out, and_203_out);
  and and_406 (and_406_out, and_405_out, not_24_out);
  and and_407 (and_407_out, not_11_out, and_204_out);
  and and_408 (and_408_out, and_407_out, not_24_out);
  and and_409 (and_409_out, not_11_out, and_205_out);
  and and_410 (and_410_out, and_409_out, not_24_out);
  and and_411 (and_411_out, not_11_out, and_206_out);
  and and_412 (and_412_out, and_411_out, not_24_out);
  and and_413 (and_413_out, not_11_out, and_207_out);
  and and_414 (and_414_out, and_413_out, not_24_out);
  and and_415 (and_415_out, not_11_out, and_208_out);
  and and_416 (and_416_out, and_415_out, not_24_out);
  not not_25 (not_25_out, not_24_out);
  and and_417 (and_417_out, not_12_out, and_209_out);
  and and_418 (and_418_out, and_417_out, not_25_out);
  and and_419 (and_419_out, not_12_out, and_210_out);
  and and_420 (and_420_out, and_419_out, not_25_out);
  and and_421 (and_421_out, not_12_out, and_211_out);
  and and_422 (and_422_out, and_421_out, not_25_out);
  and and_423 (and_423_out, not_12_out, and_212_out);
  and and_424 (and_424_out, and_423_out, not_25_out);
  and and_425 (and_425_out, not_12_out, and_213_out);
  and and_426 (and_426_out, and_425_out, not_25_out);
  and and_427 (and_427_out, not_12_out, and_214_out);
  and and_428 (and_428_out, and_427_out, not_25_out);
  and and_429 (and_429_out, not_12_out, and_215_out);
  and and_430 (and_430_out, and_429_out, not_25_out);
  and and_431 (and_431_out, not_12_out, and_216_out);
  and and_432 (and_432_out, and_431_out, not_25_out);
  not not_26 (not_26_out, not_25_out);
  and and_433 (and_433_out, not_12_out, and_217_out);
  and and_434 (and_434_out, and_433_out, not_26_out);
  and and_435 (and_435_out, not_12_out, and_218_out);
  and and_436 (and_436_out, and_435_out, not_26_out);
  and and_437 (and_437_out, not_12_out, and_219_out);
  and and_438 (and_438_out, and_437_out, not_26_out);
  and and_439 (and_439_out, not_12_out, and_220_out);
  and and_440 (and_440_out, and_439_out, not_26_out);
  and and_441 (and_441_out, not_12_out, and_221_out);
  and and_442 (and_442_out, and_441_out, not_26_out);
  and and_443 (and_443_out, not_12_out, and_222_out);
  and and_444 (and_444_out, and_443_out, not_26_out);
  and and_445 (and_445_out, not_12_out, and_223_out);
  and and_446 (and_446_out, and_445_out, not_26_out);
  and and_447 (and_447_out, not_12_out, and_224_out);
  and and_448 (and_448_out, and_447_out, not_26_out);
  not not_27 (not_27_out, not_26_out);
  and and_449 (and_449_out, not_14_out, and_225_out);
  and and_450 (and_450_out, and_449_out, not_27_out);
  and and_451 (and_451_out, not_14_out, and_226_out);
  and and_452 (and_452_out, and_451_out, not_27_out);
  and and_453 (and_453_out, not_14_out, and_227_out);
  and and_454 (and_454_out, and_453_out, not_27_out);
  and and_455 (and_455_out, not_14_out, and_228_out);
  and and_456 (and_456_out, and_455_out, not_27_out);
  and and_457 (and_457_out, not_14_out, and_229_out);
  and and_458 (and_458_out, and_457_out, not_27_out);
  and and_459 (and_459_out, not_14_out, and_230_out);
  and and_460 (and_460_out, and_459_out, not_27_out);
  and and_461 (and_461_out, not_14_out, and_231_out);
  and and_462 (and_462_out, and_461_out, not_27_out);
  and and_463 (and_463_out, not_14_out, and_232_out);
  and and_464 (and_464_out, and_463_out, not_27_out);
  not not_28 (not_28_out, not_27_out);
  and and_465 (and_465_out, not_14_out, and_233_out);
  and and_466 (and_466_out, and_465_out, not_28_out);
  and and_467 (and_467_out, not_14_out, and_234_out);
  and and_468 (and_468_out, and_467_out, not_28_out);
  and and_469 (and_469_out, not_14_out, and_235_out);
  and and_470 (and_470_out, and_469_out, not_28_out);
  and and_471 (and_471_out, not_14_out, and_236_out);
  and and_472 (and_472_out, and_471_out, not_28_out);
  and and_473 (and_473_out, not_14_out, and_237_out);
  and and_474 (and_474_out, and_473_out, not_28_out);
  and and_475 (and_475_out, not_14_out, and_238_out);
  and and_476 (and_476_out, and_475_out, not_28_out);
  and and_477 (and_477_out, not_14_out, and_239_out);
  and and_478 (and_478_out, and_477_out, not_28_out);
  and and_479 (and_479_out, not_14_out, and_240_out);
  and and_480 (and_480_out, and_479_out, not_28_out);
  or or_1 (_7_16, and_242_out, or_5_out);
  or or_2 (_6_16, and_244_out, or_6_out);
  or or_3 (_5_16, and_246_out, or_7_out);
  or or_4 (_4_16, and_248_out, or_8_out);
  or or_5 (or_5_out, and_258_out, or_9_out);
  or or_6 (or_6_out, and_260_out, or_10_out);
  or or_7 (or_7_out, and_262_out, or_11_out);
  or or_8 (or_8_out, and_264_out, or_12_out);
  or or_9 (or_9_out, and_274_out, or_13_out);
  or or_10 (or_10_out, and_276_out, or_14_out);
  or or_11 (or_11_out, and_278_out, or_15_out);
  or or_12 (or_12_out, and_280_out, or_16_out);
  or or_13 (or_13_out, and_290_out, or_17_out);
  or or_14 (or_14_out, and_292_out, or_18_out);
  or or_15 (or_15_out, and_294_out, or_19_out);
  or or_16 (or_16_out, and_296_out, or_20_out);
  or or_17 (or_17_out, and_306_out, or_21_out);
  or or_18 (or_18_out, and_308_out, or_22_out);
  or or_19 (or_19_out, and_310_out, or_23_out);
  or or_20 (or_20_out, and_312_out, or_24_out);
  or or_21 (or_21_out, and_322_out, or_25_out);
  or or_22 (or_22_out, and_324_out, or_26_out);
  or or_23 (or_23_out, and_326_out, or_27_out);
  or or_24 (or_24_out, and_328_out, or_28_out);
  or or_25 (or_25_out, and_338_out, or_29_out);
  or or_26 (or_26_out, and_340_out, or_30_out);
  or or_27 (or_27_out, and_342_out, or_31_out);
  or or_28 (or_28_out, and_344_out, or_32_out);
  or or_29 (or_29_out, and_354_out, or_33_out);
  or or_30 (or_30_out, and_356_out, or_34_out);
  or or_31 (or_31_out, and_358_out, or_35_out);
  or or_32 (or_32_out, and_360_out, or_36_out);
  or or_33 (or_33_out, and_370_out, or_37_out);
  or or_34 (or_34_out, and_372_out, or_38_out);
  or or_35 (or_35_out, and_374_out, or_39_out);
  or or_36 (or_36_out, and_376_out, or_40_out);
  or or_37 (or_37_out, and_386_out, or_41_out);
  or or_38 (or_38_out, and_388_out, or_42_out);
  or or_39 (or_39_out, and_390_out, or_43_out);
  or or_40 (or_40_out, and_392_out, or_44_out);
  or or_41 (or_41_out, and_402_out, or_45_out);
  or or_42 (or_42_out, and_404_out, or_46_out);
  or or_43 (or_43_out, and_406_out, or_47_out);
  or or_44 (or_44_out, and_408_out, or_48_out);
  or or_45 (or_45_out, and_418_out, or_49_out);
  or or_46 (or_46_out, and_420_out, or_50_out);
  or or_47 (or_47_out, and_422_out, or_51_out);
  or or_48 (or_48_out, and_424_out, or_52_out);
  or or_49 (or_49_out, and_434_out, or_53_out);
  or or_50 (or_50_out, and_436_out, or_54_out);
  or or_51 (or_51_out, and_438_out, or_55_out);
  or or_52 (or_52_out, and_440_out, or_56_out);
  or or_53 (or_53_out, and_450_out, and_466_out);
  or or_54 (or_54_out, and_452_out, and_468_out);
  or or_55 (or_55_out, and_454_out, and_470_out);
  or or_56 (or_56_out, and_456_out, and_472_out);
  or or_57 (_3_16, and_250_out, or_61_out);
  or or_58 (_2_16, and_252_out, or_62_out);
  or or_59 (_1_16, and_254_out, or_63_out);
  or or_60 (_0, and_256_out, or_64_out);
  or or_61 (or_61_out, and_266_out, or_65_out);
  or or_62 (or_62_out, and_268_out, or_66_out);
  or or_63 (or_63_out, and_270_out, or_67_out);
  or or_64 (or_64_out, and_272_out, or_68_out);
  or or_65 (or_65_out, and_282_out, or_69_out);
  or or_66 (or_66_out, and_284_out, or_70_out);
  or or_67 (or_67_out, and_286_out, or_71_out);
  or or_68 (or_68_out, and_288_out, or_72_out);
  or or_69 (or_69_out, and_298_out, or_73_out);
  or or_70 (or_70_out, and_300_out, or_74_out);
  or or_71 (or_71_out, and_302_out, or_75_out);
  or or_72 (or_72_out, and_304_out, or_76_out);
  or or_73 (or_73_out, and_314_out, or_77_out);
  or or_74 (or_74_out, and_316_out, or_78_out);
  or or_75 (or_75_out, and_318_out, or_79_out);
  or or_76 (or_76_out, and_320_out, or_80_out);
  or or_77 (or_77_out, and_330_out, or_81_out);
  or or_78 (or_78_out, and_332_out, or_82_out);
  or or_79 (or_79_out, and_334_out, or_83_out);
  or or_80 (or_80_out, and_336_out, or_84_out);
  or or_81 (or_81_out, and_346_out, or_85_out);
  or or_82 (or_82_out, and_348_out, or_86_out);
  or or_83 (or_83_out, and_350_out, or_87_out);
  or or_84 (or_84_out, and_352_out, or_88_out);
  or or_85 (or_85_out, and_362_out, or_89_out);
  or or_86 (or_86_out, and_364_out, or_90_out);
  or or_87 (or_87_out, and_366_out, or_91_out);
  or or_88 (or_88_out, and_368_out, or_92_out);
  or or_89 (or_89_out, and_378_out, or_93_out);
  or or_90 (or_90_out, and_380_out, or_94_out);
  or or_91 (or_91_out, and_382_out, or_95_out);
  or or_92 (or_92_out, and_384_out, or_96_out);
  or or_93 (or_93_out, and_394_out, or_97_out);
  or or_94 (or_94_out, and_396_out, or_98_out);
  or or_95 (or_95_out, and_398_out, or_99_out);
  or or_96 (or_96_out, and_400_out, or_100_out);
  or or_97 (or_97_out, and_410_out, or_101_out);
  or or_98 (or_98_out, and_412_out, or_102_out);
  or or_99 (or_99_out, and_414_out, or_103_out);
  or or_100 (or_100_out, and_416_out, or_104_out);
  or or_101 (or_101_out, and_426_out, or_105_out);
  or or_102 (or_102_out, and_428_out, or_106_out);
  or or_103 (or_103_out, and_430_out, or_107_out);
  or or_104 (or_104_out, and_432_out, or_108_out);
  or or_105 (or_105_out, and_442_out, or_109_out);
  or or_106 (or_106_out, and_444_out, or_110_out);
  or or_107 (or_107_out, and_446_out, or_111_out);
  or or_108 (or_108_out, and_448_out, or_112_out);
  or or_109 (or_109_out, and_458_out, and_474_out);
  or or_110 (or_110_out, and_460_out, and_476_out);
  or or_111 (or_111_out, and_462_out, and_478_out);
  or or_112 (or_112_out, and_464_out, and_480_out);
endmodule

module _7_Way_Multiplexor (
  input  S2,
  input  S1,
  input  S0,
  input  A0,
  input  _1,
  input  _2,
  input  _3,
  input  _4,
  input  _5,
  input  _6,
  input  _7,
  input  B0,
  input  _1_2,
  input  _2_2,
  input  _3_2,
  input  _4_2,
  input  _5_2,
  input  _6_2,
  input  _7_2,
  input  C0,
  input  _1_3,
  input  _2_3,
  input  _3_3,
  input  _4_3,
  input  _5_3,
  input  _6_3,
  input  _7_3,
  input  D0,
  input  _1_4,
  input  _2_4,
  input  _3_4,
  input  _4_4,
  input  _5_4,
  input  _6_4,
  input  _7_4,
  input  E0,
  input  _1_5,
  input  _2_5,
  input  _3_5,
  input  _4_5,
  input  _5_5,
  input  _6_5,
  input  _7_5,
  input  F0,
  input  _1_6,
  input  _2_6,
  input  _3_6,
  input  _4_6,
  input  _5_6,
  input  _6_6,
  input  _7_6,
  input  G0,
  input  _1_7,
  input  _2_7,
  input  _3_7,
  input  _4_7,
  input  _5_7,
  input  _6_7,
  input  _7_7,
  output _7_8,
  output _6_8,
  output _5_8,
  output _4_8,
  output _3_8,
  output _2_8,
  output _1_8,
  output _0
);

  wire and_1_out, and_2_out, and_3_out, and_4_out, and_5_out, and_6_out, and_7_out, and_8_out, and_9_out,
       and_10_out, and_11_out, and_12_out, and_13_out, and_14_out, and_15_out, and_16_out, and_17_out,
       and_18_out, and_19_out, and_20_out, and_21_out, and_22_out, and_23_out, and_24_out, and_25_out,
       and_26_out, and_27_out, and_28_out, and_29_out, and_30_out, and_31_out, and_32_out, and_33_out,
       and_34_out, and_35_out, and_36_out, and_37_out, and_38_out, and_39_out, and_40_out, and_41_out,
       and_42_out, and_43_out, and_44_out, and_45_out, and_46_out, and_47_out, and_48_out, and_49_out,
       and_50_out, and_51_out, and_52_out, and_53_out, and_54_out, and_55_out, and_56_out, and_57_out,
       and_58_out, and_59_out, and_60_out, and_61_out, and_62_out, and_63_out, and_64_out, and_65_out,
       and_66_out, and_67_out, and_68_out, and_69_out, and_70_out, and_71_out, and_72_out, and_73_out,
       and_74_out, and_75_out, and_76_out, and_77_out, and_78_out, and_79_out, and_80_out, and_81_out,
       and_82_out, and_83_out, and_84_out, and_85_out, and_86_out, and_87_out, and_88_out, and_89_out,
       and_90_out, and_91_out, and_92_out, and_93_out, and_94_out, and_95_out, and_96_out, and_97_out,
       and_98_out, and_99_out, and_100_out, and_101_out, and_102_out, and_103_out, and_104_out, and_105_out,
       and_106_out, and_107_out, and_108_out, and_109_out, and_110_out, and_111_out, and_112_out,
       and_113_out, and_114_out, and_115_out, and_116_out, and_117_out, and_118_out, and_119_out,
       and_120_out, and_121_out, and_122_out, and_123_out, and_124_out, and_125_out, and_126_out,
       and_127_out, and_128_out, and_129_out, and_130_out, and_131_out, and_132_out, and_133_out,
       and_134_out, and_135_out, and_136_out, and_137_out, and_138_out, and_139_out, and_140_out,
       and_141_out, and_142_out, and_143_out, and_144_out, and_145_out, and_146_out, and_147_out,
       and_148_out, and_149_out, and_150_out, and_151_out, and_152_out, and_153_out, and_154_out,
       and_155_out, and_156_out, and_157_out, and_158_out, and_159_out, and_160_out, and_161_out,
       and_162_out, and_163_out, and_164_out, and_165_out, and_166_out, and_167_out, and_168_out, not_1_out,
       not_2_out, not_3_out, not_4_out, not_5_out, not_6_out, not_7_out, not_8_out, not_9_out, not_10_out,
       not_11_out, not_12_out, or_4_out, or_5_out, or_6_out, or_7_out, or_8_out, or_9_out, or_10_out,
       or_11_out, or_12_out, or_13_out, or_14_out, or_15_out, or_16_out, or_17_out, or_18_out, or_23_out,
       or_24_out, or_25_out, or_26_out, or_27_out, or_28_out, or_29_out, or_30_out, or_31_out, or_32_out,
       or_33_out, or_34_out, or_35_out, or_36_out, or_37_out, or_38_out, or_39_out, or_40_out, or_41_out,
       or_42_out, or_44_out, or_45_out, or_46_out, or_47_out, or_48_out;

  not not_1 (not_1_out, S2);
  and and_1 (and_1_out, A0, not_1_out);
  and and_2 (and_2_out, _1, not_1_out);
  and and_3 (and_3_out, _2, not_1_out);
  and and_4 (and_4_out, _3, not_1_out);
  and and_5 (and_5_out, _4, not_1_out);
  and and_6 (and_6_out, _5, not_1_out);
  and and_7 (and_7_out, _6, not_1_out);
  and and_8 (and_8_out, _7, not_1_out);
  and and_9 (and_9_out, B0, not_1_out);
  and and_10 (and_10_out, _1_2, not_1_out);
  and and_11 (and_11_out, _2_2, not_1_out);
  and and_12 (and_12_out, _3_2, not_1_out);
  and and_13 (and_13_out, _4_2, not_1_out);
  and and_14 (and_14_out, _5_2, not_1_out);
  and and_15 (and_15_out, _6_2, not_1_out);
  and and_16 (and_16_out, _7_2, not_1_out);
  and and_17 (and_17_out, C0, not_1_out);
  and and_18 (and_18_out, _1_3, not_1_out);
  and and_19 (and_19_out, _2_3, not_1_out);
  and and_20 (and_20_out, _3_3, not_1_out);
  and and_21 (and_21_out, _4_3, not_1_out);
  and and_22 (and_22_out, _5_3, not_1_out);
  and and_23 (and_23_out, _6_3, not_1_out);
  and and_24 (and_24_out, _7_3, not_1_out);
  not not_2 (not_2_out, not_1_out);
  and and_25 (and_25_out, D0, not_2_out);
  and and_26 (and_26_out, _1_4, not_2_out);
  and and_27 (and_27_out, _2_4, not_2_out);
  and and_28 (and_28_out, _3_4, not_2_out);
  and and_29 (and_29_out, _4_4, not_2_out);
  and and_30 (and_30_out, _5_4, not_2_out);
  and and_31 (and_31_out, _6_4, not_2_out);
  and and_32 (and_32_out, _7_4, not_2_out);
  and and_33 (and_33_out, E0, not_2_out);
  and and_34 (and_34_out, _1_5, not_2_out);
  and and_35 (and_35_out, _2_5, not_2_out);
  and and_36 (and_36_out, _3_5, not_2_out);
  and and_37 (and_37_out, _4_5, not_2_out);
  and and_38 (and_38_out, _5_5, not_2_out);
  and and_39 (and_39_out, _6_5, not_2_out);
  and and_40 (and_40_out, _7_5, not_2_out);
  and and_41 (and_41_out, F0, not_2_out);
  and and_42 (and_42_out, _1_6, not_2_out);
  and and_43 (and_43_out, _2_6, not_2_out);
  and and_44 (and_44_out, _3_6, not_2_out);
  and and_45 (and_45_out, _4_6, not_2_out);
  and and_46 (and_46_out, _5_6, not_2_out);
  and and_47 (and_47_out, _6_6, not_2_out);
  and and_48 (and_48_out, _7_6, not_2_out);
  and and_49 (and_49_out, G0, not_2_out);
  and and_50 (and_50_out, _1_7, not_2_out);
  and and_51 (and_51_out, _2_7, not_2_out);
  and and_52 (and_52_out, _3_7, not_2_out);
  and and_53 (and_53_out, _4_7, not_2_out);
  and and_54 (and_54_out, _5_7, not_2_out);
  and and_55 (and_55_out, _6_7, not_2_out);
  and and_56 (and_56_out, _7_7, not_2_out);
  not not_3 (not_3_out, S1);
  and and_57 (and_57_out, not_3_out, and_1_out);
  and and_58 (and_58_out, not_3_out, and_2_out);
  and and_59 (and_59_out, not_3_out, and_3_out);
  and and_60 (and_60_out, not_3_out, and_4_out);
  and and_61 (and_61_out, not_3_out, and_5_out);
  and and_62 (and_62_out, not_3_out, and_6_out);
  and and_63 (and_63_out, not_3_out, and_7_out);
  and and_64 (and_64_out, not_3_out, and_8_out);
  not not_4 (not_4_out, not_3_out);
  not not_5 (not_5_out, S0);
  and and_65 (and_65_out, not_4_out, and_9_out);
  and and_66 (and_66_out, not_4_out, and_10_out);
  and and_67 (and_67_out, not_4_out, and_11_out);
  and and_68 (and_68_out, not_4_out, and_12_out);
  and and_69 (and_69_out, not_4_out, and_13_out);
  and and_70 (and_70_out, not_4_out, and_14_out);
  and and_71 (and_71_out, not_4_out, and_15_out);
  and and_72 (and_72_out, not_4_out, and_16_out);
  not not_6 (not_6_out, not_5_out);
  and and_73 (and_73_out, not_4_out, and_17_out);
  and and_74 (and_74_out, not_4_out, and_18_out);
  and and_75 (and_75_out, not_4_out, and_19_out);
  and and_76 (and_76_out, not_4_out, and_20_out);
  and and_77 (and_77_out, not_4_out, and_21_out);
  and and_78 (and_78_out, not_4_out, and_22_out);
  and and_79 (and_79_out, not_4_out, and_23_out);
  and and_80 (and_80_out, not_4_out, and_24_out);
  not not_7 (not_7_out, not_6_out);
  not not_8 (not_8_out, not_4_out);
  and and_81 (and_81_out, not_8_out, and_25_out);
  and and_82 (and_82_out, not_8_out, and_26_out);
  and and_83 (and_83_out, not_8_out, and_27_out);
  and and_84 (and_84_out, not_8_out, and_28_out);
  and and_85 (and_85_out, not_8_out, and_29_out);
  and and_86 (and_86_out, not_8_out, and_30_out);
  and and_87 (and_87_out, not_8_out, and_31_out);
  and and_88 (and_88_out, not_8_out, and_32_out);
  not not_9 (not_9_out, not_7_out);
  and and_89 (and_89_out, not_8_out, and_33_out);
  and and_90 (and_90_out, not_8_out, and_34_out);
  and and_91 (and_91_out, not_8_out, and_35_out);
  and and_92 (and_92_out, not_8_out, and_36_out);
  and and_93 (and_93_out, not_8_out, and_37_out);
  and and_94 (and_94_out, not_8_out, and_38_out);
  and and_95 (and_95_out, not_8_out, and_39_out);
  and and_96 (and_96_out, not_8_out, and_40_out);
  not not_10 (not_10_out, not_9_out);
  not not_11 (not_11_out, not_8_out);
  and and_97 (and_97_out, not_11_out, and_41_out);
  and and_98 (and_98_out, not_11_out, and_42_out);
  and and_99 (and_99_out, not_11_out, and_43_out);
  and and_100 (and_100_out, not_11_out, and_44_out);
  and and_101 (and_101_out, not_11_out, and_45_out);
  and and_102 (and_102_out, not_11_out, and_46_out);
  and and_103 (and_103_out, not_11_out, and_47_out);
  and and_104 (and_104_out, not_11_out, and_48_out);
  not not_12 (not_12_out, not_10_out);
  and and_105 (and_105_out, not_11_out, and_49_out);
  and and_106 (and_106_out, not_11_out, and_50_out);
  and and_107 (and_107_out, not_11_out, and_51_out);
  and and_108 (and_108_out, not_11_out, and_52_out);
  and and_109 (and_109_out, not_11_out, and_53_out);
  and and_110 (and_110_out, not_11_out, and_54_out);
  and and_111 (and_111_out, not_11_out, and_55_out);
  and and_112 (and_112_out, not_11_out, and_56_out);
  or or_1 (_7_8, and_113_out, or_4_out);
  and and_113 (and_113_out, and_57_out, S0);
  or or_2 (_6_8, and_114_out, or_5_out);
  or or_3 (_5_8, and_115_out, or_6_out);
  and and_114 (and_114_out, and_58_out, S0);
  and and_115 (and_115_out, and_59_out, S0);
  and and_116 (and_116_out, and_60_out, S0);
  and and_117 (and_117_out, and_61_out, S0);
  and and_118 (and_118_out, and_62_out, S0);
  and and_119 (and_119_out, and_63_out, S0);
  and and_120 (and_120_out, and_64_out, S0);
  or or_4 (or_4_out, and_121_out, or_7_out);
  and and_121 (and_121_out, and_65_out, not_5_out);
  or or_5 (or_5_out, and_122_out, or_8_out);
  or or_6 (or_6_out, and_123_out, or_9_out);
  and and_122 (and_122_out, and_66_out, not_5_out);
  and and_123 (and_123_out, and_67_out, not_5_out);
  and and_124 (and_124_out, and_68_out, not_5_out);
  and and_125 (and_125_out, and_69_out, not_5_out);
  and and_126 (and_126_out, and_70_out, not_5_out);
  and and_127 (and_127_out, and_71_out, not_5_out);
  and and_128 (and_128_out, and_72_out, not_5_out);
  or or_7 (or_7_out, and_129_out, or_10_out);
  or or_8 (or_8_out, and_130_out, or_11_out);
  and and_129 (and_129_out, and_73_out, not_6_out);
  or or_9 (or_9_out, and_131_out, or_12_out);
  and and_130 (and_130_out, and_74_out, not_6_out);
  and and_131 (and_131_out, and_75_out, not_6_out);
  and and_132 (and_132_out, and_76_out, not_6_out);
  and and_133 (and_133_out, and_77_out, not_6_out);
  and and_134 (and_134_out, and_78_out, not_6_out);
  and and_135 (and_135_out, and_79_out, not_6_out);
  and and_136 (and_136_out, and_80_out, not_6_out);
  or or_10 (or_10_out, and_137_out, or_13_out);
  and and_137 (and_137_out, and_81_out, not_7_out);
  or or_11 (or_11_out, and_138_out, or_14_out);
  or or_12 (or_12_out, and_139_out, or_15_out);
  and and_138 (and_138_out, and_82_out, not_7_out);
  and and_139 (and_139_out, and_83_out, not_7_out);
  and and_140 (and_140_out, and_84_out, not_7_out);
  and and_141 (and_141_out, and_85_out, not_7_out);
  and and_142 (and_142_out, and_86_out, not_7_out);
  and and_143 (and_143_out, and_87_out, not_7_out);
  and and_144 (and_144_out, and_88_out, not_7_out);
  or or_13 (or_13_out, and_145_out, or_16_out);
  and and_145 (and_145_out, and_89_out, not_9_out);
  or or_14 (or_14_out, and_146_out, or_17_out);
  or or_15 (or_15_out, and_147_out, or_18_out);
  and and_146 (and_146_out, and_90_out, not_9_out);
  and and_147 (and_147_out, and_91_out, not_9_out);
  and and_148 (and_148_out, and_92_out, not_9_out);
  and and_149 (and_149_out, and_93_out, not_9_out);
  and and_150 (and_150_out, and_94_out, not_9_out);
  and and_151 (and_151_out, and_95_out, not_9_out);
  and and_152 (and_152_out, and_96_out, not_9_out);
  or or_16 (or_16_out, and_153_out, and_161_out);
  and and_153 (and_153_out, and_97_out, not_10_out);
  or or_17 (or_17_out, and_154_out, and_162_out);
  and and_154 (and_154_out, and_98_out, not_10_out);
  or or_18 (or_18_out, and_155_out, and_163_out);
  and and_155 (and_155_out, and_99_out, not_10_out);
  and and_156 (and_156_out, and_100_out, not_10_out);
  and and_157 (and_157_out, and_101_out, not_10_out);
  and and_158 (and_158_out, and_102_out, not_10_out);
  and and_159 (and_159_out, and_103_out, not_10_out);
  and and_160 (and_160_out, and_104_out, not_10_out);
  and and_161 (and_161_out, and_105_out, not_12_out);
  and and_162 (and_162_out, and_106_out, not_12_out);
  and and_163 (and_163_out, and_107_out, not_12_out);
  and and_164 (and_164_out, and_108_out, not_12_out);
  and and_165 (and_165_out, and_109_out, not_12_out);
  and and_166 (and_166_out, and_110_out, not_12_out);
  and and_167 (and_167_out, and_111_out, not_12_out);
  and and_168 (and_168_out, and_112_out, not_12_out);
  or or_19 (_4_8, and_116_out, or_23_out);
  or or_20 (_3_8, and_117_out, or_24_out);
  or or_21 (_2_8, and_118_out, or_25_out);
  or or_22 (_1_8, and_119_out, or_26_out);
  or or_23 (or_23_out, and_124_out, or_27_out);
  or or_24 (or_24_out, and_125_out, or_28_out);
  or or_25 (or_25_out, and_126_out, or_29_out);
  or or_26 (or_26_out, and_127_out, or_30_out);
  or or_27 (or_27_out, and_132_out, or_31_out);
  or or_28 (or_28_out, and_133_out, or_32_out);
  or or_29 (or_29_out, and_134_out, or_33_out);
  or or_30 (or_30_out, and_135_out, or_34_out);
  or or_31 (or_31_out, and_140_out, or_35_out);
  or or_32 (or_32_out, and_141_out, or_36_out);
  or or_33 (or_33_out, and_142_out, or_37_out);
  or or_34 (or_34_out, and_143_out, or_38_out);
  or or_35 (or_35_out, and_148_out, or_39_out);
  or or_36 (or_36_out, and_149_out, or_40_out);
  or or_37 (or_37_out, and_150_out, or_41_out);
  or or_38 (or_38_out, and_151_out, or_42_out);
  or or_39 (or_39_out, and_156_out, and_164_out);
  or or_40 (or_40_out, and_157_out, and_165_out);
  or or_41 (or_41_out, and_158_out, and_166_out);
  or or_42 (or_42_out, and_159_out, and_167_out);
  or or_43 (_0, and_120_out, or_44_out);
  or or_44 (or_44_out, and_128_out, or_45_out);
  or or_45 (or_45_out, and_136_out, or_46_out);
  or or_46 (or_46_out, and_144_out, or_47_out);
  or or_47 (or_47_out, and_152_out, or_48_out);
  or or_48 (or_48_out, and_160_out, and_168_out);
endmodule

module LED_Matrix_Controller (
  input  Value,
  input  Clear,
  input  Clock,
  input  in_4,
  input  in_5,
  input  in_6,
  input  in_7,
  input  in_8,
  input  in_9,
  input  in_10,
  input  in_11,
  output [15:0] out_12,
  output [15:0] out_13,
  output [15:0] out_14,
  output [15:0] out_15,
  output [15:0] out_16,
  output [15:0] out_17,
  output [15:0] out_18,
  output [15:0] out_19,
  output [15:0] out_20,
  output [15:0] out_21,
  output [15:0] out_22,
  output [15:0] out_23,
  output [15:0] out_24,
  output [15:0] out_25,
  output [15:0] out_26,
  output [15:0] out_27
);

  wire [15:0] and_1_out, and_2_out, and_3_out, and_4_out, and_5_out, and_6_out, and_7_out, and_8_out,
       and_9_out, and_10_out, and_11_out, and_12_out, and_13_out, and_14_out, and_15_out, and_16_out,
       and_17_out, and_18_out, and_19_out, and_20_out, and_21_out, and_22_out, and_23_out, and_24_out,
       and_25_out, and_26_out, and_27_out, and_28_out, and_29_out, and_30_out, and_31_out, and_32_out,
       and_33_out, bit_extender_1_out, bit_extender_2_out, decoder_1_out0, decoder_2_out0, not_1_out,
       not_2_out, not_3_out, not_4_out, not_5_out, not_6_out, not_7_out, not_8_out, not_9_out, not_10_out,
       not_11_out, not_12_out, not_13_out, not_14_out, not_15_out, not_16_out, or_1_out, or_2_out, or_3_out,
       or_4_out, or_5_out, or_6_out, or_7_out, or_8_out, or_9_out, or_10_out, or_11_out, or_12_out,
       or_13_out, or_14_out, or_15_out, or_16_out;

  Decoder #(.select(4), .enable("false")) decoder_1 (
    .out0(decoder_1_out0[0]), .out1(decoder_1_out0[1]), .out2(decoder_1_out0[2]), .out3(decoder_1_out0[3]),
    .out4(decoder_1_out0[4]), .out5(decoder_1_out0[5]), .out6(decoder_1_out0[6]), .out7(decoder_1_out0[7]),
    .out8(decoder_1_out0[8]), .out9(decoder_1_out0[9]), .out10(decoder_1_out0[10]),
    .out11(decoder_1_out0[11]), .out12(decoder_1_out0[12]), .out13(decoder_1_out0[13]),
    .out14(decoder_1_out0[14]), .out15(decoder_1_out0[15]), .sel({in_4, in_5, in_6, in_7}));
  Decoder #(.select(4), .enable("false")) decoder_2 (
    .out0(decoder_2_out0[0]), .out1(decoder_2_out0[1]), .out2(decoder_2_out0[2]), .out3(decoder_2_out0[3]),
    .out4(decoder_2_out0[4]), .out5(decoder_2_out0[5]), .out6(decoder_2_out0[6]), .out7(decoder_2_out0[7]),
    .out8(decoder_2_out0[8]), .out9(decoder_2_out0[9]), .out10(decoder_2_out0[10]),
    .out11(decoder_2_out0[11]), .out12(decoder_2_out0[12]), .out13(decoder_2_out0[13]),
    .out14(decoder_2_out0[14]), .out15(decoder_2_out0[15]), .sel({in_8, in_9, in_10, in_11}));
  assign bit_extender_1_out = {{15{Clock}}, Clock};  // Bit_Extender bit_extender_1
  assign and_1_out = bit_extender_1_out & decoder_2_out0;  // AND_Gate and_1, 16 bits wide
  assign bit_extender_2_out = {{15{Value}}, Value};  // Bit_Extender bit_extender_2
  assign and_2_out = bit_extender_2_out & decoder_1_out0;  // AND_Gate and_2, 16 bits wide
  assign not_1_out = ~decoder_1_out0;  // NOT_Gate not_1, 16 bits wide
  assign and_3_out = not_1_out & out_12;  // AND_Gate and_3, 16 bits wide
  assign and_4_out = bit_extender_2_out & decoder_1_out0;  // AND_Gate and_4, 16 bits wide
  assign not_2_out = ~decoder_1_out0;  // NOT_Gate not_2, 16 bits wide
  assign and_5_out = not_2_out & out_13;  // AND_Gate and_5, 16 bits wide
  assign and_6_out = bit_extender_2_out & decoder_1_out0;  // AND_Gate and_6, 16 bits wide
  assign not_3_out = ~decoder_1_out0;  // NOT_Gate not_3, 16 bits wide
  assign and_7_out = not_3_out & out_14;  // AND_Gate and_7, 16 bits wide
  assign and_8_out = bit_extender_2_out & decoder_1_out0;  // AND_Gate and_8, 16 bits wide
  assign not_4_out = ~decoder_1_out0;  // NOT_Gate not_4, 16 bits wide
  assign and_9_out = not_4_out & out_15;  // AND_Gate and_9, 16 bits wide
  assign and_10_out = bit_extender_2_out & decoder_1_out0;  // AND_Gate and_10, 16 bits wide
  assign not_5_out = ~decoder_1_out0;  // NOT_Gate not_5, 16 bits wide
  assign and_11_out = not_5_out & out_16;  // AND_Gate and_11, 16 bits wide
  assign and_12_out = bit_extender_2_out & decoder_1_out0;  // AND_Gate and_12, 16 bits wide
  assign not_6_out = ~decoder_1_out0;  // NOT_Gate not_6, 16 bits wide
  assign and_13_out = not_6_out & out_17;  // AND_Gate and_13, 16 bits wide
  assign and_14_out = bit_extender_2_out & decoder_1_out0;  // AND_Gate and_14, 16 bits wide
  assign not_7_out = ~decoder_1_out0;  // NOT_Gate not_7, 16 bits wide
  assign and_15_out = not_7_out & out_18;  // AND_Gate and_15, 16 bits wide
  assign and_16_out = bit_extender_2_out & decoder_1_out0;  // AND_Gate and_16, 16 bits wide
  assign not_8_out = ~decoder_1_out0;  // NOT_Gate not_8, 16 bits wide
  assign and_17_out = not_8_out & out_19;  // AND_Gate and_17, 16 bits wide
  assign and_18_out = bit_extender_2_out & decoder_1_out0;  // AND_Gate and_18, 16 bits wide
  assign not_9_out = ~decoder_1_out0;  // NOT_Gate not_9, 16 bits wide
  assign and_19_out = not_9_out & out_20;  // AND_Gate and_19, 16 bits wide
  assign and_20_out = bit_extender_2_out & decoder_1_out0;  // AND_Gate and_20, 16 bits wide
  assign not_10_out = ~decoder_1_out0;  // NOT_Gate not_10, 16 bits wide
  assign and_21_out = not_10_out & out_21;  // AND_Gate and_21, 16 bits wide
  assign and_22_out = bit_extender_2_out & decoder_1_out0;  // AND_Gate and_22, 16 bits wide
  assign not_11_out = ~decoder_1_out0;  // NOT_Gate not_11, 16 bits wide
  assign and_23_out = not_11_out & out_22;  // AND_Gate and_23, 16 bits wide
  assign and_24_out = bit_extender_2_out & decoder_1_out0;  // AND_Gate and_24, 16 bits wide
  assign not_12_out = ~decoder_1_out0;  // NOT_Gate not_12, 16 bits wide
  assign and_25_out = not_12_out & out_23;  // AND_Gate and_25, 16 bits wide
  assign and_26_out = bit_extender_2_out & decoder_1_out0;  // AND_Gate and_26, 16 bits wide
  assign not_13_out = ~decoder_1_out0;  // NOT_Gate not_13, 16 bits wide
  assign and_27_out = not_13_out & out_24;  // AND_Gate and_27, 16 bits wide
  assign and_28_out = bit_extender_2_out & decoder_1_out0;  // AND_Gate and_28, 16 bits wide
  assign not_14_out = ~decoder_1_out0;  // NOT_Gate not_14, 16 bits wide
  assign and_29_out = not_14_out & out_25;  // AND_Gate and_29, 16 bits wide
  assign and_30_out = bit_extender_2_out & decoder_1_out0;  // AND_Gate and_30, 16 bits wide
  assign not_15_out = ~decoder_1_out0;  // NOT_Gate not_15, 16 bits wide
  assign and_31_out = not_15_out & out_26;  // AND_Gate and_31, 16 bits wide
  assign and_32_out = bit_extender_2_out & decoder_1_out0;  // AND_Gate and_32, 16 bits wide
  assign not_16_out = ~decoder_1_out0;  // NOT_Gate not_16, 16 bits wide
  assign and_33_out = not_16_out & out_27;  // AND_Gate and_33, 16 bits wide
  Register_part #(.width(16)) register_1 (.D(or_1_out), .Q(out_12), .clk(and_1_out[0]), .clr(Clear));  // open: en
  assign or_1_out = and_2_out | and_3_out;  // OR_Gate or_1, 16 bits wide
  assign or_2_out = and_4_out | and_5_out;  // OR_Gate or_2, 16 bits wide
  Register_part #(.width(16)) register_2 (.D(or_2_out), .Q(out_13), .clk(and_1_out[1]), .clr(Clear));  // open: en
  assign or_3_out = and_6_out | and_7_out;  // OR_Gate or_3, 16 bits wide
  Register_part #(.width(16)) register_3 (.D(or_3_out), .Q(out_14), .clk(and_1_out[2]), .clr(Clear));  // open: en
  Register_part #(.width(16)) register_4 (.D(or_4_out), .Q(out_15), .clk(and_1_out[3]), .clr(Clear));  // open: en
  assign or_4_out = and_8_out | and_9_out;  // OR_Gate or_4, 16 bits wide
  Register_part #(.width(16)) register_5 (.D(or_5_out), .Q(out_16), .clk(and_1_out[4]), .clr(Clear));  // open: en
  assign or_5_out = and_10_out | and_11_out;  // OR_Gate or_5, 16 bits wide
  assign or_6_out = and_12_out | and_13_out;  // OR_Gate or_6, 16 bits wide
  Register_part #(.width(16)) register_6 (.D(or_6_out), .Q(out_17), .clk(and_1_out[5]), .clr(Clear));  // open: en
  Register_part #(.width(16)) register_7 (.D(or_7_out), .Q(out_18), .clk(and_1_out[6]), .clr(Clear));  // open: en
  assign or_7_out = and_14_out | and_15_out;  // OR_Gate or_7, 16 bits wide
  Register_part #(.width(16)) register_8 (.D(or_8_out), .Q(out_19), .clk(and_1_out[7]), .clr(Clear));  // open: en
  assign or_8_out = and_16_out | and_17_out;  // OR_Gate or_8, 16 bits wide
  Register_part #(.width(16)) register_9 (.D(or_9_out), .Q(out_20), .clk(and_1_out[8]), .clr(Clear));  // open: en
  assign or_9_out = and_18_out | and_19_out;  // OR_Gate or_9, 16 bits wide
  assign or_10_out = and_20_out | and_21_out;  // OR_Gate or_10, 16 bits wide
  Register_part #(.width(16)) register_10 (.D(or_10_out), .Q(out_21), .clk(and_1_out[9]), .clr(Clear));  // open: en
  assign or_11_out = and_22_out | and_23_out;  // OR_Gate or_11, 16 bits wide
  Register_part #(.width(16)) register_11 (.D(or_11_out), .Q(out_22), .clk(and_1_out[10]), .clr(Clear));  // open: en
  assign or_12_out = and_24_out | and_25_out;  // OR_Gate or_12, 16 bits wide
  Register_part #(.width(16)) register_12 (.D(or_12_out), .Q(out_23), .clk(and_1_out[11]), .clr(Clear));  // open: en
  Register_part #(.width(16)) register_13 (.D(or_13_out), .Q(out_24), .clk(and_1_out[12]), .clr(Clear));  // open: en
  assign or_13_out = and_26_out | and_27_out;  // OR_Gate or_13, 16 bits wide
  assign or_14_out = and_28_out | and_29_out;  // OR_Gate or_14, 16 bits wide
  Register_part #(.width(16)) register_14 (.D(or_14_out), .Q(out_25), .clk(and_1_out[13]), .clr(Clear));  // open: en
  Register_part #(.width(16)) register_15 (.D(or_15_out), .Q(out_26), .clk(and_1_out[14]), .clr(Clear));  // open: en
  assign or_15_out = and_30_out | and_31_out;  // OR_Gate or_15, 16 bits wide
  assign or_16_out = and_32_out | and_33_out;  // OR_Gate or_16, 16 bits wide
  Register_part #(.width(16)) register_16 (.D(or_16_out), .Q(out_27), .clk(and_1_out[15]), .clr(Clear));  // open: en
endmodule
